// Digital circuit ALU (Arithmetic logic unit) Simplified.dig as structural Verilog
module ALU__Arithmetic_logic_unit__Simplified (
  input  [7:0] A,
  input  [7:0] B,
  input  [2:0] Op,
  input  [2:0] Shamt,
  output [7:0] R,
  output Igual
);

  wire comparator_1_lt;
  wire [3:0] Shamt_t;
  wire [7:0] AComp, add_1_s, ADiv, AMult, ANeg, AShiftD, AShiftE, ASoma, ASub, barrelshifter_1_out,
       barrelshifter_2_out, BComp, BDiv, bitextender_2_out, BMult, BSoma, BSub, div_1_q, neg_1_out, sub_1_s;
  wire [15:0] mul_1_mul;

  BitExtender #(.inputBits(3), .outputBits(4)) bitextender_1 (.in(Shamt), .out(Shamt_t));
  Demultiplexer #(.Selector_Bits(3), .Bits(8)) demultiplexer_1 (
    .sel(Op), .in(A), .out_0(ASoma), .out_1(ASub), .out_2(AMult), .out_3(ADiv), .out_4(ANeg), .out_5(AComp),
    .out_6(AShiftE), .out_7(AShiftD));
  Demultiplexer #(.Selector_Bits(3), .Bits(8)) demultiplexer_2 (
    .sel(Op), .in(B), .out_0(BSoma), .out_1(BSub), .out_2(BMult), .out_3(BDiv), .out_5(BComp));  // open: out_4, out_6, out_7
  Add #(.Bits(8)) add_1 (.a(ASoma), .b(BSoma), .c_i(1'b0), .s(add_1_s));  // open: c_o
  Sub #(.Bits(8)) sub_1 (.a(ASub), .b(BSub), .c_i(1'b0), .s(sub_1_s));  // open: c_o
  Mul #(.Bits(8)) mul_1 (.a(AMult), .b(BMult), .mul(mul_1_mul));
  Div #(.Bits(8)) div_1 (.a(ADiv), .b(BDiv), .q(div_1_q));  // open: r
  Neg #(.Bits(8)) neg_1 (.in(ANeg), .out(neg_1_out));
  Comparator #(.Bits(8)) comparator_1 (.a(AComp), .b(BComp), .eq(Igual), .lt(comparator_1_lt));  // open: gt
  BarrelShifter #(.Bits(8)) barrelshifter_1 (.in(AShiftE), .shift(Shamt_t), .out(barrelshifter_1_out));
  BarrelShifter #(.Bits(8), .direction("right")) barrelshifter_2 (
    .in(AShiftD), .shift(Shamt_t), .out(barrelshifter_2_out));
  BitExtender #(.inputBits(1), .outputBits(8)) bitextender_2 (.in(comparator_1_lt), .out(bitextender_2_out));
  Multiplexer #(.Selector_Bits(3), .Bits(8)) multiplexer_1 (
    .sel(Op), .in_0(add_1_s), .in_1(sub_1_s), .in_2(mul_1_mul[7:0]), .in_3(div_1_q), .in_4(neg_1_out),
    .in_5(bitextender_2_out), .in_6(barrelshifter_1_out), .in_7(barrelshifter_2_out), .out(R));
endmodule
