// Digital circuit ALU (Arithmetic logic unit).dig as structural Verilog
module ALU__Arithmetic_logic_unit (
  input  A0,
  input  A1,
  input  A2,
  input  A3,
  input  A4,
  input  A5,
  input  A6,
  input  A7,
  input  B0,
  input  B1,
  input  B2,
  input  B3,
  input  B4,
  input  B5,
  input  B6,
  input  B7,
  input  OP0,
  input  OP1,
  input  OP2,
  input  OP3,
  input  B,
  input  Cin,
  output S0,
  output S1,
  output S2,
  output S3,
  output S4,
  output S5,
  output S6,
  output S7,
  output Cout
);

  wire and_1_out, and_2_out, and_3_out, and_4_out, and_5_out, and_6_out, and_7_out, and_8_out, and_9_out,
       and_10_out, and_11_out, and_12_out, and_13_out, and_14_out, and_15_out, and_16_out, and_17_out,
       and_18_out, and_19_out, and_20_out, and_21_out, and_22_out, and_23_out, and_24_out, and_25_out,
       and_26_out, and_27_out, and_28_out, and_29_out, and_30_out, and_31_out, and_32_out, and_33_out,
       and_34_out, and_35_out, and_36_out, and_37_out, and_38_out, and_39_out, and_40_out, and_41_out,
       and_42_out, and_43_out, and_44_out, and_45_out, and_46_out, and_47_out, and_48_out, and_49_out,
       and_50_out, and_51_out, and_52_out, and_53_out, and_54_out, and_55_out, and_56_out, and_57_out,
       and_58_out, and_59_out, and_60_out, and_61_out, and_62_out, and_63_out, and_64_out, and_65_out,
       and_66_out, and_67_out, and_68_out, and_69_out, and_70_out, and_71_out, and_72_out, and_73_out,
       and_74_out, and_75_out, and_76_out, and_77_out, and_78_out, and_79_out, and_80_out, and_81_out,
       and_82_out, and_83_out, and_84_out, and_85_out, and_86_out, and_87_out, and_88_out, and_89_out,
       and_90_out, and_91_out, and_92_out, and_93_out, and_94_out, and_95_out, and_96_out, and_97_out,
       and_98_out, and_99_out, and_100_out, and_101_out, and_102_out, and_103_out, and_104_out, and_105_out,
       and_106_out, and_107_out, and_108_out, and_109_out, and_110_out, and_111_out, and_112_out,
       and_113_out, and_114_out, and_115_out, and_116_out, and_117_out, and_118_out, and_119_out,
       and_120_out, and_121_out, and_122_out, and_123_out, and_124_out, and_125_out, and_126_out,
       and_127_out, and_128_out, and_129_out, and_130_out, and_131_out, and_132_out, and_133_out,
       and_134_out, and_135_out, and_136_out, and_137_out, and_138_out, and_139_out, and_140_out,
       and_141_out, and_142_out, and_143_out, and_144_out, and_145_out, and_146_out, and_147_out,
       and_148_out, and_149_out, and_150_out, and_151_out, and_152_out, and_153_out, and_154_out,
       and_155_out, and_156_out, and_157_out, and_158_out, and_159_out, and_160_out, and_161_out,
       and_162_out, and_163_out, and_164_out, and_165_out, and_166_out, and_167_out, and_168_out,
       and_169_out, and_170_out, and_171_out, and_172_out, and_173_out, and_174_out, and_175_out,
       and_176_out, and_177_out, and_178_out, and_179_out, and_180_out, and_181_out, and_182_out,
       and_183_out, and_184_out, and_185_out, and_186_out, and_187_out, and_188_out, and_189_out,
       and_190_out, and_191_out, and_192_out, and_193_out, and_194_out, and_195_out, and_196_out,
       and_197_out, and_198_out, and_199_out, and_200_out, and_201_out, and_202_out, and_203_out,
       and_204_out, and_205_out, and_206_out, and_207_out, and_208_out, and_209_out, and_210_out,
       and_211_out, and_212_out, and_213_out, and_214_out, and_215_out, and_216_out, and_217_out,
       and_218_out, and_219_out, and_220_out, and_221_out, and_222_out, and_223_out, and_224_out,
       and_225_out, and_226_out, and_227_out, and_228_out, and_229_out, and_230_out, and_231_out,
       and_232_out, and_233_out, and_234_out, and_235_out, and_236_out, and_237_out, and_238_out,
       and_239_out, and_240_out, and_241_out, and_242_out, and_243_out, and_244_out, and_245_out,
       and_246_out, and_247_out, and_248_out, and_249_out, and_250_out, and_251_out, and_252_out,
       and_253_out, and_254_out, and_255_out, and_256_out, and_257_out, and_258_out, and_259_out,
       and_260_out, and_261_out, and_262_out, and_263_out, and_264_out, and_265_out, and_266_out,
       and_267_out, and_268_out, and_269_out, and_270_out, and_271_out, and_272_out, and_273_out,
       and_274_out, and_275_out, and_276_out, and_277_out, and_278_out, and_279_out, and_280_out,
       and_281_out, and_282_out, and_283_out, and_284_out, and_285_out, and_286_out, and_287_out,
       and_288_out, and_289_out, and_290_out, and_291_out, and_292_out, and_293_out, and_294_out,
       and_295_out, and_296_out, and_297_out, and_298_out, and_299_out, and_300_out, and_301_out,
       and_302_out, and_303_out, and_304_out, and_305_out, and_306_out, and_307_out, and_308_out,
       and_309_out, and_310_out, and_311_out, and_312_out, and_313_out, and_314_out, and_315_out,
       and_316_out, and_317_out, and_318_out, and_319_out, and_320_out, and_321_out, and_322_out,
       and_323_out, and_324_out, and_325_out, and_326_out, and_327_out, and_328_out, and_329_out,
       and_330_out, and_331_out, and_332_out, and_333_out, and_334_out, and_335_out, and_336_out,
       and_337_out, and_338_out, and_339_out, and_340_out, and_341_out, and_342_out, and_343_out,
       and_344_out, and_345_out, and_346_out, and_347_out, and_348_out, and_349_out, and_350_out,
       and_351_out, and_352_out, and_353_out, and_354_out, and_355_out, and_356_out, and_357_out,
       and_358_out, and_359_out, and_360_out, and_361_out, and_362_out, and_363_out, and_364_out,
       and_365_out, and_366_out, and_367_out, and_368_out, and_369_out, and_370_out, and_371_out,
       and_372_out, and_373_out, and_374_out, and_375_out, and_376_out, and_377_out, and_378_out,
       and_379_out, and_380_out, and_381_out, and_382_out, and_383_out, and_384_out, and_385_out,
       and_386_out, and_387_out, and_388_out, and_389_out, and_390_out, and_391_out, and_392_out,
       and_393_out, and_394_out, and_395_out, and_396_out, and_397_out, and_398_out, and_399_out,
       and_400_out, and_401_out, and_402_out, and_403_out, and_404_out, and_405_out, and_406_out,
       and_407_out, and_408_out, and_409_out, and_410_out, and_411_out, and_412_out, and_413_out,
       and_414_out, and_415_out, and_416_out, and_417_out, and_418_out, and_419_out, and_420_out,
       and_421_out, and_422_out, and_423_out, and_424_out, and_425_out, and_426_out, and_427_out,
       and_428_out, and_429_out, and_430_out, and_431_out, and_432_out, and_433_out, and_434_out,
       and_435_out, and_436_out, and_437_out, and_438_out, and_439_out, and_440_out, and_441_out,
       and_442_out, and_443_out, and_444_out, and_445_out, and_446_out, and_447_out, and_448_out,
       and_449_out, and_450_out, and_451_out, and_452_out, and_453_out, and_454_out, and_455_out,
       and_456_out, and_457_out, and_458_out, and_459_out, and_460_out, and_461_out, and_462_out,
       and_463_out, and_464_out, and_465_out, and_466_out, and_467_out, and_468_out, and_469_out,
       and_470_out, and_471_out, and_472_out, and_473_out, and_474_out, and_475_out, and_476_out,
       and_477_out, and_478_out, and_479_out, and_480_out, and_481_out, and_482_out, and_483_out,
       and_484_out, and_485_out, and_486_out, and_487_out, and_488_out, and_489_out, and_490_out,
       and_491_out, and_492_out, and_493_out, and_494_out, and_495_out, and_496_out, and_497_out,
       and_498_out, and_499_out, and_500_out, and_501_out, and_502_out, and_503_out, and_504_out,
       and_505_out, and_506_out, and_507_out, and_508_out, and_509_out, and_510_out, and_511_out,
       and_512_out, and_513_out, and_514_out, and_515_out, and_516_out, and_517_out, and_518_out,
       and_519_out, and_520_out, and_521_out, and_522_out, and_523_out, and_524_out, and_525_out,
       and_526_out, and_527_out, and_528_out, and_529_out, and_530_out, and_531_out, and_532_out,
       and_533_out, and_534_out, and_535_out, and_536_out, and_537_out, and_538_out, and_539_out,
       and_540_out, and_541_out, and_542_out, and_543_out, and_544_out, and_545_out, and_546_out,
       and_547_out, and_548_out, and_549_out, and_550_out, and_551_out, and_552_out, and_553_out,
       and_554_out, and_555_out, nand_1_out, nand_2_out, nand_3_out, nand_4_out, nand_5_out, nand_6_out,
       nand_7_out, nand_8_out, nor_1_out, nor_2_out, nor_3_out, nor_4_out, nor_5_out, nor_6_out, nor_7_out,
       nor_8_out, not_1_out, not_2_out, not_3_out, not_4_out, not_5_out, not_6_out, not_7_out, not_8_out,
       not_9_out, not_10_out, not_11_out, not_12_out, not_13_out, not_14_out, not_15_out, not_16_out,
       not_17_out, not_18_out, not_19_out, not_20_out, not_21_out, not_22_out, not_23_out, not_24_out,
       not_25_out, not_26_out, not_27_out, not_28_out, not_29_out, not_30_out, not_31_out, not_32_out,
       not_33_out, not_34_out, not_35_out, not_36_out, not_37_out, not_38_out, not_39_out, not_40_out,
       not_41_out, not_42_out, not_43_out, not_44_out, not_45_out, not_46_out, not_47_out, not_48_out,
       not_49_out, not_50_out, not_51_out, not_52_out, not_53_out, not_54_out, not_55_out, not_56_out,
       not_57_out, not_58_out, not_59_out, not_60_out, not_61_out, not_62_out, not_63_out, not_64_out,
       not_65_out, not_66_out, not_67_out, not_68_out, not_69_out, not_70_out, not_71_out, not_72_out,
       not_73_out, or_1_out, or_2_out, or_4_out, or_5_out, or_6_out, or_7_out, or_9_out, or_10_out,
       or_11_out, or_12_out, or_14_out, or_15_out, or_16_out, or_17_out, or_19_out, or_20_out, or_21_out,
       or_22_out, or_24_out, or_25_out, or_26_out, or_27_out, or_29_out, or_30_out, or_31_out, or_32_out,
       or_33_out, or_34_out, or_35_out, or_36_out, or_37_out, or_38_out, or_39_out, or_40_out, or_41_out,
       or_42_out, or_43_out, or_44_out, or_45_out, or_46_out, or_47_out, or_49_out, or_50_out, or_51_out,
       or_52_out, or_53_out, or_54_out, or_55_out, or_56_out, or_57_out, or_58_out, or_59_out, or_60_out,
       or_61_out, or_62_out, or_63_out, or_64_out, or_65_out, or_66_out, or_67_out, or_68_out, or_69_out,
       or_70_out, or_72_out, or_73_out, or_74_out, or_75_out, or_76_out, or_77_out, or_78_out, or_79_out,
       or_80_out, or_81_out, or_82_out, or_83_out, or_84_out, or_85_out, or_86_out, or_87_out, or_88_out,
       or_89_out, or_90_out, or_91_out, or_92_out, or_93_out, or_94_out, or_95_out, or_96_out, or_97_out,
       or_98_out, or_99_out, or_100_out, or_101_out, or_102_out, or_103_out, or_104_out, or_105_out,
       or_106_out, or_107_out, or_108_out, or_109_out, or_110_out, or_111_out, or_112_out, or_113_out,
       or_114_out, or_115_out, or_116_out, or_117_out, or_118_out, or_119_out, or_120_out, or_121_out,
       or_122_out, or_123_out, or_124_out, or_125_out, or_126_out, or_127_out, or_128_out, or_129_out,
       or_130_out, or_131_out, or_132_out, or_133_out, or_134_out, or_136_out, or_137_out, or_138_out,
       or_139_out, or_140_out, or_141_out, or_142_out, or_143_out, or_144_out, or_145_out, or_146_out,
       or_147_out, or_148_out, or_149_out, or_150_out, or_151_out, or_152_out, or_153_out, or_154_out,
       or_155_out, or_156_out, or_157_out, or_158_out, or_159_out, or_160_out, or_161_out, or_162_out,
       or_163_out, or_164_out, or_165_out, or_166_out, or_167_out, or_168_out, or_169_out, or_170_out,
       or_171_out, or_172_out, or_173_out, or_174_out, or_175_out, or_176_out, or_177_out, or_178_out,
       or_179_out, or_180_out, or_181_out, or_182_out, or_183_out, or_184_out, or_185_out, or_186_out,
       or_187_out, or_188_out, or_189_out, or_190_out, or_191_out, or_192_out, or_193_out, or_194_out,
       or_195_out, or_196_out, or_197_out, or_198_out, or_199_out, or_200_out, or_201_out, or_202_out,
       or_203_out, or_204_out, or_205_out, or_206_out, or_207_out, or_208_out, or_209_out, or_211_out,
       or_212_out, or_213_out, or_214_out, or_215_out, or_216_out, or_217_out, or_218_out, or_219_out,
       or_220_out, or_221_out, or_222_out, or_223_out, or_224_out, or_225_out, or_226_out, xnor_1_out,
       xnor_2_out, xnor_3_out, xnor_4_out, xnor_5_out, xnor_6_out, xnor_7_out, xnor_8_out, xor_1_out,
       xor_2_out, xor_3_out, xor_4_out, xor_5_out, xor_6_out, xor_7_out, xor_8_out, xor_9_out, xor_10_out,
       xor_11_out, xor_12_out, xor_13_out, xor_14_out, xor_15_out, xor_16_out, xor_17_out, xor_18_out,
       xor_19_out, xor_20_out, xor_21_out, xor_22_out, xor_23_out, xor_24_out, xor_25_out, xor_26_out,
       xor_27_out, xor_28_out, xor_29_out, xor_30_out, xor_31_out, xor_33_out, xor_34_out, xor_35_out,
       xor_36_out, xor_37_out, xor_38_out, xor_39_out, xor_40_out, xor_41_out, xor_42_out, xor_43_out,
       xor_44_out, xor_45_out, xor_46_out, xor_47_out, xor_48_out, xor_49_out, xor_50_out, xor_51_out,
       xor_52_out, xor_53_out, xor_54_out, xor_55_out, xor_56_out, xor_57_out, xor_58_out, xor_59_out,
       xor_60_out, xor_61_out, xor_62_out, xor_63_out, xor_64_out, xor_65_out, xor_66_out, xor_67_out,
       xor_68_out, xor_69_out, xor_71_out, xor_72_out, xor_73_out, xor_74_out, xor_75_out, xor_76_out,
       xor_77_out, xor_78_out, xor_79_out, xor_80_out, xor_81_out, xor_82_out, xor_83_out, xor_84_out,
       xor_85_out, xor_86_out, xor_87_out, xor_88_out, xor_89_out, xor_90_out, xor_91_out, xor_92_out,
       xor_93_out, xor_94_out, xor_95_out, xor_96_out, xor_97_out, xor_98_out, xor_99_out, xor_100_out,
       xor_102_out, xor_103_out, xor_104_out, xor_105_out, xor_106_out, xor_107_out, xor_108_out,
       xor_109_out, xor_110_out, xor_111_out, xor_112_out, xor_113_out, xor_114_out, xor_115_out,
       xor_116_out, xor_117_out, xor_118_out, xor_119_out, xor_120_out, xor_121_out, xor_122_out,
       xor_123_out, xor_124_out, xor_125_out, xor_126_out, xor_127_out, xor_128_out, xor_129_out,
       xor_130_out, xor_131_out, xor_133_out, xor_134_out, xor_135_out, xor_136_out, xor_137_out,
       xor_138_out, xor_139_out, xor_140_out, xor_141_out, xor_142_out, xor_143_out, xor_144_out,
       xor_145_out, xor_146_out, xor_147_out, xor_148_out, xor_149_out, xor_150_out, xor_151_out,
       xor_152_out, xor_153_out, xor_154_out, xor_155_out, xor_156_out, xor_157_out, xor_158_out,
       xor_159_out, xor_160_out, xor_161_out, xor_162_out, xor_164_out, xor_165_out, xor_166_out,
       xor_167_out, xor_168_out, xor_169_out, xor_170_out, xor_171_out, xor_172_out, xor_173_out,
       xor_174_out, xor_175_out, xor_176_out, xor_177_out, xor_178_out, xor_179_out, xor_180_out,
       xor_181_out, xor_182_out, xor_183_out, xor_184_out, xor_185_out, xor_186_out, xor_187_out,
       xor_188_out, xor_189_out, xor_190_out, xor_191_out, xor_192_out, xor_193_out, xor_195_out,
       xor_196_out, xor_197_out, xor_198_out, xor_199_out, xor_200_out, xor_201_out, xor_202_out,
       xor_203_out, xor_204_out, xor_205_out, xor_206_out, xor_207_out, xor_208_out, xor_209_out,
       xor_210_out, xor_211_out, xor_212_out, xor_213_out, xor_214_out, xor_215_out, xor_216_out,
       xor_217_out, xor_218_out, xor_219_out, xor_220_out, xor_221_out, xor_222_out, xor_223_out,
       xor_224_out, xor_226_out, xor_227_out, xor_228_out, xor_229_out, xor_230_out, xor_231_out,
       xor_232_out, xor_233_out, xor_234_out, xor_235_out, xor_236_out, xor_237_out, xor_238_out,
       xor_239_out, xor_240_out, xor_241_out, xor_242_out, xor_243_out, xor_244_out, xor_245_out,
       xor_246_out, xor_247_out, xor_248_out, xor_249_out, xor_250_out, xor_251_out, xor_252_out,
       xor_253_out, xor_254_out, xor_255_out, xor_256_out;

  not not_1 (not_1_out, OP3);
  not not_2 (not_2_out, OP2);
  not not_3 (not_3_out, OP1);
  not not_4 (not_4_out, OP0);
  and and_1 (and_1_out, not_1_out, not_2_out, not_3_out, not_4_out, xor_8_out);
  and and_2 (and_2_out, not_1_out, not_2_out, not_3_out, OP0, or_40_out);
  or or_1 (or_1_out, and_4_out, and_3_out, and_2_out, and_1_out);
  and and_3 (and_3_out, not_1_out, not_2_out, OP1, not_4_out, and_108_out);
  and and_4 (and_4_out, not_1_out, not_2_out, OP1, OP0, xor_16_out);
  and and_5 (and_5_out, not_1_out, OP2, not_3_out, not_4_out, xor_40_out);
  and and_6 (and_6_out, not_1_out, OP2, not_3_out, OP0, xnor_8_out);
  or or_2 (or_2_out, and_8_out, and_7_out, and_6_out, and_5_out);
  and and_7 (and_7_out, not_1_out, OP2, OP1, not_4_out, nor_8_out);
  and and_8 (and_8_out, not_1_out, OP2, OP1, OP0, nand_8_out);
  and and_9 (and_9_out, OP3, not_2_out, not_3_out, not_4_out, xor_226_out);
  or or_3 (S7, or_5_out, or_4_out, or_2_out, or_1_out);
  and and_10 (and_10_out, OP3, not_2_out, not_3_out, OP0, or_57_out);
  or or_4 (or_4_out, and_12_out, and_11_out, and_10_out, and_9_out);
  and and_11 (and_11_out, OP3, not_2_out, OP1, not_4_out, xor_7_out);
  and and_12 (and_12_out, OP3, not_2_out, OP1, OP0, 1'b0);
  and and_13 (and_13_out, OP3, OP2, not_3_out, not_4_out, or_226_out);
  and and_14 (and_14_out, OP3, OP2, not_3_out, OP0, 1'b0);
  or or_5 (or_5_out, and_16_out, and_15_out, and_14_out, and_13_out);
  and and_15 (and_15_out, OP3, OP2, OP1, not_4_out, 1'b0);
  and and_16 (and_16_out, OP3, OP2, OP1, OP0, 1'b0);
  and and_17 (and_17_out, not_1_out, not_2_out, not_3_out, not_4_out, xor_7_out);
  and and_18 (and_18_out, not_1_out, not_2_out, not_3_out, OP0, or_39_out);
  or or_6 (or_6_out, and_20_out, and_19_out, and_18_out, and_17_out);
  and and_19 (and_19_out, not_1_out, not_2_out, OP1, not_4_out, and_107_out);
  and and_20 (and_20_out, not_1_out, not_2_out, OP1, OP0, xor_15_out);
  and and_21 (and_21_out, not_1_out, OP2, not_3_out, not_4_out, xor_39_out);
  and and_22 (and_22_out, not_1_out, OP2, not_3_out, OP0, xnor_7_out);
  or or_7 (or_7_out, and_24_out, and_23_out, and_22_out, and_21_out);
  and and_23 (and_23_out, not_1_out, OP2, OP1, not_4_out, nor_7_out);
  and and_24 (and_24_out, not_1_out, OP2, OP1, OP0, nand_7_out);
  and and_25 (and_25_out, OP3, not_2_out, not_3_out, not_4_out, xor_195_out);
  or or_8 (S6, or_10_out, or_9_out, or_7_out, or_6_out);
  and and_26 (and_26_out, OP3, not_2_out, not_3_out, OP0, or_80_out);
  or or_9 (or_9_out, and_28_out, and_27_out, and_26_out, and_25_out);
  and and_27 (and_27_out, OP3, not_2_out, OP1, not_4_out, xor_6_out);
  and and_28 (and_28_out, OP3, not_2_out, OP1, OP0, xor_8_out);
  and and_29 (and_29_out, OP3, OP2, not_3_out, not_4_out, or_225_out);
  and and_30 (and_30_out, OP3, OP2, not_3_out, OP0, 1'b0);
  or or_10 (or_10_out, and_32_out, and_31_out, and_30_out, and_29_out);
  and and_31 (and_31_out, OP3, OP2, OP1, not_4_out, 1'b0);
  and and_32 (and_32_out, OP3, OP2, OP1, OP0, 1'b0);
  and and_33 (and_33_out, not_1_out, not_2_out, not_3_out, not_4_out, xor_6_out);
  and and_34 (and_34_out, not_1_out, not_2_out, not_3_out, OP0, or_38_out);
  or or_11 (or_11_out, and_36_out, and_35_out, and_34_out, and_33_out);
  and and_35 (and_35_out, not_1_out, not_2_out, OP1, not_4_out, and_106_out);
  and and_36 (and_36_out, not_1_out, not_2_out, OP1, OP0, xor_14_out);
  and and_37 (and_37_out, not_1_out, OP2, not_3_out, not_4_out, xor_38_out);
  and and_38 (and_38_out, not_1_out, OP2, not_3_out, OP0, xnor_6_out);
  or or_12 (or_12_out, and_40_out, and_39_out, and_38_out, and_37_out);
  and and_39 (and_39_out, not_1_out, OP2, OP1, not_4_out, nor_6_out);
  and and_40 (and_40_out, not_1_out, OP2, OP1, OP0, nand_6_out);
  and and_41 (and_41_out, OP3, not_2_out, not_3_out, not_4_out, xor_164_out);
  or or_13 (S5, or_15_out, or_14_out, or_12_out, or_11_out);
  and and_42 (and_42_out, OP3, not_2_out, not_3_out, OP0, or_103_out);
  or or_14 (or_14_out, and_44_out, and_43_out, and_42_out, and_41_out);
  and and_43 (and_43_out, OP3, not_2_out, OP1, not_4_out, xor_5_out);
  and and_44 (and_44_out, OP3, not_2_out, OP1, OP0, xor_7_out);
  and and_45 (and_45_out, OP3, OP2, not_3_out, not_4_out, or_224_out);
  and and_46 (and_46_out, OP3, OP2, not_3_out, OP0, 1'b0);
  or or_15 (or_15_out, and_48_out, and_47_out, and_46_out, and_45_out);
  and and_47 (and_47_out, OP3, OP2, OP1, not_4_out, 1'b0);
  and and_48 (and_48_out, OP3, OP2, OP1, OP0, 1'b0);
  and and_49 (and_49_out, not_1_out, not_2_out, not_3_out, not_4_out, xor_5_out);
  and and_50 (and_50_out, not_1_out, not_2_out, not_3_out, OP0, or_37_out);
  or or_16 (or_16_out, and_52_out, and_51_out, and_50_out, and_49_out);
  and and_51 (and_51_out, not_1_out, not_2_out, OP1, not_4_out, and_105_out);
  and and_52 (and_52_out, not_1_out, not_2_out, OP1, OP0, xor_13_out);
  and and_53 (and_53_out, not_1_out, OP2, not_3_out, not_4_out, xor_37_out);
  and and_54 (and_54_out, not_1_out, OP2, not_3_out, OP0, xnor_5_out);
  or or_17 (or_17_out, and_56_out, and_55_out, and_54_out, and_53_out);
  and and_55 (and_55_out, not_1_out, OP2, OP1, not_4_out, nor_5_out);
  and and_56 (and_56_out, not_1_out, OP2, OP1, OP0, nand_5_out);
  and and_57 (and_57_out, OP3, not_2_out, not_3_out, not_4_out, xor_133_out);
  or or_18 (S4, or_20_out, or_19_out, or_17_out, or_16_out);
  and and_58 (and_58_out, OP3, not_2_out, not_3_out, OP0, or_127_out);
  or or_19 (or_19_out, and_60_out, and_59_out, and_58_out, and_57_out);
  and and_59 (and_59_out, OP3, not_2_out, OP1, not_4_out, xor_4_out);
  and and_60 (and_60_out, OP3, not_2_out, OP1, OP0, xor_6_out);
  and and_61 (and_61_out, OP3, OP2, not_3_out, not_4_out, or_223_out);
  and and_62 (and_62_out, OP3, OP2, not_3_out, OP0, 1'b0);
  or or_20 (or_20_out, and_64_out, and_63_out, and_62_out, and_61_out);
  and and_63 (and_63_out, OP3, OP2, OP1, not_4_out, 1'b0);
  and and_64 (and_64_out, OP3, OP2, OP1, OP0, 1'b0);
  and and_65 (and_65_out, not_1_out, not_2_out, not_3_out, not_4_out, xor_4_out);
  and and_66 (and_66_out, not_1_out, not_2_out, not_3_out, OP0, or_36_out);
  or or_21 (or_21_out, and_68_out, and_67_out, and_66_out, and_65_out);
  and and_67 (and_67_out, not_1_out, not_2_out, OP1, not_4_out, and_104_out);
  and and_68 (and_68_out, not_1_out, not_2_out, OP1, OP0, xor_12_out);
  and and_69 (and_69_out, not_1_out, OP2, not_3_out, not_4_out, xor_36_out);
  and and_70 (and_70_out, not_1_out, OP2, not_3_out, OP0, xnor_4_out);
  or or_22 (or_22_out, and_72_out, and_71_out, and_70_out, and_69_out);
  and and_71 (and_71_out, not_1_out, OP2, OP1, not_4_out, nor_4_out);
  and and_72 (and_72_out, not_1_out, OP2, OP1, OP0, nand_4_out);
  and and_73 (and_73_out, OP3, not_2_out, not_3_out, not_4_out, xor_102_out);
  or or_23 (S3, or_25_out, or_24_out, or_22_out, or_21_out);
  and and_74 (and_74_out, OP3, not_2_out, not_3_out, OP0, or_151_out);
  or or_24 (or_24_out, and_76_out, and_75_out, and_74_out, and_73_out);
  and and_75 (and_75_out, OP3, not_2_out, OP1, not_4_out, xor_3_out);
  and and_76 (and_76_out, OP3, not_2_out, OP1, OP0, xor_5_out);
  and and_77 (and_77_out, OP3, OP2, not_3_out, not_4_out, or_222_out);
  and and_78 (and_78_out, OP3, OP2, not_3_out, OP0, 1'b0);
  or or_25 (or_25_out, and_80_out, and_79_out, and_78_out, and_77_out);
  and and_79 (and_79_out, OP3, OP2, OP1, not_4_out, 1'b0);
  and and_80 (and_80_out, OP3, OP2, OP1, OP0, 1'b0);
  and and_81 (and_81_out, not_1_out, not_2_out, not_3_out, not_4_out, xor_3_out);
  and and_82 (and_82_out, not_1_out, not_2_out, not_3_out, OP0, or_35_out);
  or or_26 (or_26_out, and_84_out, and_83_out, and_82_out, and_81_out);
  and and_83 (and_83_out, not_1_out, not_2_out, OP1, not_4_out, and_103_out);
  and and_84 (and_84_out, not_1_out, not_2_out, OP1, OP0, xor_11_out);
  and and_85 (and_85_out, not_1_out, OP2, not_3_out, not_4_out, xor_35_out);
  and and_86 (and_86_out, not_1_out, OP2, not_3_out, OP0, xnor_3_out);
  or or_27 (or_27_out, and_88_out, and_87_out, and_86_out, and_85_out);
  and and_87 (and_87_out, not_1_out, OP2, OP1, not_4_out, nor_3_out);
  and and_88 (and_88_out, not_1_out, OP2, OP1, OP0, nand_3_out);
  and and_89 (and_89_out, OP3, not_2_out, not_3_out, not_4_out, xor_71_out);
  or or_28 (S2, or_31_out, or_29_out, or_27_out, or_26_out);
  and and_90 (and_90_out, OP3, not_2_out, not_3_out, OP0, or_174_out);
  or or_29 (or_29_out, and_92_out, and_91_out, and_90_out, and_89_out);
  LED led_1 (.in(S7));
  and and_91 (and_91_out, OP3, not_2_out, OP1, not_4_out, xor_2_out);
  LED led_2 (.in(S3));
  LED led_3 (.in(S4));
  LED led_4 (.in(S5));
  LED led_5 (.in(S6));
  and and_92 (and_92_out, OP3, not_2_out, OP1, OP0, xor_4_out);
  LED led_6 (.in(S0));
  LED led_7 (.in(S1));
  LED led_8 (.in(S2));
  and and_93 (and_93_out, OP3, OP2, not_3_out, not_4_out, or_221_out);
  and and_94 (and_94_out, OP3, OP2, not_3_out, OP0, 1'b0);
  or or_30 (or_30_out, B, and_95_out);
  and and_95 (and_95_out, not_5_out, not_6_out, not_7_out, not_8_out);
  not not_5 (not_5_out, OP0);
  not not_6 (not_6_out, OP1);
  or or_31 (or_31_out, and_97_out, and_96_out, and_94_out, and_93_out);
  not not_7 (not_7_out, OP2);
  not not_8 (not_8_out, OP3);
  and and_96 (and_96_out, OP3, OP2, OP1, not_4_out, 1'b0);
  and and_97 (and_97_out, OP3, OP2, OP1, OP0, 1'b0);
  and and_98 (and_98_out, not_1_out, not_2_out, not_3_out, not_4_out, xor_2_out);
  and and_99 (and_99_out, not_1_out, not_2_out, not_3_out, OP0, or_34_out);
  or or_32 (or_32_out, and_109_out, and_100_out, and_99_out, and_98_out);
  not not_9 (not_9_out, B4);
  not not_10 (not_10_out, B5);
  not not_11 (not_11_out, B6);
  not not_12 (not_12_out, B7);
  nand nand_1 (nand_1_out, A0, B0);
  nand nand_2 (nand_2_out, A1, B1);
  nand nand_3 (nand_3_out, A2, B2);
  nand nand_4 (nand_4_out, A3, B3);
  nand nand_5 (nand_5_out, A4, B4);
  nand nand_6 (nand_6_out, A5, B5);
  nand nand_7 (nand_7_out, A6, B6);
  nand nand_8 (nand_8_out, A7, B7);
  nor nor_1 (nor_1_out, A0, B0);
  nor nor_2 (nor_2_out, A1, B1);
  nor nor_3 (nor_3_out, A2, B2);
  nor nor_4 (nor_4_out, A3, B3);
  nor nor_5 (nor_5_out, A4, B4);
  nor nor_6 (nor_6_out, A5, B5);
  nor nor_7 (nor_7_out, A6, B6);
  nor nor_8 (nor_8_out, A7, B7);
  xnor xnor_1 (xnor_1_out, A0, B0);
  xnor xnor_2 (xnor_2_out, A1, B1);
  xnor xnor_3 (xnor_3_out, A2, B2);
  xnor xnor_4 (xnor_4_out, A3, B3);
  xnor xnor_5 (xnor_5_out, A4, B4);
  xnor xnor_6 (xnor_6_out, A5, B5);
  xnor xnor_7 (xnor_7_out, A6, B6);
  xnor xnor_8 (xnor_8_out, A7, B7);
  xor xor_1 (xor_1_out, B0, or_30_out);
  xor xor_2 (xor_2_out, B1, or_30_out);
  xor xor_3 (xor_3_out, B2, or_30_out);
  xor xor_4 (xor_4_out, B3, or_30_out);
  xor xor_5 (xor_5_out, B4, or_30_out);
  xor xor_6 (xor_6_out, B5, or_30_out);
  xor xor_7 (xor_7_out, B6, or_30_out);
  xor xor_8 (xor_8_out, B7, or_30_out);
  and and_100 (and_100_out, not_1_out, not_2_out, OP1, not_4_out, and_102_out);
  not not_13 (not_13_out, B0);
  not not_14 (not_14_out, B1);
  not not_15 (not_15_out, B2);
  not not_16 (not_16_out, B3);
  xor xor_9 (xor_9_out, A0, xor_1_out);
  and and_101 (and_101_out, A0, xor_1_out);
  or or_33 (or_33_out, A0, xor_1_out);
  xor xor_10 (xor_10_out, A1, xor_2_out);
  and and_102 (and_102_out, A1, xor_2_out);
  or or_34 (or_34_out, A1, xor_2_out);
  xor xor_11 (xor_11_out, A2, xor_3_out);
  and and_103 (and_103_out, A2, xor_3_out);
  or or_35 (or_35_out, A2, xor_3_out);
  xor xor_12 (xor_12_out, A3, xor_4_out);
  and and_104 (and_104_out, A3, xor_4_out);
  or or_36 (or_36_out, A3, xor_4_out);
  xor xor_13 (xor_13_out, A4, xor_5_out);
  and and_105 (and_105_out, A4, xor_5_out);
  or or_37 (or_37_out, A4, xor_5_out);
  xor xor_14 (xor_14_out, A5, xor_6_out);
  and and_106 (and_106_out, A5, xor_6_out);
  or or_38 (or_38_out, A5, xor_6_out);
  xor xor_15 (xor_15_out, A6, xor_7_out);
  and and_107 (and_107_out, A6, xor_7_out);
  or or_39 (or_39_out, A6, xor_7_out);
  xor xor_16 (xor_16_out, A7, xor_8_out);
  and and_108 (and_108_out, A7, xor_8_out);
  or or_40 (or_40_out, A7, xor_8_out);
  and and_109 (and_109_out, not_1_out, not_2_out, OP1, OP0, xor_10_out);
  xor xor_17 (xor_17_out, not_13_out, A7);
  and and_110 (and_110_out, A7, not_13_out);
  xor xor_18 (xor_18_out, not_14_out, 1'b0);
  and and_111 (and_111_out, 1'b0, not_14_out);
  xor xor_19 (xor_19_out, not_15_out, 1'b0);
  and and_112 (and_112_out, 1'b0, not_15_out);
  xor xor_20 (xor_20_out, not_16_out, 1'b0);
  and and_113 (and_113_out, 1'b0, not_16_out);
  xor xor_21 (xor_21_out, not_9_out, 1'b0);
  and and_114 (and_114_out, 1'b0, not_9_out);
  xor xor_22 (xor_22_out, not_10_out, 1'b0);
  and and_115 (and_115_out, 1'b0, not_10_out);
  xor xor_23 (xor_23_out, not_11_out, 1'b0);
  and and_116 (and_116_out, 1'b0, not_11_out);
  xor xor_24 (xor_24_out, not_12_out, 1'b0);
  and and_117 (and_117_out, 1'b0, not_12_out);
  and and_118 (and_118_out, A0, B0);
  and and_119 (and_119_out, A0, B1);
  and and_120 (and_120_out, B0, A1);
  and and_121 (and_121_out, A0, B2);
  and and_122 (and_122_out, B1, A1);
  and and_123 (and_123_out, A0, B3);
  and and_124 (and_124_out, B2, A1);
  and and_125 (and_125_out, A0, B4);
  and and_126 (and_126_out, B3, A1);
  and and_127 (and_127_out, A0, B5);
  and and_128 (and_128_out, B4, A1);
  and and_129 (and_129_out, A0, B6);
  and and_130 (and_130_out, B5, A1);
  and and_131 (and_131_out, A0, B7);
  and and_132 (and_132_out, B6, A1);
  and and_133 (and_133_out, B7, A1);
  and and_134 (and_134_out, not_1_out, OP2, not_3_out, not_4_out, xor_34_out);
  xor xor_25 (xor_25_out, 1'b1, xor_17_out);
  and and_135 (and_135_out, xor_17_out, 1'b1);
  xor xor_26 (xor_26_out, or_50_out, xor_18_out);
  and and_136 (and_136_out, xor_18_out, or_50_out);
  xor xor_27 (xor_27_out, or_51_out, xor_19_out);
  and and_137 (and_137_out, xor_19_out, or_51_out);
  xor xor_28 (xor_28_out, or_52_out, xor_20_out);
  and and_138 (and_138_out, xor_20_out, or_52_out);
  xor xor_29 (xor_29_out, or_53_out, xor_21_out);
  and and_139 (and_139_out, xor_21_out, or_53_out);
  xor xor_30 (xor_30_out, or_54_out, xor_22_out);
  and and_140 (and_140_out, xor_22_out, or_54_out);
  xor xor_31 (xor_31_out, or_55_out, xor_23_out);
  and and_141 (and_141_out, xor_23_out, or_55_out);
  // XOr xor_32 has open pins: In_1=or_56_out, In_2=xor_24_out, out=open
  and and_142 (and_142_out, xor_24_out, or_56_out);
  xor xor_33 (xor_33_out, Cin, xor_9_out);
  and and_143 (and_143_out, xor_9_out, Cin);
  xor xor_34 (xor_34_out, or_41_out, xor_10_out);
  and and_144 (and_144_out, xor_10_out, or_41_out);
  xor xor_35 (xor_35_out, or_42_out, xor_11_out);
  and and_145 (and_145_out, xor_11_out, or_42_out);
  xor xor_36 (xor_36_out, or_43_out, xor_12_out);
  and and_146 (and_146_out, xor_12_out, or_43_out);
  xor xor_37 (xor_37_out, or_44_out, xor_13_out);
  and and_147 (and_147_out, xor_13_out, or_44_out);
  xor xor_38 (xor_38_out, or_45_out, xor_14_out);
  and and_148 (and_148_out, xor_14_out, or_45_out);
  xor xor_39 (xor_39_out, or_46_out, xor_15_out);
  and and_149 (and_149_out, xor_15_out, or_46_out);
  xor xor_40 (xor_40_out, or_47_out, xor_16_out);
  and and_150 (and_150_out, xor_16_out, or_47_out);
  and and_151 (and_151_out, not_1_out, OP2, not_3_out, OP0, xnor_2_out);
  xor xor_41 (xor_41_out, and_120_out, and_119_out);
  and and_152 (and_152_out, and_120_out, and_119_out);
  xor xor_42 (xor_42_out, and_122_out, and_121_out);
  and and_153 (and_153_out, and_122_out, and_121_out);
  xor xor_43 (xor_43_out, and_124_out, and_123_out);
  and and_154 (and_154_out, and_124_out, and_123_out);
  xor xor_44 (xor_44_out, and_126_out, and_125_out);
  and and_155 (and_155_out, and_126_out, and_125_out);
  xor xor_45 (xor_45_out, and_128_out, and_127_out);
  and and_156 (and_156_out, and_128_out, and_127_out);
  xor xor_46 (xor_46_out, and_130_out, and_129_out);
  and and_157 (and_157_out, and_130_out, and_129_out);
  xor xor_47 (xor_47_out, and_132_out, and_131_out);
  and and_158 (and_158_out, and_132_out, and_131_out);
  xor xor_48 (xor_48_out, and_133_out, or_63_out);
  and and_159 (and_159_out, and_133_out, or_63_out);
  or or_41 (or_41_out, and_143_out, and_101_out);
  or or_42 (or_42_out, and_144_out, and_102_out);
  or or_43 (or_43_out, and_145_out, and_103_out);
  or or_44 (or_44_out, and_146_out, and_104_out);
  or or_45 (or_45_out, and_147_out, and_105_out);
  or or_46 (or_46_out, and_148_out, and_106_out);
  or or_47 (or_47_out, and_149_out, and_107_out);
  or or_48 (Cout, and_150_out, and_108_out);
  or or_49 (or_49_out, and_181_out, and_166_out, and_151_out, and_134_out);
  or or_50 (or_50_out, and_110_out, and_135_out);
  or or_51 (or_51_out, and_111_out, and_136_out);
  or or_52 (or_52_out, and_112_out, and_137_out);
  or or_53 (or_53_out, and_113_out, and_138_out);
  or or_54 (or_54_out, and_114_out, and_139_out);
  or or_55 (or_55_out, and_115_out, and_140_out);
  or or_56 (or_56_out, and_116_out, and_141_out);
  or or_57 (or_57_out, and_117_out, and_142_out);
  xor xor_49 (xor_49_out, and_152_out, xor_42_out);
  and and_160 (and_160_out, xor_42_out, and_152_out);
  xor xor_50 (xor_50_out, or_58_out, xor_43_out);
  and and_161 (and_161_out, xor_43_out, or_58_out);
  xor xor_51 (xor_51_out, or_59_out, xor_44_out);
  and and_162 (and_162_out, xor_44_out, or_59_out);
  xor xor_52 (xor_52_out, or_60_out, xor_45_out);
  and and_163 (and_163_out, xor_45_out, or_60_out);
  xor xor_53 (xor_53_out, or_61_out, xor_46_out);
  and and_164 (and_164_out, xor_46_out, or_61_out);
  xor xor_54 (xor_54_out, or_62_out, xor_47_out);
  and and_165 (and_165_out, xor_47_out, or_62_out);
  and and_166 (and_166_out, not_1_out, OP2, OP1, not_4_out, nor_2_out);
  and and_167 (and_167_out, or_57_out, xor_25_out);
  and and_168 (and_168_out, A7, not_17_out);
  not not_17 (not_17_out, or_57_out);
  and and_169 (and_169_out, or_57_out, xor_26_out);
  and and_170 (and_170_out, 1'b0, not_18_out);
  not not_18 (not_18_out, or_57_out);
  and and_171 (and_171_out, or_57_out, xor_27_out);
  and and_172 (and_172_out, 1'b0, not_19_out);
  not not_19 (not_19_out, or_57_out);
  and and_173 (and_173_out, or_57_out, xor_28_out);
  and and_174 (and_174_out, 1'b0, not_20_out);
  not not_20 (not_20_out, or_57_out);
  and and_175 (and_175_out, or_57_out, xor_29_out);
  and and_176 (and_176_out, 1'b0, not_21_out);
  not not_21 (not_21_out, or_57_out);
  and and_177 (and_177_out, or_57_out, xor_30_out);
  and and_178 (and_178_out, 1'b0, not_22_out);
  not not_22 (not_22_out, or_57_out);
  and and_179 (and_179_out, or_57_out, xor_31_out);
  and and_180 (and_180_out, 1'b0, not_23_out);
  not not_23 (not_23_out, or_57_out);
  or or_58 (or_58_out, and_160_out, and_153_out);
  or or_59 (or_59_out, and_161_out, and_154_out);
  or or_60 (or_60_out, and_162_out, and_155_out);
  or or_61 (or_61_out, and_163_out, and_156_out);
  or or_62 (or_62_out, and_164_out, and_157_out);
  or or_63 (or_63_out, and_165_out, and_158_out);
  and and_181 (and_181_out, not_1_out, OP2, OP1, OP0, nand_2_out);
  or or_64 (or_64_out, and_167_out, and_168_out);
  or or_65 (or_65_out, and_169_out, and_170_out);
  or or_66 (or_66_out, and_171_out, and_172_out);
  or or_67 (or_67_out, and_173_out, and_174_out);
  or or_68 (or_68_out, and_175_out, and_176_out);
  or or_69 (or_69_out, and_177_out, and_178_out);
  or or_70 (or_70_out, and_179_out, and_180_out);
  and and_182 (and_182_out, OP3, not_2_out, not_3_out, not_4_out, xor_41_out);
  or or_71 (S1, or_95_out, or_72_out, or_49_out, or_32_out);
  and and_183 (and_183_out, OP3, not_2_out, not_3_out, OP0, or_196_out);
  xor xor_55 (xor_55_out, not_13_out, A6);
  and and_184 (and_184_out, A6, not_13_out);
  xor xor_56 (xor_56_out, not_14_out, or_64_out);
  and and_185 (and_185_out, or_64_out, not_14_out);
  xor xor_57 (xor_57_out, not_15_out, or_65_out);
  and and_186 (and_186_out, or_65_out, not_15_out);
  xor xor_58 (xor_58_out, not_16_out, or_66_out);
  and and_187 (and_187_out, or_66_out, not_16_out);
  xor xor_59 (xor_59_out, not_9_out, or_67_out);
  and and_188 (and_188_out, or_67_out, not_9_out);
  xor xor_60 (xor_60_out, not_10_out, or_68_out);
  and and_189 (and_189_out, or_68_out, not_10_out);
  xor xor_61 (xor_61_out, not_11_out, or_69_out);
  and and_190 (and_190_out, or_69_out, not_11_out);
  xor xor_62 (xor_62_out, not_12_out, or_70_out);
  and and_191 (and_191_out, or_70_out, not_12_out);
  and and_192 (and_192_out, A2, B0);
  and and_193 (and_193_out, A2, B1);
  and and_194 (and_194_out, A2, B2);
  and and_195 (and_195_out, A2, B3);
  and and_196 (and_196_out, A2, B4);
  and and_197 (and_197_out, A2, B5);
  and and_198 (and_198_out, A2, B6);
  and and_199 (and_199_out, A2, B7);
  or or_72 (or_72_out, and_217_out, and_208_out, and_183_out, and_182_out);
  xor xor_63 (xor_63_out, 1'b1, xor_55_out);
  and and_200 (and_200_out, xor_55_out, 1'b1);
  xor xor_64 (xor_64_out, or_73_out, xor_56_out);
  and and_201 (and_201_out, xor_56_out, or_73_out);
  xor xor_65 (xor_65_out, or_74_out, xor_57_out);
  and and_202 (and_202_out, xor_57_out, or_74_out);
  xor xor_66 (xor_66_out, or_75_out, xor_58_out);
  and and_203 (and_203_out, xor_58_out, or_75_out);
  xor xor_67 (xor_67_out, or_76_out, xor_59_out);
  and and_204 (and_204_out, xor_59_out, or_76_out);
  xor xor_68 (xor_68_out, or_77_out, xor_60_out);
  and and_205 (and_205_out, xor_60_out, or_77_out);
  xor xor_69 (xor_69_out, or_78_out, xor_61_out);
  and and_206 (and_206_out, xor_61_out, or_78_out);
  // XOr xor_70 has open pins: In_1=or_79_out, In_2=xor_62_out, out=open
  and and_207 (and_207_out, xor_62_out, or_79_out);
  and and_208 (and_208_out, OP3, not_2_out, OP1, not_4_out, xor_1_out);
  xor xor_71 (xor_71_out, xor_49_out, and_192_out);
  and and_209 (and_209_out, xor_49_out, and_192_out);
  xor xor_72 (xor_72_out, xor_50_out, and_193_out);
  and and_210 (and_210_out, xor_50_out, and_193_out);
  xor xor_73 (xor_73_out, xor_51_out, and_194_out);
  and and_211 (and_211_out, xor_51_out, and_194_out);
  xor xor_74 (xor_74_out, xor_52_out, and_195_out);
  and and_212 (and_212_out, xor_52_out, and_195_out);
  xor xor_75 (xor_75_out, xor_53_out, and_196_out);
  and and_213 (and_213_out, xor_53_out, and_196_out);
  xor xor_76 (xor_76_out, xor_54_out, and_197_out);
  and and_214 (and_214_out, xor_54_out, and_197_out);
  xor xor_77 (xor_77_out, xor_48_out, and_198_out);
  and and_215 (and_215_out, xor_48_out, and_198_out);
  xor xor_78 (xor_78_out, and_159_out, and_199_out);
  and and_216 (and_216_out, and_159_out, and_199_out);
  and and_217 (and_217_out, OP3, not_2_out, OP1, OP0, xor_3_out);
  or or_73 (or_73_out, and_184_out, and_200_out);
  not not_24 (not_24_out, or_80_out);
  or or_74 (or_74_out, and_185_out, and_201_out);
  not not_25 (not_25_out, or_80_out);
  or or_75 (or_75_out, and_186_out, and_202_out);
  not not_26 (not_26_out, or_80_out);
  or or_76 (or_76_out, and_187_out, and_203_out);
  not not_27 (not_27_out, or_80_out);
  or or_77 (or_77_out, and_188_out, and_204_out);
  not not_28 (not_28_out, or_80_out);
  or or_78 (or_78_out, and_189_out, and_205_out);
  not not_29 (not_29_out, or_80_out);
  or or_79 (or_79_out, and_190_out, and_206_out);
  not not_30 (not_30_out, or_80_out);
  or or_80 (or_80_out, and_191_out, and_207_out);
  xor xor_79 (xor_79_out, and_209_out, xor_72_out);
  and and_218 (and_218_out, xor_72_out, and_209_out);
  xor xor_80 (xor_80_out, or_88_out, xor_73_out);
  and and_219 (and_219_out, xor_73_out, or_88_out);
  xor xor_81 (xor_81_out, or_89_out, xor_74_out);
  and and_220 (and_220_out, xor_74_out, or_89_out);
  xor xor_82 (xor_82_out, or_90_out, xor_75_out);
  and and_221 (and_221_out, xor_75_out, or_90_out);
  xor xor_83 (xor_83_out, or_91_out, xor_76_out);
  and and_222 (and_222_out, xor_76_out, or_91_out);
  xor xor_84 (xor_84_out, or_92_out, xor_77_out);
  and and_223 (and_223_out, xor_77_out, or_92_out);
  xor xor_85 (xor_85_out, or_93_out, xor_78_out);
  and and_224 (and_224_out, xor_78_out, or_93_out);
  and and_225 (and_225_out, OP3, OP2, not_3_out, not_4_out, or_220_out);
  and and_226 (and_226_out, or_80_out, xor_63_out);
  and and_227 (and_227_out, A6, not_24_out);
  and and_228 (and_228_out, or_80_out, xor_64_out);
  and and_229 (and_229_out, or_64_out, not_25_out);
  and and_230 (and_230_out, or_80_out, xor_65_out);
  and and_231 (and_231_out, or_65_out, not_26_out);
  and and_232 (and_232_out, or_80_out, xor_66_out);
  and and_233 (and_233_out, or_66_out, not_27_out);
  and and_234 (and_234_out, or_80_out, xor_67_out);
  and and_235 (and_235_out, or_67_out, not_28_out);
  and and_236 (and_236_out, or_80_out, xor_68_out);
  and and_237 (and_237_out, or_68_out, not_29_out);
  and and_238 (and_238_out, or_80_out, xor_69_out);
  and and_239 (and_239_out, or_69_out, not_30_out);
  and and_240 (and_240_out, OP3, OP2, not_3_out, OP0, 1'b0);
  or or_81 (or_81_out, and_226_out, and_227_out);
  or or_82 (or_82_out, and_228_out, and_229_out);
  or or_83 (or_83_out, and_230_out, and_231_out);
  or or_84 (or_84_out, and_232_out, and_233_out);
  or or_85 (or_85_out, and_234_out, and_235_out);
  or or_86 (or_86_out, and_236_out, and_237_out);
  or or_87 (or_87_out, and_238_out, and_239_out);
  or or_88 (or_88_out, and_218_out, and_210_out);
  or or_89 (or_89_out, and_219_out, and_211_out);
  or or_90 (or_90_out, and_220_out, and_212_out);
  or or_91 (or_91_out, and_221_out, and_213_out);
  or or_92 (or_92_out, and_222_out, and_214_out);
  or or_93 (or_93_out, and_223_out, and_215_out);
  or or_94 (or_94_out, and_224_out, and_216_out);
  or or_95 (or_95_out, and_250_out, and_241_out, and_240_out, and_225_out);
  xor xor_86 (xor_86_out, not_13_out, A5);
  xor xor_87 (xor_87_out, not_14_out, or_81_out);
  xor xor_88 (xor_88_out, not_15_out, or_82_out);
  xor xor_89 (xor_89_out, not_16_out, or_83_out);
  xor xor_90 (xor_90_out, not_9_out, or_84_out);
  xor xor_91 (xor_91_out, not_10_out, or_85_out);
  xor xor_92 (xor_92_out, not_11_out, or_86_out);
  xor xor_93 (xor_93_out, not_12_out, or_87_out);
  and and_241 (and_241_out, OP3, OP2, OP1, not_4_out, 1'b0);
  and and_242 (and_242_out, A5, not_13_out);
  and and_243 (and_243_out, or_81_out, not_14_out);
  and and_244 (and_244_out, or_82_out, not_15_out);
  and and_245 (and_245_out, or_83_out, not_16_out);
  and and_246 (and_246_out, or_84_out, not_9_out);
  and and_247 (and_247_out, or_85_out, not_10_out);
  and and_248 (and_248_out, or_86_out, not_11_out);
  and and_249 (and_249_out, or_87_out, not_12_out);
  and and_250 (and_250_out, OP3, OP2, OP1, OP0, 1'b0);
  xor xor_94 (xor_94_out, 1'b1, xor_86_out);
  and and_251 (and_251_out, xor_86_out, 1'b1);
  xor xor_95 (xor_95_out, or_96_out, xor_87_out);
  and and_252 (and_252_out, xor_87_out, or_96_out);
  xor xor_96 (xor_96_out, or_97_out, xor_88_out);
  and and_253 (and_253_out, xor_88_out, or_97_out);
  xor xor_97 (xor_97_out, or_98_out, xor_89_out);
  and and_254 (and_254_out, xor_89_out, or_98_out);
  xor xor_98 (xor_98_out, or_99_out, xor_90_out);
  and and_255 (and_255_out, xor_90_out, or_99_out);
  xor xor_99 (xor_99_out, or_100_out, xor_91_out);
  and and_256 (and_256_out, xor_91_out, or_100_out);
  xor xor_100 (xor_100_out, or_101_out, xor_92_out);
  and and_257 (and_257_out, xor_92_out, or_101_out);
  // XOr xor_101 has open pins: In_1=or_102_out, In_2=xor_93_out, out=open
  and and_258 (and_258_out, xor_93_out, or_102_out);
  and and_259 (and_259_out, A3, B0);
  and and_260 (and_260_out, A3, B1);
  and and_261 (and_261_out, A3, B2);
  and and_262 (and_262_out, A3, B3);
  and and_263 (and_263_out, A3, B4);
  and and_264 (and_264_out, A3, B5);
  and and_265 (and_265_out, A3, B6);
  and and_266 (and_266_out, A3, B7);
  and and_267 (and_267_out, not_1_out, not_2_out, not_3_out, not_4_out, xor_1_out);
  xor xor_102 (xor_102_out, xor_79_out, and_259_out);
  and and_268 (and_268_out, xor_79_out, and_259_out);
  xor xor_103 (xor_103_out, xor_80_out, and_260_out);
  and and_269 (and_269_out, xor_80_out, and_260_out);
  xor xor_104 (xor_104_out, xor_81_out, and_261_out);
  and and_270 (and_270_out, xor_81_out, and_261_out);
  xor xor_105 (xor_105_out, xor_82_out, and_262_out);
  and and_271 (and_271_out, xor_82_out, and_262_out);
  xor xor_106 (xor_106_out, xor_83_out, and_263_out);
  and and_272 (and_272_out, xor_83_out, and_263_out);
  xor xor_107 (xor_107_out, xor_84_out, and_264_out);
  and and_273 (and_273_out, xor_84_out, and_264_out);
  xor xor_108 (xor_108_out, xor_85_out, and_265_out);
  and and_274 (and_274_out, xor_85_out, and_265_out);
  xor xor_109 (xor_109_out, or_94_out, and_266_out);
  and and_275 (and_275_out, or_94_out, and_266_out);
  and and_276 (and_276_out, not_1_out, not_2_out, not_3_out, OP0, or_33_out);
  or or_96 (or_96_out, and_242_out, and_251_out);
  not not_31 (not_31_out, or_103_out);
  or or_97 (or_97_out, and_243_out, and_252_out);
  not not_32 (not_32_out, or_103_out);
  or or_98 (or_98_out, and_244_out, and_253_out);
  not not_33 (not_33_out, or_103_out);
  or or_99 (or_99_out, and_245_out, and_254_out);
  not not_34 (not_34_out, or_103_out);
  or or_100 (or_100_out, and_246_out, and_255_out);
  not not_35 (not_35_out, or_103_out);
  or or_101 (or_101_out, and_247_out, and_256_out);
  not not_36 (not_36_out, or_103_out);
  or or_102 (or_102_out, and_248_out, and_257_out);
  not not_37 (not_37_out, or_103_out);
  or or_103 (or_103_out, and_249_out, and_258_out);
  or or_104 (or_104_out, and_299_out, and_298_out, and_276_out, and_267_out);
  and and_277 (and_277_out, or_103_out, xor_94_out);
  and and_278 (and_278_out, A5, not_31_out);
  and and_279 (and_279_out, or_103_out, xor_95_out);
  and and_280 (and_280_out, or_81_out, not_32_out);
  and and_281 (and_281_out, or_103_out, xor_96_out);
  and and_282 (and_282_out, or_82_out, not_33_out);
  and and_283 (and_283_out, or_103_out, xor_97_out);
  and and_284 (and_284_out, or_83_out, not_34_out);
  and and_285 (and_285_out, or_103_out, xor_98_out);
  and and_286 (and_286_out, or_84_out, not_35_out);
  and and_287 (and_287_out, or_103_out, xor_99_out);
  and and_288 (and_288_out, or_85_out, not_36_out);
  and and_289 (and_289_out, or_103_out, xor_100_out);
  and and_290 (and_290_out, or_86_out, not_37_out);
  xor xor_110 (xor_110_out, and_268_out, xor_103_out);
  and and_291 (and_291_out, xor_103_out, and_268_out);
  xor xor_111 (xor_111_out, or_112_out, xor_104_out);
  and and_292 (and_292_out, xor_104_out, or_112_out);
  xor xor_112 (xor_112_out, or_113_out, xor_105_out);
  and and_293 (and_293_out, xor_105_out, or_113_out);
  xor xor_113 (xor_113_out, or_114_out, xor_106_out);
  and and_294 (and_294_out, xor_106_out, or_114_out);
  xor xor_114 (xor_114_out, or_115_out, xor_107_out);
  and and_295 (and_295_out, xor_107_out, or_115_out);
  xor xor_115 (xor_115_out, or_116_out, xor_108_out);
  and and_296 (and_296_out, xor_108_out, or_116_out);
  xor xor_116 (xor_116_out, or_117_out, xor_109_out);
  and and_297 (and_297_out, xor_109_out, or_117_out);
  and and_298 (and_298_out, not_1_out, not_2_out, OP1, not_4_out, and_101_out);
  or or_105 (or_105_out, and_277_out, and_278_out);
  or or_106 (or_106_out, and_279_out, and_280_out);
  or or_107 (or_107_out, and_281_out, and_282_out);
  or or_108 (or_108_out, and_283_out, and_284_out);
  or or_109 (or_109_out, and_285_out, and_286_out);
  or or_110 (or_110_out, and_287_out, and_288_out);
  or or_111 (or_111_out, and_289_out, and_290_out);
  or or_112 (or_112_out, and_291_out, and_269_out);
  or or_113 (or_113_out, and_292_out, and_270_out);
  or or_114 (or_114_out, and_293_out, and_271_out);
  or or_115 (or_115_out, and_294_out, and_272_out);
  or or_116 (or_116_out, and_295_out, and_273_out);
  or or_117 (or_117_out, and_296_out, and_274_out);
  or or_118 (or_118_out, and_297_out, and_275_out);
  and and_299 (and_299_out, not_1_out, not_2_out, OP1, OP0, xor_9_out);
  xor xor_117 (xor_117_out, not_13_out, A4);
  and and_300 (and_300_out, A4, not_13_out);
  xor xor_118 (xor_118_out, not_14_out, or_105_out);
  and and_301 (and_301_out, or_105_out, not_14_out);
  xor xor_119 (xor_119_out, not_15_out, or_106_out);
  and and_302 (and_302_out, or_106_out, not_15_out);
  xor xor_120 (xor_120_out, not_16_out, or_107_out);
  and and_303 (and_303_out, or_107_out, not_16_out);
  xor xor_121 (xor_121_out, not_9_out, or_108_out);
  and and_304 (and_304_out, or_108_out, not_9_out);
  xor xor_122 (xor_122_out, not_10_out, or_109_out);
  and and_305 (and_305_out, or_109_out, not_10_out);
  xor xor_123 (xor_123_out, not_11_out, or_110_out);
  and and_306 (and_306_out, or_110_out, not_11_out);
  xor xor_124 (xor_124_out, not_12_out, or_111_out);
  and and_307 (and_307_out, or_111_out, not_12_out);
  and and_308 (and_308_out, not_1_out, OP2, not_3_out, not_4_out, xor_33_out);
  xor xor_125 (xor_125_out, 1'b1, xor_117_out);
  and and_309 (and_309_out, xor_117_out, 1'b1);
  xor xor_126 (xor_126_out, or_120_out, xor_118_out);
  and and_310 (and_310_out, xor_118_out, or_120_out);
  xor xor_127 (xor_127_out, or_121_out, xor_119_out);
  and and_311 (and_311_out, xor_119_out, or_121_out);
  xor xor_128 (xor_128_out, or_122_out, xor_120_out);
  and and_312 (and_312_out, xor_120_out, or_122_out);
  xor xor_129 (xor_129_out, or_123_out, xor_121_out);
  and and_313 (and_313_out, xor_121_out, or_123_out);
  xor xor_130 (xor_130_out, or_124_out, xor_122_out);
  and and_314 (and_314_out, xor_122_out, or_124_out);
  xor xor_131 (xor_131_out, or_125_out, xor_123_out);
  and and_315 (and_315_out, xor_123_out, or_125_out);
  // XOr xor_132 has open pins: In_1=or_126_out, In_2=xor_124_out, out=open
  and and_316 (and_316_out, xor_124_out, or_126_out);
  and and_317 (and_317_out, not_1_out, OP2, not_3_out, OP0, xnor_1_out);
  and and_318 (and_318_out, A4, B0);
  and and_319 (and_319_out, A4, B1);
  and and_320 (and_320_out, A4, B2);
  and and_321 (and_321_out, A4, B3);
  and and_322 (and_322_out, A4, B4);
  and and_323 (and_323_out, A4, B5);
  and and_324 (and_324_out, A4, B6);
  and and_325 (and_325_out, A4, B7);
  or or_119 (or_119_out, and_349_out, and_326_out, and_317_out, and_308_out);
  or or_120 (or_120_out, and_300_out, and_309_out);
  or or_121 (or_121_out, and_301_out, and_310_out);
  or or_122 (or_122_out, and_302_out, and_311_out);
  or or_123 (or_123_out, and_303_out, and_312_out);
  or or_124 (or_124_out, and_304_out, and_313_out);
  or or_125 (or_125_out, and_305_out, and_314_out);
  or or_126 (or_126_out, and_306_out, and_315_out);
  or or_127 (or_127_out, and_307_out, and_316_out);
  and and_326 (and_326_out, not_1_out, OP2, OP1, not_4_out, nor_1_out);
  and and_327 (and_327_out, or_127_out, xor_125_out);
  and and_328 (and_328_out, A4, not_38_out);
  not not_38 (not_38_out, or_127_out);
  and and_329 (and_329_out, or_127_out, xor_126_out);
  and and_330 (and_330_out, or_105_out, not_39_out);
  not not_39 (not_39_out, or_127_out);
  and and_331 (and_331_out, or_127_out, xor_127_out);
  and and_332 (and_332_out, or_106_out, not_40_out);
  not not_40 (not_40_out, or_127_out);
  and and_333 (and_333_out, or_127_out, xor_128_out);
  and and_334 (and_334_out, or_107_out, not_41_out);
  not not_41 (not_41_out, or_127_out);
  and and_335 (and_335_out, or_127_out, xor_129_out);
  and and_336 (and_336_out, or_108_out, not_42_out);
  not not_42 (not_42_out, or_127_out);
  and and_337 (and_337_out, or_127_out, xor_130_out);
  and and_338 (and_338_out, or_109_out, not_43_out);
  not not_43 (not_43_out, or_127_out);
  and and_339 (and_339_out, or_127_out, xor_131_out);
  and and_340 (and_340_out, or_110_out, not_44_out);
  not not_44 (not_44_out, or_127_out);
  xor xor_133 (xor_133_out, xor_110_out, and_318_out);
  and and_341 (and_341_out, xor_110_out, and_318_out);
  xor xor_134 (xor_134_out, xor_111_out, and_319_out);
  and and_342 (and_342_out, xor_111_out, and_319_out);
  xor xor_135 (xor_135_out, xor_112_out, and_320_out);
  and and_343 (and_343_out, xor_112_out, and_320_out);
  xor xor_136 (xor_136_out, xor_113_out, and_321_out);
  and and_344 (and_344_out, xor_113_out, and_321_out);
  xor xor_137 (xor_137_out, xor_114_out, and_322_out);
  and and_345 (and_345_out, xor_114_out, and_322_out);
  xor xor_138 (xor_138_out, xor_115_out, and_323_out);
  and and_346 (and_346_out, xor_115_out, and_323_out);
  xor xor_139 (xor_139_out, xor_116_out, and_324_out);
  and and_347 (and_347_out, xor_116_out, and_324_out);
  xor xor_140 (xor_140_out, or_118_out, and_325_out);
  and and_348 (and_348_out, or_118_out, and_325_out);
  and and_349 (and_349_out, not_1_out, OP2, OP1, OP0, nand_1_out);
  or or_128 (or_128_out, and_327_out, and_328_out);
  or or_129 (or_129_out, and_329_out, and_330_out);
  or or_130 (or_130_out, and_331_out, and_332_out);
  or or_131 (or_131_out, and_333_out, and_334_out);
  or or_132 (or_132_out, and_335_out, and_336_out);
  or or_133 (or_133_out, and_337_out, and_338_out);
  or or_134 (or_134_out, and_339_out, and_340_out);
  xor xor_141 (xor_141_out, and_341_out, xor_134_out);
  and and_350 (and_350_out, xor_134_out, and_341_out);
  xor xor_142 (xor_142_out, or_136_out, xor_135_out);
  and and_351 (and_351_out, xor_135_out, or_136_out);
  xor xor_143 (xor_143_out, or_137_out, xor_136_out);
  and and_352 (and_352_out, xor_136_out, or_137_out);
  xor xor_144 (xor_144_out, or_138_out, xor_137_out);
  and and_353 (and_353_out, xor_137_out, or_138_out);
  xor xor_145 (xor_145_out, or_139_out, xor_138_out);
  and and_354 (and_354_out, xor_138_out, or_139_out);
  xor xor_146 (xor_146_out, or_140_out, xor_139_out);
  and and_355 (and_355_out, xor_139_out, or_140_out);
  xor xor_147 (xor_147_out, or_141_out, xor_140_out);
  and and_356 (and_356_out, xor_140_out, or_141_out);
  and and_357 (and_357_out, OP3, not_2_out, not_3_out, not_4_out, and_118_out);
  or or_135 (S0, or_159_out, or_143_out, or_119_out, or_104_out);
  or or_136 (or_136_out, and_350_out, and_342_out);
  or or_137 (or_137_out, and_351_out, and_343_out);
  or or_138 (or_138_out, and_352_out, and_344_out);
  or or_139 (or_139_out, and_353_out, and_345_out);
  or or_140 (or_140_out, and_354_out, and_346_out);
  or or_141 (or_141_out, and_355_out, and_347_out);
  or or_142 (or_142_out, and_356_out, and_348_out);
  and and_358 (and_358_out, OP3, not_2_out, not_3_out, OP0, or_218_out);
  xor xor_148 (xor_148_out, not_13_out, A3);
  and and_359 (and_359_out, A3, not_13_out);
  xor xor_149 (xor_149_out, not_14_out, or_128_out);
  and and_360 (and_360_out, or_128_out, not_14_out);
  xor xor_150 (xor_150_out, not_15_out, or_129_out);
  and and_361 (and_361_out, or_129_out, not_15_out);
  xor xor_151 (xor_151_out, not_16_out, or_130_out);
  and and_362 (and_362_out, or_130_out, not_16_out);
  xor xor_152 (xor_152_out, not_9_out, or_131_out);
  and and_363 (and_363_out, or_131_out, not_9_out);
  xor xor_153 (xor_153_out, not_10_out, or_132_out);
  and and_364 (and_364_out, or_132_out, not_10_out);
  xor xor_154 (xor_154_out, not_11_out, or_133_out);
  and and_365 (and_365_out, or_133_out, not_11_out);
  xor xor_155 (xor_155_out, not_12_out, or_134_out);
  and and_366 (and_366_out, or_134_out, not_12_out);
  or or_143 (or_143_out, and_376_out, and_375_out, and_358_out, and_357_out);
  xor xor_156 (xor_156_out, 1'b1, xor_148_out);
  and and_367 (and_367_out, xor_148_out, 1'b1);
  xor xor_157 (xor_157_out, or_144_out, xor_149_out);
  and and_368 (and_368_out, xor_149_out, or_144_out);
  xor xor_158 (xor_158_out, or_145_out, xor_150_out);
  and and_369 (and_369_out, xor_150_out, or_145_out);
  xor xor_159 (xor_159_out, or_146_out, xor_151_out);
  and and_370 (and_370_out, xor_151_out, or_146_out);
  xor xor_160 (xor_160_out, or_147_out, xor_152_out);
  and and_371 (and_371_out, xor_152_out, or_147_out);
  xor xor_161 (xor_161_out, or_148_out, xor_153_out);
  and and_372 (and_372_out, xor_153_out, or_148_out);
  xor xor_162 (xor_162_out, or_149_out, xor_154_out);
  and and_373 (and_373_out, xor_154_out, or_149_out);
  // XOr xor_163 has open pins: In_1=or_150_out, In_2=xor_155_out, out=open
  and and_374 (and_374_out, xor_155_out, or_150_out);
  and and_375 (and_375_out, OP3, not_2_out, OP1, not_4_out, 1'b0);
  and and_376 (and_376_out, OP3, not_2_out, OP1, OP0, xor_2_out);
  or or_144 (or_144_out, and_359_out, and_367_out);
  or or_145 (or_145_out, and_360_out, and_368_out);
  or or_146 (or_146_out, and_361_out, and_369_out);
  or or_147 (or_147_out, and_362_out, and_370_out);
  or or_148 (or_148_out, and_363_out, and_371_out);
  or or_149 (or_149_out, and_364_out, and_372_out);
  or or_150 (or_150_out, and_365_out, and_373_out);
  or or_151 (or_151_out, and_366_out, and_374_out);
  and and_377 (and_377_out, A5, B0);
  and and_378 (and_378_out, A5, B1);
  and and_379 (and_379_out, A5, B2);
  and and_380 (and_380_out, A5, B3);
  and and_381 (and_381_out, A5, B4);
  and and_382 (and_382_out, A5, B5);
  and and_383 (and_383_out, A5, B6);
  and and_384 (and_384_out, A5, B7);
  and and_385 (and_385_out, OP3, OP2, not_3_out, not_4_out, or_219_out);
  and and_386 (and_386_out, or_151_out, xor_156_out);
  and and_387 (and_387_out, A3, not_45_out);
  not not_45 (not_45_out, or_151_out);
  and and_388 (and_388_out, or_151_out, xor_157_out);
  and and_389 (and_389_out, or_128_out, not_46_out);
  not not_46 (not_46_out, or_151_out);
  and and_390 (and_390_out, or_151_out, xor_158_out);
  and and_391 (and_391_out, or_129_out, not_47_out);
  not not_47 (not_47_out, or_151_out);
  and and_392 (and_392_out, or_151_out, xor_159_out);
  and and_393 (and_393_out, or_130_out, not_48_out);
  not not_48 (not_48_out, or_151_out);
  and and_394 (and_394_out, or_151_out, xor_160_out);
  and and_395 (and_395_out, or_131_out, not_49_out);
  not not_49 (not_49_out, or_151_out);
  and and_396 (and_396_out, or_151_out, xor_161_out);
  and and_397 (and_397_out, or_132_out, not_50_out);
  not not_50 (not_50_out, or_151_out);
  and and_398 (and_398_out, or_151_out, xor_162_out);
  and and_399 (and_399_out, or_133_out, not_51_out);
  not not_51 (not_51_out, or_151_out);
  xor xor_164 (xor_164_out, xor_141_out, and_377_out);
  and and_400 (and_400_out, xor_141_out, and_377_out);
  xor xor_165 (xor_165_out, xor_142_out, and_378_out);
  and and_401 (and_401_out, xor_142_out, and_378_out);
  xor xor_166 (xor_166_out, xor_143_out, and_379_out);
  and and_402 (and_402_out, xor_143_out, and_379_out);
  xor xor_167 (xor_167_out, xor_144_out, and_380_out);
  and and_403 (and_403_out, xor_144_out, and_380_out);
  xor xor_168 (xor_168_out, xor_145_out, and_381_out);
  and and_404 (and_404_out, xor_145_out, and_381_out);
  xor xor_169 (xor_169_out, xor_146_out, and_382_out);
  and and_405 (and_405_out, xor_146_out, and_382_out);
  xor xor_170 (xor_170_out, xor_147_out, and_383_out);
  and and_406 (and_406_out, xor_147_out, and_383_out);
  xor xor_171 (xor_171_out, or_142_out, and_384_out);
  and and_407 (and_407_out, or_142_out, and_384_out);
  and and_408 (and_408_out, OP3, OP2, not_3_out, OP0, 1'b0);
  or or_152 (or_152_out, and_386_out, and_387_out);
  or or_153 (or_153_out, and_388_out, and_389_out);
  or or_154 (or_154_out, and_390_out, and_391_out);
  or or_155 (or_155_out, and_392_out, and_393_out);
  or or_156 (or_156_out, and_394_out, and_395_out);
  or or_157 (or_157_out, and_396_out, and_397_out);
  or or_158 (or_158_out, and_398_out, and_399_out);
  or or_159 (or_159_out, and_425_out, and_416_out, and_408_out, and_385_out);
  xor xor_172 (xor_172_out, and_400_out, xor_165_out);
  and and_409 (and_409_out, xor_165_out, and_400_out);
  xor xor_173 (xor_173_out, or_160_out, xor_166_out);
  and and_410 (and_410_out, xor_166_out, or_160_out);
  xor xor_174 (xor_174_out, or_161_out, xor_167_out);
  and and_411 (and_411_out, xor_167_out, or_161_out);
  xor xor_175 (xor_175_out, or_162_out, xor_168_out);
  and and_412 (and_412_out, xor_168_out, or_162_out);
  xor xor_176 (xor_176_out, or_163_out, xor_169_out);
  and and_413 (and_413_out, xor_169_out, or_163_out);
  xor xor_177 (xor_177_out, or_164_out, xor_170_out);
  and and_414 (and_414_out, xor_170_out, or_164_out);
  xor xor_178 (xor_178_out, or_165_out, xor_171_out);
  and and_415 (and_415_out, xor_171_out, or_165_out);
  and and_416 (and_416_out, OP3, OP2, OP1, not_4_out, 1'b0);
  xor xor_179 (xor_179_out, not_13_out, A2);
  and and_417 (and_417_out, A2, not_13_out);
  xor xor_180 (xor_180_out, not_14_out, or_152_out);
  and and_418 (and_418_out, or_152_out, not_14_out);
  xor xor_181 (xor_181_out, not_15_out, or_153_out);
  and and_419 (and_419_out, or_153_out, not_15_out);
  xor xor_182 (xor_182_out, not_16_out, or_154_out);
  and and_420 (and_420_out, or_154_out, not_16_out);
  xor xor_183 (xor_183_out, not_9_out, or_155_out);
  and and_421 (and_421_out, or_155_out, not_9_out);
  xor xor_184 (xor_184_out, not_10_out, or_156_out);
  and and_422 (and_422_out, or_156_out, not_10_out);
  xor xor_185 (xor_185_out, not_11_out, or_157_out);
  and and_423 (and_423_out, or_157_out, not_11_out);
  xor xor_186 (xor_186_out, not_12_out, or_158_out);
  and and_424 (and_424_out, or_158_out, not_12_out);
  or or_160 (or_160_out, and_409_out, and_401_out);
  or or_161 (or_161_out, and_410_out, and_402_out);
  or or_162 (or_162_out, and_411_out, and_403_out);
  or or_163 (or_163_out, and_412_out, and_404_out);
  or or_164 (or_164_out, and_413_out, and_405_out);
  or or_165 (or_165_out, and_414_out, and_406_out);
  or or_166 (or_166_out, and_415_out, and_407_out);
  and and_425 (and_425_out, OP3, OP2, OP1, OP0, 1'b0);
  xor xor_187 (xor_187_out, 1'b1, xor_179_out);
  and and_426 (and_426_out, xor_179_out, 1'b1);
  xor xor_188 (xor_188_out, or_167_out, xor_180_out);
  and and_427 (and_427_out, xor_180_out, or_167_out);
  xor xor_189 (xor_189_out, or_168_out, xor_181_out);
  and and_428 (and_428_out, xor_181_out, or_168_out);
  xor xor_190 (xor_190_out, or_169_out, xor_182_out);
  and and_429 (and_429_out, xor_182_out, or_169_out);
  xor xor_191 (xor_191_out, or_170_out, xor_183_out);
  and and_430 (and_430_out, xor_183_out, or_170_out);
  xor xor_192 (xor_192_out, or_171_out, xor_184_out);
  and and_431 (and_431_out, xor_184_out, or_171_out);
  xor xor_193 (xor_193_out, or_172_out, xor_185_out);
  and and_432 (and_432_out, xor_185_out, or_172_out);
  // XOr xor_194 has open pins: In_1=or_173_out, In_2=xor_186_out, out=open
  and and_433 (and_433_out, xor_186_out, or_173_out);
  or or_167 (or_167_out, and_417_out, and_426_out);
  not not_52 (not_52_out, or_174_out);
  or or_168 (or_168_out, and_418_out, and_427_out);
  not not_53 (not_53_out, or_174_out);
  or or_169 (or_169_out, and_419_out, and_428_out);
  not not_54 (not_54_out, or_174_out);
  or or_170 (or_170_out, and_420_out, and_429_out);
  not not_55 (not_55_out, or_174_out);
  or or_171 (or_171_out, and_421_out, and_430_out);
  not not_56 (not_56_out, or_174_out);
  or or_172 (or_172_out, and_422_out, and_431_out);
  not not_57 (not_57_out, or_174_out);
  or or_173 (or_173_out, and_423_out, and_432_out);
  not not_58 (not_58_out, or_174_out);
  or or_174 (or_174_out, and_424_out, and_433_out);
  and and_434 (and_434_out, A6, B0);
  and and_435 (and_435_out, A6, B1);
  and and_436 (and_436_out, A6, B2);
  and and_437 (and_437_out, A6, B3);
  and and_438 (and_438_out, A6, B4);
  and and_439 (and_439_out, A6, B5);
  and and_440 (and_440_out, A6, B6);
  and and_441 (and_441_out, A6, B7);
  and and_442 (and_442_out, or_174_out, xor_187_out);
  and and_443 (and_443_out, A2, not_52_out);
  and and_444 (and_444_out, or_174_out, xor_188_out);
  and and_445 (and_445_out, or_152_out, not_53_out);
  and and_446 (and_446_out, or_174_out, xor_189_out);
  and and_447 (and_447_out, or_153_out, not_54_out);
  and and_448 (and_448_out, or_174_out, xor_190_out);
  and and_449 (and_449_out, or_154_out, not_55_out);
  and and_450 (and_450_out, or_174_out, xor_191_out);
  and and_451 (and_451_out, or_155_out, not_56_out);
  and and_452 (and_452_out, or_174_out, xor_192_out);
  and and_453 (and_453_out, or_156_out, not_57_out);
  and and_454 (and_454_out, or_174_out, xor_193_out);
  and and_455 (and_455_out, or_157_out, not_58_out);
  or or_175 (or_175_out, and_442_out, and_443_out);
  or or_176 (or_176_out, and_444_out, and_445_out);
  or or_177 (or_177_out, and_446_out, and_447_out);
  or or_178 (or_178_out, and_448_out, and_449_out);
  or or_179 (or_179_out, and_450_out, and_451_out);
  or or_180 (or_180_out, and_452_out, and_453_out);
  or or_181 (or_181_out, and_454_out, and_455_out);
  xor xor_195 (xor_195_out, xor_172_out, and_434_out);
  and and_456 (and_456_out, xor_172_out, and_434_out);
  xor xor_196 (xor_196_out, xor_173_out, and_435_out);
  and and_457 (and_457_out, xor_173_out, and_435_out);
  xor xor_197 (xor_197_out, xor_174_out, and_436_out);
  and and_458 (and_458_out, xor_174_out, and_436_out);
  xor xor_198 (xor_198_out, xor_175_out, and_437_out);
  and and_459 (and_459_out, xor_175_out, and_437_out);
  xor xor_199 (xor_199_out, xor_176_out, and_438_out);
  and and_460 (and_460_out, xor_176_out, and_438_out);
  xor xor_200 (xor_200_out, xor_177_out, and_439_out);
  and and_461 (and_461_out, xor_177_out, and_439_out);
  xor xor_201 (xor_201_out, xor_178_out, and_440_out);
  and and_462 (and_462_out, xor_178_out, and_440_out);
  xor xor_202 (xor_202_out, or_166_out, and_441_out);
  and and_463 (and_463_out, or_166_out, and_441_out);
  xor xor_203 (xor_203_out, not_13_out, A1);
  xor xor_204 (xor_204_out, not_14_out, or_175_out);
  xor xor_205 (xor_205_out, not_15_out, or_176_out);
  xor xor_206 (xor_206_out, not_16_out, or_177_out);
  xor xor_207 (xor_207_out, not_9_out, or_178_out);
  xor xor_208 (xor_208_out, not_10_out, or_179_out);
  xor xor_209 (xor_209_out, not_11_out, or_180_out);
  xor xor_210 (xor_210_out, not_12_out, or_181_out);
  xor xor_211 (xor_211_out, and_456_out, xor_196_out);
  and and_464 (and_464_out, xor_196_out, and_456_out);
  xor xor_212 (xor_212_out, or_182_out, xor_197_out);
  and and_465 (and_465_out, xor_197_out, or_182_out);
  xor xor_213 (xor_213_out, or_183_out, xor_198_out);
  and and_466 (and_466_out, xor_198_out, or_183_out);
  xor xor_214 (xor_214_out, or_184_out, xor_199_out);
  and and_467 (and_467_out, xor_199_out, or_184_out);
  xor xor_215 (xor_215_out, or_185_out, xor_200_out);
  and and_468 (and_468_out, xor_200_out, or_185_out);
  xor xor_216 (xor_216_out, or_186_out, xor_201_out);
  and and_469 (and_469_out, xor_201_out, or_186_out);
  xor xor_217 (xor_217_out, or_187_out, xor_202_out);
  and and_470 (and_470_out, xor_202_out, or_187_out);
  and and_471 (and_471_out, A1, not_13_out);
  and and_472 (and_472_out, or_175_out, not_14_out);
  and and_473 (and_473_out, or_176_out, not_15_out);
  and and_474 (and_474_out, or_177_out, not_16_out);
  and and_475 (and_475_out, or_178_out, not_9_out);
  and and_476 (and_476_out, or_179_out, not_10_out);
  and and_477 (and_477_out, or_180_out, not_11_out);
  and and_478 (and_478_out, or_181_out, not_12_out);
  or or_182 (or_182_out, and_464_out, and_457_out);
  or or_183 (or_183_out, and_465_out, and_458_out);
  or or_184 (or_184_out, and_466_out, and_459_out);
  or or_185 (or_185_out, and_467_out, and_460_out);
  or or_186 (or_186_out, and_468_out, and_461_out);
  or or_187 (or_187_out, and_469_out, and_462_out);
  or or_188 (or_188_out, and_470_out, and_463_out);
  xor xor_218 (xor_218_out, 1'b1, xor_203_out);
  and and_479 (and_479_out, xor_203_out, 1'b1);
  xor xor_219 (xor_219_out, or_189_out, xor_204_out);
  and and_480 (and_480_out, xor_204_out, or_189_out);
  xor xor_220 (xor_220_out, or_190_out, xor_205_out);
  and and_481 (and_481_out, xor_205_out, or_190_out);
  xor xor_221 (xor_221_out, or_191_out, xor_206_out);
  and and_482 (and_482_out, xor_206_out, or_191_out);
  xor xor_222 (xor_222_out, or_192_out, xor_207_out);
  and and_483 (and_483_out, xor_207_out, or_192_out);
  xor xor_223 (xor_223_out, or_193_out, xor_208_out);
  and and_484 (and_484_out, xor_208_out, or_193_out);
  xor xor_224 (xor_224_out, or_194_out, xor_209_out);
  and and_485 (and_485_out, xor_209_out, or_194_out);
  // XOr xor_225 has open pins: In_1=or_195_out, In_2=xor_210_out, out=open
  and and_486 (and_486_out, xor_210_out, or_195_out);
  or or_189 (or_189_out, and_471_out, and_479_out);
  not not_59 (not_59_out, or_196_out);
  or or_190 (or_190_out, and_472_out, and_480_out);
  not not_60 (not_60_out, or_196_out);
  or or_191 (or_191_out, and_473_out, and_481_out);
  not not_61 (not_61_out, or_196_out);
  or or_192 (or_192_out, and_474_out, and_482_out);
  not not_62 (not_62_out, or_196_out);
  or or_193 (or_193_out, and_475_out, and_483_out);
  not not_63 (not_63_out, or_196_out);
  or or_194 (or_194_out, and_476_out, and_484_out);
  not not_64 (not_64_out, or_196_out);
  or or_195 (or_195_out, and_477_out, and_485_out);
  not not_65 (not_65_out, or_196_out);
  or or_196 (or_196_out, and_478_out, and_486_out);
  and and_487 (and_487_out, or_196_out, xor_218_out);
  and and_488 (and_488_out, A1, not_59_out);
  and and_489 (and_489_out, or_196_out, xor_219_out);
  and and_490 (and_490_out, or_175_out, not_60_out);
  and and_491 (and_491_out, or_196_out, xor_220_out);
  and and_492 (and_492_out, or_176_out, not_61_out);
  and and_493 (and_493_out, or_196_out, xor_221_out);
  and and_494 (and_494_out, or_177_out, not_62_out);
  and and_495 (and_495_out, or_196_out, xor_222_out);
  and and_496 (and_496_out, or_178_out, not_63_out);
  and and_497 (and_497_out, or_196_out, xor_223_out);
  and and_498 (and_498_out, or_179_out, not_64_out);
  and and_499 (and_499_out, or_196_out, xor_224_out);
  and and_500 (and_500_out, or_180_out, not_65_out);
  and and_501 (and_501_out, A7, B0);
  and and_502 (and_502_out, A7, B1);
  and and_503 (and_503_out, A7, B2);
  and and_504 (and_504_out, A7, B3);
  and and_505 (and_505_out, A7, B4);
  and and_506 (and_506_out, A7, B5);
  and and_507 (and_507_out, A7, B6);
  and and_508 (and_508_out, A7, B7);
  or or_197 (or_197_out, and_487_out, and_488_out);
  or or_198 (or_198_out, and_489_out, and_490_out);
  or or_199 (or_199_out, and_491_out, and_492_out);
  or or_200 (or_200_out, and_493_out, and_494_out);
  or or_201 (or_201_out, and_495_out, and_496_out);
  or or_202 (or_202_out, and_497_out, and_498_out);
  or or_203 (or_203_out, and_499_out, and_500_out);
  xor xor_226 (xor_226_out, xor_211_out, and_501_out);
  and and_509 (and_509_out, xor_211_out, and_501_out);
  xor xor_227 (xor_227_out, xor_212_out, and_502_out);
  and and_510 (and_510_out, xor_212_out, and_502_out);
  xor xor_228 (xor_228_out, xor_213_out, and_503_out);
  and and_511 (and_511_out, xor_213_out, and_503_out);
  xor xor_229 (xor_229_out, xor_214_out, and_504_out);
  and and_512 (and_512_out, xor_214_out, and_504_out);
  xor xor_230 (xor_230_out, xor_215_out, and_505_out);
  and and_513 (and_513_out, xor_215_out, and_505_out);
  xor xor_231 (xor_231_out, xor_216_out, and_506_out);
  and and_514 (and_514_out, xor_216_out, and_506_out);
  xor xor_232 (xor_232_out, xor_217_out, and_507_out);
  and and_515 (and_515_out, xor_217_out, and_507_out);
  xor xor_233 (xor_233_out, or_188_out, and_508_out);
  and and_516 (and_516_out, or_188_out, and_508_out);
  xor xor_234 (xor_234_out, not_13_out, A0);
  and and_517 (and_517_out, A0, not_13_out);
  xor xor_235 (xor_235_out, not_14_out, or_197_out);
  and and_518 (and_518_out, or_197_out, not_14_out);
  xor xor_236 (xor_236_out, not_15_out, or_198_out);
  and and_519 (and_519_out, or_198_out, not_15_out);
  xor xor_237 (xor_237_out, not_16_out, or_199_out);
  and and_520 (and_520_out, or_199_out, not_16_out);
  xor xor_238 (xor_238_out, not_9_out, or_200_out);
  and and_521 (and_521_out, or_200_out, not_9_out);
  xor xor_239 (xor_239_out, not_10_out, or_201_out);
  and and_522 (and_522_out, or_201_out, not_10_out);
  xor xor_240 (xor_240_out, not_11_out, or_202_out);
  and and_523 (and_523_out, or_202_out, not_11_out);
  xor xor_241 (xor_241_out, not_12_out, or_203_out);
  and and_524 (and_524_out, or_203_out, not_12_out);
  xor xor_242 (xor_242_out, 1'b1, xor_234_out);
  and and_525 (and_525_out, xor_234_out, 1'b1);
  xor xor_243 (xor_243_out, or_211_out, xor_235_out);
  and and_526 (and_526_out, xor_235_out, or_211_out);
  xor xor_244 (xor_244_out, or_212_out, xor_236_out);
  and and_527 (and_527_out, xor_236_out, or_212_out);
  xor xor_245 (xor_245_out, or_213_out, xor_237_out);
  and and_528 (and_528_out, xor_237_out, or_213_out);
  xor xor_246 (xor_246_out, or_214_out, xor_238_out);
  and and_529 (and_529_out, xor_238_out, or_214_out);
  xor xor_247 (xor_247_out, or_215_out, xor_239_out);
  and and_530 (and_530_out, xor_239_out, or_215_out);
  xor xor_248 (xor_248_out, or_216_out, xor_240_out);
  and and_531 (and_531_out, xor_240_out, or_216_out);
  xor xor_249 (xor_249_out, or_217_out, xor_241_out);
  and and_532 (and_532_out, xor_241_out, or_217_out);
  xor xor_250 (xor_250_out, and_509_out, xor_227_out);
  and and_533 (and_533_out, xor_227_out, and_509_out);
  xor xor_251 (xor_251_out, or_204_out, xor_228_out);
  and and_534 (and_534_out, xor_228_out, or_204_out);
  xor xor_252 (xor_252_out, or_205_out, xor_229_out);
  and and_535 (and_535_out, xor_229_out, or_205_out);
  xor xor_253 (xor_253_out, or_206_out, xor_230_out);
  and and_536 (and_536_out, xor_230_out, or_206_out);
  xor xor_254 (xor_254_out, or_207_out, xor_231_out);
  and and_537 (and_537_out, xor_231_out, or_207_out);
  xor xor_255 (xor_255_out, or_208_out, xor_232_out);
  and and_538 (and_538_out, xor_232_out, or_208_out);
  xor xor_256 (xor_256_out, or_209_out, xor_233_out);
  and and_539 (and_539_out, xor_233_out, or_209_out);
  LED led_9 (.in(xor_250_out));
  or or_204 (or_204_out, and_533_out, and_510_out);
  LED led_10 (.in(xor_251_out));
  or or_205 (or_205_out, and_534_out, and_511_out);
  LED led_11 (.in(xor_252_out));
  or or_206 (or_206_out, and_535_out, and_512_out);
  LED led_12 (.in(xor_253_out));
  or or_207 (or_207_out, and_536_out, and_513_out);
  LED led_13 (.in(xor_254_out));
  or or_208 (or_208_out, and_537_out, and_514_out);
  LED led_14 (.in(xor_255_out));
  or or_209 (or_209_out, and_538_out, and_515_out);
  LED led_15 (.in(xor_256_out));
  // Or or_210 has open pins: In_1=and_539_out, In_2=and_516_out, out=open
  or or_211 (or_211_out, and_517_out, and_525_out);
  or or_212 (or_212_out, and_518_out, and_526_out);
  or or_213 (or_213_out, and_519_out, and_527_out);
  or or_214 (or_214_out, and_520_out, and_528_out);
  or or_215 (or_215_out, and_521_out, and_529_out);
  or or_216 (or_216_out, and_522_out, and_530_out);
  or or_217 (or_217_out, and_523_out, and_531_out);
  or or_218 (or_218_out, and_524_out, and_532_out);
  and and_540 (and_540_out, or_218_out, xor_242_out);
  and and_541 (and_541_out, A0, not_66_out);
  not not_66 (not_66_out, or_218_out);
  and and_542 (and_542_out, or_218_out, xor_243_out);
  and and_543 (and_543_out, or_197_out, not_67_out);
  not not_67 (not_67_out, or_218_out);
  and and_544 (and_544_out, or_218_out, xor_244_out);
  and and_545 (and_545_out, or_198_out, not_68_out);
  not not_68 (not_68_out, or_218_out);
  and and_546 (and_546_out, or_218_out, xor_245_out);
  and and_547 (and_547_out, or_199_out, not_69_out);
  not not_69 (not_69_out, or_218_out);
  and and_548 (and_548_out, or_218_out, xor_246_out);
  and and_549 (and_549_out, or_200_out, not_70_out);
  not not_70 (not_70_out, or_218_out);
  and and_550 (and_550_out, or_218_out, xor_247_out);
  and and_551 (and_551_out, or_201_out, not_71_out);
  not not_71 (not_71_out, or_218_out);
  and and_552 (and_552_out, or_218_out, xor_248_out);
  and and_553 (and_553_out, or_202_out, not_72_out);
  not not_72 (not_72_out, or_218_out);
  and and_554 (and_554_out, or_218_out, xor_249_out);
  and and_555 (and_555_out, or_203_out, not_73_out);
  not not_73 (not_73_out, or_218_out);
  or or_219 (or_219_out, and_540_out, and_541_out);
  or or_220 (or_220_out, and_542_out, and_543_out);
  or or_221 (or_221_out, and_544_out, and_545_out);
  or or_222 (or_222_out, and_546_out, and_547_out);
  or or_223 (or_223_out, and_548_out, and_549_out);
  or or_224 (or_224_out, and_550_out, and_551_out);
  or or_225 (or_225_out, and_552_out, and_553_out);
  or or_226 (or_226_out, and_554_out, and_555_out);

  // Notes on the sheet:
  //   Complemento B
  //   B
  //   A
  //   AvB
  //   !B
  //   A\^B
  //   SumDiff
  //   A⊕B
  //   Co
  //   NOT
  //   OR
  //   AND
  //   XOR
  //   SUMDIFF
  //   NAND
  //   NOR
  //   XNOR
  //   MUL
endmodule
