// Digital circuit Adder1.dig as structural Verilog
module Adder1 (
  input  A1,
  input  A2,
  input  A3,
  input  A4,
  input  A5,
  input  A6,
  input  A7,
  input  A8,
  output S0,
  output S1,
  output S2,
  output S3,
  output S4,
  output S5,
  output S6,
  output S7
);

  wire and_1_out, and_2_out, and_3_out, and_4_out, and_5_out, and_6_out;

  not not_1 (S0, A1);
  xor xor_1 (S1, A1, A2);
  and and_1 (and_1_out, A2, A1);
  xor xor_2 (S2, and_1_out, A3);
  and and_2 (and_2_out, A3, and_1_out);
  xor xor_3 (S3, and_2_out, A4);
  and and_3 (and_3_out, A4, and_2_out);
  xor xor_4 (S4, and_3_out, A5);
  and and_4 (and_4_out, A5, and_3_out);
  xor xor_5 (S5, and_4_out, A6);
  and and_5 (and_5_out, A6, and_4_out);
  xor xor_6 (S6, and_5_out, A7);
  and and_6 (and_6_out, A7, and_5_out);
  xor xor_7 (S7, and_6_out, A8);

  // Notes on the sheet:
  //   SumDiff
endmodule
