// Digital circuit Comparador.dig as structural Verilog
module Comparador (
  input  in_1,
  input  in_2,
  input  in_3,
  input  in_4,
  input  in_5,
  input  in_6,
  input  in_7,
  input  in_8,
  input  in_9,
  input  in_10,
  input  in_11,
  input  in_12,
  input  in_13,
  input  in_14,
  input  in_15,
  input  in_16,
  output eq,
  output lt
);

  wire and_1_out, and_2_out, and_3_out, and_4_out, and_5_out, and_6_out, and_7_out, and_8_out, and_9_out,
       and_10_out, and_11_out, and_12_out, and_13_out, and_14_out, and_15_out, and_16_out, and_17_out,
       and_18_out, and_19_out, and_20_out, and_21_out, and_22_out, and_23_out, and_24_out, and_25_out,
       and_26_out, and_27_out, and_28_out, and_29_out, and_30_out, and_31_out, and_32_out, and_33_out,
       and_34_out, and_35_out, and_36_out, and_37_out, and_38_out, and_39_out, and_40_out, and_41_out,
       and_42_out, not_1_out, not_2_out, not_3_out, not_4_out, not_5_out, not_6_out, not_7_out, not_8_out,
       or_1_out, or_2_out, or_3_out, or_4_out, or_5_out, or_6_out, xnor_1_out, xnor_3_out, xnor_4_out,
       xnor_5_out, xnor_6_out, xnor_7_out, xnor_8_out;

  xnor xnor_1 (xnor_1_out, in_8, in_16);
  not xnor_2 (in_7, in_15);  // XNOr open: In_1
  xnor xnor_3 (xnor_3_out, in_6, in_14);
  xnor xnor_4 (xnor_4_out, in_5, in_13);
  xnor xnor_5 (xnor_5_out, in_4, in_12);
  xnor xnor_6 (xnor_6_out, in_3, in_11);
  xnor xnor_7 (xnor_7_out, in_2, in_10);
  xnor xnor_8 (xnor_8_out, in_1, in_9);
  and and_1 (and_1_out, not_1_out, in_8);
  not not_1 (not_1_out, in_16);
  and and_2 (and_2_out, not_2_out, in_7);
  not not_2 (not_2_out, in_15);
  and and_3 (and_3_out, not_3_out, in_6);
  not not_3 (not_3_out, in_14);
  and and_4 (and_4_out, not_4_out, in_5);
  not not_4 (not_4_out, in_13);
  and and_5 (and_5_out, not_5_out, in_4);
  not not_5 (not_5_out, in_12);
  and and_6 (and_6_out, not_6_out, in_3);
  not not_6 (not_6_out, in_11);
  and and_7 (and_7_out, not_7_out, in_2);
  not not_7 (not_7_out, in_10);
  and and_8 (and_8_out, not_8_out, in_1);
  not not_8 (not_8_out, in_9);
  and and_9 (and_9_out, xnor_1_out, and_2_out);
  and and_10 (and_10_out, xnor_1_out, and_3_out);
  and and_11 (and_11_out, xnor_1_out, and_4_out);
  and and_12 (and_12_out, xnor_1_out, and_5_out);
  and and_13 (and_13_out, xnor_1_out, and_6_out);
  and and_14 (and_14_out, xnor_1_out, and_7_out);
  and and_15 (and_15_out, xnor_1_out, and_8_out);
  and and_16 (and_16_out, in_7, and_10_out);
  and and_17 (and_17_out, in_7, and_11_out);
  and and_18 (and_18_out, in_7, and_12_out);
  and and_19 (and_19_out, in_7, and_13_out);
  and and_20 (and_20_out, in_7, and_14_out);
  and and_21 (and_21_out, in_7, and_15_out);
  and and_22 (and_22_out, xnor_3_out, and_17_out);
  and and_23 (and_23_out, xnor_3_out, and_18_out);
  and and_24 (and_24_out, xnor_3_out, and_19_out);
  and and_25 (and_25_out, xnor_3_out, and_20_out);
  and and_26 (and_26_out, xnor_3_out, and_21_out);
  and and_27 (and_27_out, xnor_4_out, and_23_out);
  and and_28 (and_28_out, xnor_4_out, and_24_out);
  and and_29 (and_29_out, xnor_4_out, and_25_out);
  and and_30 (and_30_out, xnor_4_out, and_26_out);
  and and_31 (and_31_out, xnor_5_out, and_28_out);
  and and_32 (and_32_out, xnor_5_out, and_29_out);
  and and_33 (and_33_out, xnor_5_out, and_30_out);
  and and_34 (and_34_out, xnor_1_out, in_7);
  and and_35 (and_35_out, xnor_6_out, and_32_out);
  and and_36 (and_36_out, xnor_6_out, and_33_out);
  and and_37 (and_37_out, and_34_out, xnor_3_out);
  or or_1 (or_1_out, and_1_out, and_9_out);
  and and_38 (and_38_out, xnor_7_out, and_36_out);
  or or_2 (or_2_out, or_1_out, and_16_out);
  and and_39 (and_39_out, and_37_out, xnor_4_out);
  or or_3 (or_3_out, or_2_out, and_22_out);
  and and_40 (and_40_out, and_39_out, xnor_5_out);
  or or_4 (or_4_out, or_3_out, and_27_out);
  and and_41 (and_41_out, and_40_out, xnor_6_out);
  or or_5 (or_5_out, or_4_out, and_31_out);
  and and_42 (and_42_out, and_41_out, xnor_7_out);
  or or_6 (or_6_out, or_5_out, and_35_out);
  or or_7 (lt, or_6_out, and_38_out);
  and and_43 (eq, and_42_out, xnor_8_out);
endmodule
