// Digital circuit Control Unit Simplified.dig as structural Verilog
module Control_Unit_Simplified (
  input  [2:0] func,
  output RegDst,
  output RegWrite,
  output ALUScr,
  output MemWrite,
  output MemRead,
  output MemToReg,
  output Branch,
  output Jump,
  output [1:0] ALUOp
);

  wire and_1_out, and_4_out, and_5_out, and_8_out, and_9_out, nor_2_out;

  nor nor_1 (RegDst, func[0], func[1], func[2]);
  nor nor_2 (nor_2_out, func[1], func[2]);
  and and_1 (and_1_out, ~func[0], ~func[1], func[2]);  // And
  xor xor_1 (ALUScr, func[0], func[1], func[2]);
  and and_2 (MemWrite, ~func[0], func[1], ~func[2]);  // And
  and and_3 (MemRead, func[0], ~func[1], ~func[2]);  // And
  and and_4 (and_4_out, ~func[0], ~func[1], ~func[2]);  // And
  and and_5 (and_5_out, ~func[0], ~func[1], func[2]);  // And
  and and_6 (Branch, func[0], func[1], ~func[2]);  // And
  and and_7 (Jump, func[0], func[1], func[2]);
  and and_8 (and_8_out, func[0], func[1], ~func[2]);  // And
  and and_9 (and_9_out, ~func[0], ~func[1], func[2]);  // And
  and and_10 (ALUOp[1], ~func[0], ~func[1]);  // And
  or or_1 (MemToReg, and_4_out, and_5_out);
  or or_2 (ALUOp[0], and_8_out, and_9_out);
  or or_3 (RegWrite, nor_2_out, and_1_out);
  // Pins of 1 and 2 bits meet at ALUOp
endmodule
