// Digital circuit Controle ULA 2x3 bits.dig as structural Verilog
module Controle_ULA_2x3_bits (
  input  Funct0,
  input  ALUOp0,
  input  ALUOp1,
  input  Funct1,
  input  Funct2,
  output ULACtrl0,
  output ULACtrl1,
  output ULACtrl2
);

  wire and_1_out, and_2_out, and_3_out, and_4_out, and_5_out, and_6_out, and_7_out, and_8_out, and_9_out,
       and_10_out, and_11_out, and_12_out, not_1_out, not_2_out;

  not not_1 (not_1_out, ALUOp0);
  not not_2 (not_2_out, ALUOp1);
  and and_1 (and_1_out, 1'b0, not_2_out, not_1_out);
  and and_2 (and_2_out, 1'b1, not_2_out, ALUOp0);
  and and_3 (and_3_out, Funct2, ALUOp1, not_1_out);
  and and_4 (and_4_out, 1'b0, ALUOp1, ALUOp0);
  and and_5 (and_5_out, 1'b0, not_2_out, not_1_out);
  and and_6 (and_6_out, 1'b0, not_2_out, ALUOp0);
  and and_7 (and_7_out, Funct1, ALUOp1, not_1_out);
  and and_8 (and_8_out, 1'b0, ALUOp1, ALUOp0);
  and and_9 (and_9_out, 1'b0, not_2_out, not_1_out);
  and and_10 (and_10_out, 1'b1, not_2_out, ALUOp0);
  and and_11 (and_11_out, Funct0, ALUOp1, not_1_out);
  and and_12 (and_12_out, 1'b0, ALUOp1, ALUOp0);
  or or_1 (ULACtrl2, and_1_out, and_2_out, and_3_out, and_4_out);
  or or_2 (ULACtrl1, and_5_out, and_6_out, and_7_out, and_8_out);
  or or_3 (ULACtrl0, and_9_out, and_10_out, and_11_out, and_12_out);
endmodule
