// Digital circuit Demux 3x8bits.dig as structural Verilog
module Demux_3x8bits (
  input  in_1,
  input  in_2,
  input  in_3
);

  wire and_1_out, and_2_out, and_3_out, and_4_out, and_5_out, and_6_out, and_7_out, and_8_out, and_9_out,
       and_10_out, and_11_out, and_12_out, and_13_out, and_14_out, and_15_out, and_16_out, and_17_out,
       and_18_out, and_19_out, and_20_out, and_21_out, and_22_out, and_23_out, and_24_out, and_25_out,
       and_26_out, and_27_out, and_28_out, and_29_out, and_30_out, and_31_out, and_32_out, and_33_out,
       and_34_out, and_35_out, and_36_out, and_37_out, and_38_out, and_39_out, and_40_out, and_41_out,
       and_42_out, and_43_out, and_44_out, and_45_out, and_46_out, and_47_out, and_48_out, and_49_out,
       and_50_out, and_51_out, and_52_out, and_53_out, and_54_out, and_55_out, and_56_out, and_57_out,
       and_58_out, and_59_out, and_60_out, and_61_out, and_62_out, and_63_out, and_64_out, not_1_out,
       not_2_out, not_3_out, or_1_out, or_2_out, or_3_out, or_4_out, or_5_out, or_6_out, or_7_out, or_8_out,
       or_9_out, or_10_out, or_11_out, or_12_out, or_13_out, or_14_out, or_15_out, or_16_out, undriven,
       undriven_2, undriven_3, undriven_4, undriven_5, undriven_6, undriven_7, undriven_8, undriven_9,
       undriven_10, undriven_11, undriven_12, undriven_13, undriven_14, undriven_15, undriven_16,
       undriven_17, undriven_18, undriven_19, undriven_20, undriven_21, undriven_22, undriven_23,
       undriven_24, undriven_25, undriven_26, undriven_27, undriven_28, undriven_29, undriven_30,
       undriven_31, undriven_32, undriven_33, undriven_34, undriven_35, undriven_36, undriven_37,
       undriven_38, undriven_39, undriven_40, undriven_41, undriven_42, undriven_43, undriven_44,
       undriven_45, undriven_46, undriven_47, undriven_48, undriven_49, undriven_50, undriven_51,
       undriven_52, undriven_53, undriven_54, undriven_55, undriven_56, undriven_57, undriven_58,
       undriven_59, undriven_60, undriven_61, undriven_62, undriven_63, undriven_64;

  not not_1 (not_1_out, in_2);
  not not_2 (not_2_out, in_3);
  and and_1 (and_1_out, undriven_64, in_3, in_2, in_1);
  and and_2 (and_2_out, undriven_63, in_3, in_2, in_1);
  and and_3 (and_3_out, undriven_62, in_3, in_2, in_1);
  and and_4 (and_4_out, undriven_61, in_3, in_2, in_1);
  and and_5 (and_5_out, undriven_60, in_3, in_2, in_1);
  and and_6 (and_6_out, undriven_59, in_3, in_2, in_1);
  and and_7 (and_7_out, undriven_58, in_3, in_2, in_1);
  and and_8 (and_8_out, undriven_57, in_3, in_2, in_1);
  and and_9 (and_9_out, undriven_56, in_3, in_2, not_3_out);
  and and_10 (and_10_out, undriven_55, in_3, in_2, not_3_out);
  and and_11 (and_11_out, undriven_54, in_3, in_2, not_3_out);
  and and_12 (and_12_out, undriven_53, in_3, in_2, not_3_out);
  and and_13 (and_13_out, undriven_52, in_3, in_2, not_3_out);
  and and_14 (and_14_out, undriven_51, in_3, in_2, not_3_out);
  and and_15 (and_15_out, undriven_50, in_3, in_2, not_3_out);
  and and_16 (and_16_out, undriven_49, in_3, in_2, not_3_out);
  and and_17 (and_17_out, undriven_48, in_3, not_1_out, in_1);
  and and_18 (and_18_out, undriven_47, in_3, not_1_out, in_1);
  and and_19 (and_19_out, undriven_46, in_3, not_1_out, in_1);
  and and_20 (and_20_out, undriven_45, in_3, not_1_out, in_1);
  and and_21 (and_21_out, undriven_44, in_3, not_1_out, in_1);
  and and_22 (and_22_out, undriven_43, in_3, not_1_out, in_1);
  and and_23 (and_23_out, undriven_42, in_3, not_1_out, in_1);
  and and_24 (and_24_out, undriven_41, in_3, not_1_out, in_1);
  and and_25 (and_25_out, undriven_40, in_3, not_1_out, not_3_out);
  and and_26 (and_26_out, undriven_39, in_3, not_1_out, not_3_out);
  and and_27 (and_27_out, undriven_38, in_3, not_1_out, not_3_out);
  and and_28 (and_28_out, undriven_37, in_3, not_1_out, not_3_out);
  and and_29 (and_29_out, undriven_36, in_3, not_1_out, not_3_out);
  and and_30 (and_30_out, undriven_35, in_3, not_1_out, not_3_out);
  and and_31 (and_31_out, undriven_34, in_3, not_1_out, not_3_out);
  and and_32 (and_32_out, undriven_33, in_3, not_1_out, not_3_out);
  and and_33 (and_33_out, undriven_32, not_2_out, in_2, in_1);
  and and_34 (and_34_out, undriven_31, not_2_out, in_2, in_1);
  and and_35 (and_35_out, undriven_30, not_2_out, in_2, in_1);
  and and_36 (and_36_out, undriven_29, not_2_out, in_2, in_1);
  and and_37 (and_37_out, undriven_28, not_2_out, in_2, in_1);
  and and_38 (and_38_out, undriven_27, not_2_out, in_2, in_1);
  and and_39 (and_39_out, undriven_26, not_2_out, in_2, in_1);
  and and_40 (and_40_out, undriven_25, not_2_out, in_2, in_1);
  and and_41 (and_41_out, undriven_24, not_2_out, in_2, not_3_out);
  and and_42 (and_42_out, undriven_23, not_2_out, in_2, not_3_out);
  and and_43 (and_43_out, undriven_22, not_2_out, in_2, not_3_out);
  and and_44 (and_44_out, undriven_21, not_2_out, in_2, not_3_out);
  and and_45 (and_45_out, undriven_20, not_2_out, in_2, not_3_out);
  and and_46 (and_46_out, undriven_19, not_2_out, in_2, not_3_out);
  and and_47 (and_47_out, undriven_18, not_2_out, in_2, not_3_out);
  and and_48 (and_48_out, undriven_17, not_2_out, in_2, not_3_out);
  and and_49 (and_49_out, undriven_16, not_2_out, not_1_out, in_1);
  and and_50 (and_50_out, undriven_15, not_2_out, not_1_out, in_1);
  and and_51 (and_51_out, undriven_14, not_2_out, not_1_out, in_1);
  and and_52 (and_52_out, undriven_13, not_2_out, not_1_out, in_1);
  and and_53 (and_53_out, undriven_12, not_2_out, not_1_out, in_1);
  and and_54 (and_54_out, undriven_11, not_2_out, not_1_out, in_1);
  and and_55 (and_55_out, undriven_10, not_2_out, not_1_out, in_1);
  and and_56 (and_56_out, undriven_9, not_2_out, not_1_out, in_1);
  and and_57 (and_57_out, undriven, not_2_out, not_1_out, not_3_out);
  and and_58 (and_58_out, undriven_2, not_2_out, not_1_out, not_3_out);
  and and_59 (and_59_out, undriven_3, not_2_out, not_1_out, not_3_out);
  and and_60 (and_60_out, undriven_4, not_2_out, not_1_out, not_3_out);
  and and_61 (and_61_out, undriven_5, not_2_out, not_1_out, not_3_out);
  and and_62 (and_62_out, undriven_6, not_2_out, not_1_out, not_3_out);
  and and_63 (and_63_out, undriven_7, not_2_out, not_1_out, not_3_out);
  and and_64 (and_64_out, undriven_8, not_2_out, not_1_out, not_3_out);
  not not_3 (not_3_out, in_1);
  or or_1 (or_1_out, and_1_out, and_9_out, and_17_out, and_25_out);
  or or_2 (or_2_out, and_33_out, and_41_out, and_49_out, and_57_out);
  or or_3 (or_3_out, and_2_out, and_10_out, and_18_out, and_26_out);
  or or_4 (or_4_out, and_34_out, and_42_out, and_50_out, and_58_out);
  or or_5 (or_5_out, and_3_out, and_11_out, and_19_out, and_27_out);
  or or_6 (or_6_out, and_35_out, and_43_out, and_51_out, and_59_out);
  or or_7 (or_7_out, and_4_out, and_12_out, and_20_out, and_28_out);
  or or_8 (or_8_out, and_36_out, and_44_out, and_52_out, and_60_out);
  or or_9 (or_9_out, and_5_out, and_13_out, and_21_out, and_29_out);
  or or_10 (or_10_out, and_37_out, and_45_out, and_53_out, and_61_out);
  or or_11 (or_11_out, and_6_out, and_14_out, and_22_out, and_30_out);
  or or_12 (or_12_out, and_38_out, and_46_out, and_54_out, and_62_out);
  or or_13 (or_13_out, and_7_out, and_15_out, and_23_out, and_31_out);
  or or_14 (or_14_out, and_39_out, and_47_out, and_55_out, and_63_out);
  or or_15 (or_15_out, and_8_out, and_16_out, and_24_out, and_32_out);
  or or_16 (or_16_out, and_40_out, and_48_out, and_56_out, and_64_out);
  // Or or_17 has open pins: In_1=or_1_out, In_2=or_2_out, out=open
  // Or or_18 has open pins: In_1=or_3_out, In_2=or_4_out, out=open
  // Or or_19 has open pins: In_1=or_5_out, In_2=or_6_out, out=open
  // Or or_20 has open pins: In_1=or_7_out, In_2=or_8_out, out=open
  // Or or_21 has open pins: In_1=or_9_out, In_2=or_10_out, out=open
  // Or or_22 has open pins: In_1=or_11_out, In_2=or_12_out, out=open
  // Or or_23 has open pins: In_1=or_13_out, In_2=or_14_out, out=open
  // Or or_24 has open pins: In_1=or_15_out, In_2=or_16_out, out=open
endmodule
