// Digital circuit Divisor 8x8 bits.dig as structural Verilog
module Divisor_8x8_bits (
  input  in_1,
  input  in_2,
  input  in_3,
  input  in_4,
  input  in_5,
  input  in_6,
  input  in_7,
  input  in_8,
  input  in_9,
  input  in_10,
  input  in_11,
  input  in_12,
  input  in_13,
  input  in_14,
  input  in_15,
  input  in_16,
  output Q7,
  output Q6,
  output Q5,
  output Q4,
  output Q3,
  output Q2,
  output Q1,
  output Q0,
  output R7,
  output R6,
  output R5,
  output R4,
  output R3,
  output R2,
  output R1,
  output R0
);

  wire and_1_out, and_2_out, and_3_out, and_4_out, and_5_out, and_6_out, and_7_out, and_8_out, and_9_out,
       and_10_out, and_11_out, and_12_out, and_13_out, and_14_out, and_15_out, and_16_out, and_17_out,
       and_18_out, and_19_out, and_20_out, and_21_out, and_22_out, and_23_out, and_24_out, and_25_out,
       and_26_out, and_27_out, and_28_out, and_29_out, and_30_out, and_31_out, and_32_out, and_33_out,
       and_34_out, and_35_out, and_36_out, and_37_out, and_38_out, and_39_out, and_40_out, and_41_out,
       and_42_out, and_43_out, and_44_out, and_45_out, and_46_out, and_47_out, and_48_out, and_49_out,
       and_50_out, and_51_out, and_52_out, and_53_out, and_54_out, and_55_out, and_56_out, and_57_out,
       and_58_out, and_59_out, and_60_out, and_61_out, and_62_out, and_63_out, and_64_out, and_65_out,
       and_66_out, and_67_out, and_68_out, and_69_out, and_70_out, and_71_out, and_72_out, and_73_out,
       and_74_out, and_75_out, and_76_out, and_77_out, and_78_out, and_79_out, and_80_out, and_81_out,
       and_82_out, and_83_out, and_84_out, and_85_out, and_86_out, and_87_out, and_88_out, and_89_out,
       and_90_out, and_91_out, and_92_out, and_93_out, and_94_out, and_95_out, and_96_out, and_97_out,
       and_98_out, and_99_out, and_100_out, and_101_out, and_102_out, and_103_out, and_104_out, and_105_out,
       and_106_out, and_107_out, and_108_out, and_109_out, and_110_out, and_111_out, and_112_out,
       and_113_out, and_114_out, and_115_out, and_116_out, and_117_out, and_118_out, and_119_out,
       and_120_out, and_121_out, and_122_out, and_123_out, and_124_out, and_125_out, and_126_out,
       and_127_out, and_128_out, and_129_out, and_130_out, and_131_out, and_132_out, and_133_out,
       and_134_out, and_135_out, and_136_out, and_137_out, and_138_out, and_139_out, and_140_out,
       and_141_out, and_142_out, and_143_out, and_144_out, and_145_out, and_146_out, and_147_out,
       and_148_out, and_149_out, and_150_out, and_151_out, and_152_out, and_153_out, and_154_out,
       and_155_out, and_156_out, and_157_out, and_158_out, and_159_out, and_160_out, and_161_out,
       and_162_out, and_163_out, and_164_out, and_165_out, and_166_out, and_167_out, and_168_out,
       and_169_out, and_170_out, and_171_out, and_172_out, and_173_out, and_174_out, and_175_out,
       and_176_out, and_177_out, and_178_out, and_179_out, and_180_out, and_181_out, and_182_out,
       and_183_out, and_184_out, and_185_out, and_186_out, and_187_out, and_188_out, and_189_out,
       and_190_out, and_191_out, and_192_out, and_193_out, and_194_out, and_195_out, and_196_out,
       and_197_out, and_198_out, and_199_out, and_200_out, and_201_out, and_202_out, and_203_out,
       and_204_out, and_205_out, and_206_out, and_207_out, and_208_out, and_209_out, and_210_out,
       and_211_out, and_212_out, and_213_out, and_214_out, and_215_out, and_216_out, and_217_out,
       and_218_out, and_219_out, and_220_out, and_221_out, and_222_out, and_223_out, and_224_out,
       and_225_out, and_226_out, and_227_out, and_228_out, and_229_out, and_230_out, and_231_out,
       and_232_out, and_233_out, and_234_out, and_235_out, and_236_out, and_237_out, and_238_out,
       and_239_out, and_240_out, and_241_out, and_242_out, not_1_out, not_2_out, not_3_out, not_4_out,
       not_5_out, not_6_out, not_7_out, not_8_out, not_9_out, not_10_out, not_11_out, not_12_out, not_13_out,
       not_14_out, not_15_out, not_16_out, not_17_out, not_18_out, not_19_out, not_20_out, not_21_out,
       not_22_out, not_23_out, not_24_out, not_25_out, not_26_out, not_27_out, not_28_out, not_29_out,
       not_30_out, not_31_out, not_32_out, not_33_out, not_34_out, not_35_out, not_36_out, not_37_out,
       not_38_out, not_39_out, not_40_out, not_41_out, not_42_out, not_43_out, not_44_out, not_45_out,
       not_46_out, not_47_out, not_48_out, not_49_out, not_50_out, not_51_out, not_52_out, not_53_out,
       not_54_out, not_55_out, not_56_out, not_57_out, not_58_out, not_59_out, not_60_out, not_61_out,
       not_62_out, not_63_out, not_64_out, not_65_out, or_2_out, or_4_out, or_5_out, or_6_out, or_7_out,
       or_9_out, or_10_out, or_11_out, or_12_out, or_13_out, or_14_out, or_15_out, or_17_out, or_18_out,
       or_19_out, or_20_out, or_21_out, or_22_out, or_23_out, or_24_out, or_25_out, or_26_out, or_28_out,
       or_29_out, or_30_out, or_31_out, or_32_out, or_33_out, or_34_out, or_35_out, or_37_out, or_38_out,
       or_39_out, or_40_out, or_41_out, or_42_out, or_43_out, or_44_out, or_45_out, or_46_out, or_47_out,
       or_48_out, or_49_out, or_50_out, or_51_out, or_53_out, or_54_out, or_55_out, or_56_out, or_57_out,
       or_58_out, or_59_out, or_60_out, or_61_out, or_62_out, or_63_out, or_64_out, or_65_out, or_66_out,
       or_67_out, or_69_out, or_70_out, or_71_out, or_72_out, or_74_out, or_75_out, or_76_out, or_77_out,
       or_78_out, or_79_out, or_80_out, or_81_out, or_82_out, or_83_out, or_84_out, or_86_out, or_87_out,
       or_88_out, or_89_out, or_90_out, or_91_out, or_92_out, or_94_out, or_95_out, or_96_out, or_97_out,
       or_98_out, or_99_out, or_100_out, or_101_out, or_102_out, or_103_out, or_104_out, or_106_out,
       or_107_out, or_108_out, or_109_out, or_111_out, or_112_out, or_113_out, or_114_out, or_116_out,
       or_117_out, or_118_out, or_120_out, xor_1_out, xor_3_out, xor_4_out, xor_5_out, xor_7_out, xor_8_out,
       xor_9_out, xor_10_out, xor_11_out, xor_13_out, xor_14_out, xor_15_out, xor_16_out, xor_17_out,
       xor_18_out, xor_19_out, xor_20_out, xor_22_out, xor_23_out, xor_24_out, xor_25_out, xor_26_out,
       xor_27_out, xor_28_out, xor_29_out, xor_30_out, xor_31_out, xor_32_out, xor_33_out, xor_35_out,
       xor_36_out, xor_37_out, xor_38_out, xor_39_out, xor_40_out, xor_41_out, xor_42_out, xor_43_out,
       xor_44_out, xor_46_out, xor_47_out, xor_48_out, xor_49_out, xor_50_out, xor_51_out, xor_52_out,
       xor_53_out, xor_54_out, xor_55_out, xor_56_out, xor_57_out, xor_58_out, xor_59_out, xor_60_out,
       xor_61_out, xor_63_out, xor_64_out, xor_65_out, xor_66_out, xor_67_out, xor_68_out, xor_69_out,
       xor_70_out, xor_71_out, xor_72_out, xor_73_out, xor_74_out, xor_75_out, xor_76_out, xor_77_out,
       xor_78_out, xor_79_out, xor_80_out, xor_81_out, xor_82_out, xor_83_out, xor_84_out, xor_85_out,
       xor_86_out, xor_87_out, xor_88_out, xor_89_out, xor_90_out, xor_91_out, xor_92_out, xor_93_out,
       xor_94_out, xor_95_out, xor_96_out, xor_97_out, xor_98_out, xor_99_out, xor_100_out, xor_101_out,
       xor_102_out, xor_103_out, xor_104_out, xor_105_out, xor_106_out, xor_107_out, xor_108_out,
       xor_109_out, xor_110_out, xor_111_out, xor_112_out, xor_113_out, xor_114_out, xor_115_out,
       xor_116_out, xor_117_out, xor_118_out, xor_119_out, xor_120_out, xor_121_out, xor_122_out,
       xor_123_out, xor_124_out, xor_125_out, xor_126_out, xor_127_out, xor_128_out;

  LED led_1 (.in(Q7));
  LED led_2 (.in(Q6));
  LED led_3 (.in(Q5));
  LED led_4 (.in(Q4));
  LED led_5 (.in(Q3));
  LED led_6 (.in(Q2));
  LED led_7 (.in(Q1));
  LED led_8 (.in(Q0));
  LED led_9 (.in(R7));
  LED led_10 (.in(R6));
  LED led_11 (.in(R5));
  LED led_12 (.in(R4));
  LED led_13 (.in(R3));
  LED led_14 (.in(R2));
  LED led_15 (.in(R1));
  LED led_16 (.in(R0));
  and and_1 (and_1_out, 1'b0, not_5_out);
  xor xor_1 (xor_1_out, not_5_out, 1'b0);
  and and_2 (and_2_out, xor_1_out, or_2_out);
  or or_1 (Q7, and_1_out, and_2_out);
  and and_3 (and_3_out, 1'b0, not_4_out);
  // XOr xor_2 has open pins: In_1=or_2_out, In_2=xor_1_out, out=open
  and and_4 (and_4_out, xor_3_out, or_5_out);
  or or_2 (or_2_out, and_3_out, and_4_out);
  not not_1 (not_1_out, Q7);
  and and_5 (and_5_out, 1'b0, not_1_out);
  and and_6 (and_6_out, or_4_out, not_5_out);
  and and_7 (and_7_out, xor_5_out, or_7_out);
  or or_3 (Q6, and_6_out, and_7_out);
  xor xor_3 (xor_3_out, not_4_out, 1'b0);
  xor xor_4 (xor_4_out, or_5_out, xor_3_out);
  and and_8 (and_8_out, Q7, xor_4_out);
  or or_4 (or_4_out, and_8_out, and_5_out);
  xor xor_5 (xor_5_out, not_5_out, or_4_out);
  // XOr xor_6 has open pins: In_1=or_7_out, In_2=xor_5_out, out=open
  and and_9 (and_9_out, 1'b0, not_8_out);
  and and_10 (and_10_out, xor_7_out, or_9_out);
  or or_5 (or_5_out, and_9_out, and_10_out);
  not not_2 (not_2_out, Q7);
  and and_11 (and_11_out, 1'b0, not_2_out);
  and and_12 (and_12_out, or_6_out, not_4_out);
  not not_3 (not_3_out, Q6);
  xor xor_7 (xor_7_out, not_8_out, 1'b0);
  xor xor_8 (xor_8_out, or_9_out, xor_7_out);
  and and_13 (and_13_out, Q7, xor_8_out);
  or or_6 (or_6_out, and_13_out, and_11_out);
  xor xor_9 (xor_9_out, not_4_out, or_6_out);
  and and_14 (and_14_out, xor_9_out, or_12_out);
  or or_7 (or_7_out, and_12_out, and_14_out);
  and and_15 (and_15_out, or_6_out, not_3_out);
  and and_16 (and_16_out, or_10_out, not_5_out);
  and and_17 (and_17_out, xor_11_out, or_13_out);
  or or_8 (Q5, and_16_out, and_17_out);
  not not_4 (not_4_out, in_2);
  not not_5 (not_5_out, in_1);
  and and_18 (and_18_out, 1'b0, not_7_out);
  and and_19 (and_19_out, xor_13_out, or_17_out);
  or or_9 (or_9_out, and_18_out, and_19_out);
  not not_6 (not_6_out, Q7);
  and and_20 (and_20_out, or_11_out, not_8_out);
  xor xor_10 (xor_10_out, or_12_out, xor_9_out);
  and and_21 (and_21_out, Q6, xor_10_out);
  or or_10 (or_10_out, and_21_out, and_15_out);
  xor xor_11 (xor_11_out, not_5_out, or_10_out);
  // XOr xor_12 has open pins: In_1=or_13_out, In_2=xor_11_out, out=open
  not not_7 (not_7_out, in_4);
  not not_8 (not_8_out, in_3);
  xor xor_13 (xor_13_out, not_7_out, 1'b0);
  xor xor_14 (xor_14_out, or_17_out, xor_13_out);
  and and_22 (and_22_out, 1'b0, not_6_out);
  or or_11 (or_11_out, and_29_out, and_22_out);
  and and_23 (and_23_out, xor_15_out, or_18_out);
  or or_12 (or_12_out, and_20_out, and_23_out);
  not not_9 (not_9_out, Q6);
  and and_24 (and_24_out, or_11_out, not_9_out);
  and and_25 (and_25_out, or_14_out, not_4_out);
  and and_26 (and_26_out, xor_17_out, or_21_out);
  or or_13 (or_13_out, and_25_out, and_26_out);
  not not_10 (not_10_out, Q5);
  and and_27 (and_27_out, or_15_out, not_5_out);
  not not_11 (not_11_out, in_6);
  not not_12 (not_12_out, in_5);
  and and_28 (and_28_out, 1'b0, not_12_out);
  not not_13 (not_13_out, Q7);
  and and_29 (and_29_out, Q7, xor_14_out);
  xor xor_15 (xor_15_out, not_8_out, or_11_out);
  xor xor_16 (xor_16_out, or_18_out, xor_15_out);
  and and_30 (and_30_out, Q6, xor_16_out);
  or or_14 (or_14_out, and_30_out, and_24_out);
  xor xor_17 (xor_17_out, not_4_out, or_14_out);
  xor xor_18 (xor_18_out, or_21_out, xor_17_out);
  and and_31 (and_31_out, or_14_out, not_10_out);
  or or_15 (or_15_out, and_39_out, and_31_out);
  and and_32 (and_32_out, xor_20_out, or_22_out);
  or or_16 (Q4, and_27_out, and_32_out);
  not not_14 (not_14_out, in_8);
  not not_15 (not_15_out, in_7);
  xor xor_19 (xor_19_out, not_12_out, 1'b0);
  and and_33 (and_33_out, xor_19_out, or_23_out);
  or or_17 (or_17_out, and_28_out, and_33_out);
  and and_34 (and_34_out, 1'b0, not_13_out);
  and and_35 (and_35_out, or_19_out, not_7_out);
  and and_36 (and_36_out, xor_23_out, or_24_out);
  or or_18 (or_18_out, and_35_out, and_36_out);
  not not_16 (not_16_out, Q6);
  and and_37 (and_37_out, or_19_out, not_16_out);
  and and_38 (and_38_out, or_20_out, not_8_out);
  not not_17 (not_17_out, Q5);
  and and_39 (and_39_out, Q5, xor_18_out);
  xor xor_20 (xor_20_out, not_5_out, or_15_out);
  // XOr xor_21 has open pins: In_1=or_22_out, In_2=xor_20_out, out=open
  and and_40 (and_40_out, 1'b0, not_11_out);
  xor xor_22 (xor_22_out, or_23_out, xor_19_out);
  and and_41 (and_41_out, Q7, xor_22_out);
  or or_19 (or_19_out, and_41_out, and_34_out);
  xor xor_23 (xor_23_out, not_7_out, or_19_out);
  xor xor_24 (xor_24_out, or_24_out, xor_23_out);
  and and_42 (and_42_out, Q6, xor_24_out);
  or or_20 (or_20_out, and_42_out, and_37_out);
  xor xor_25 (xor_25_out, not_8_out, or_20_out);
  and and_43 (and_43_out, xor_25_out, or_30_out);
  or or_21 (or_21_out, and_38_out, and_43_out);
  and and_44 (and_44_out, or_20_out, not_17_out);
  and and_45 (and_45_out, or_25_out, not_4_out);
  and and_46 (and_46_out, xor_27_out, or_31_out);
  or or_22 (or_22_out, and_45_out, and_46_out);
  not not_18 (not_18_out, Q4);
  and and_47 (and_47_out, or_25_out, not_18_out);
  and and_48 (and_48_out, or_26_out, not_5_out);
  and and_49 (and_49_out, xor_30_out, or_32_out);
  or or_23 (or_23_out, and_40_out, and_49_out);
  not not_19 (not_19_out, Q7);
  and and_50 (and_50_out, 1'b0, not_19_out);
  and and_51 (and_51_out, or_28_out, not_12_out);
  and and_52 (and_52_out, xor_32_out, or_38_out);
  or or_24 (or_24_out, and_51_out, and_52_out);
  not not_20 (not_20_out, Q6);
  and and_53 (and_53_out, or_29_out, not_7_out);
  xor xor_26 (xor_26_out, or_30_out, xor_25_out);
  and and_54 (and_54_out, Q5, xor_26_out);
  or or_25 (or_25_out, and_54_out, and_44_out);
  xor xor_27 (xor_27_out, not_4_out, or_25_out);
  xor xor_28 (xor_28_out, or_31_out, xor_27_out);
  and and_55 (and_55_out, Q4, xor_28_out);
  or or_26 (or_26_out, and_55_out, and_47_out);
  xor xor_29 (xor_29_out, not_5_out, or_26_out);
  and and_56 (and_56_out, xor_29_out, or_35_out);
  or or_27 (Q3, and_48_out, and_56_out);
  xor xor_30 (xor_30_out, not_11_out, 1'b0);
  xor xor_31 (xor_31_out, or_32_out, xor_30_out);
  and and_57 (and_57_out, Q7, xor_31_out);
  or or_28 (or_28_out, and_57_out, and_50_out);
  xor xor_32 (xor_32_out, not_12_out, or_28_out);
  xor xor_33 (xor_33_out, or_38_out, xor_32_out);
  and and_58 (and_58_out, or_28_out, not_20_out);
  or or_29 (or_29_out, and_68_out, and_58_out);
  and and_59 (and_59_out, xor_35_out, or_39_out);
  or or_30 (or_30_out, and_53_out, and_59_out);
  not not_21 (not_21_out, Q5);
  and and_60 (and_60_out, or_29_out, not_21_out);
  and and_61 (and_61_out, or_33_out, not_8_out);
  and and_62 (and_62_out, xor_37_out, or_44_out);
  or or_31 (or_31_out, and_61_out, and_62_out);
  not not_22 (not_22_out, Q4);
  and and_63 (and_63_out, or_34_out, not_4_out);
  // XOr xor_34 has open pins: In_1=or_35_out, In_2=xor_29_out, out=open
  and and_64 (and_64_out, 1'b0, not_15_out);
  and and_65 (and_65_out, xor_39_out, or_41_out);
  or or_32 (or_32_out, and_64_out, and_65_out);
  not not_23 (not_23_out, Q7);
  and and_66 (and_66_out, 1'b0, not_23_out);
  and and_67 (and_67_out, or_37_out, not_11_out);
  not not_24 (not_24_out, Q6);
  and and_68 (and_68_out, Q6, xor_33_out);
  xor xor_35 (xor_35_out, not_7_out, or_29_out);
  xor xor_36 (xor_36_out, or_39_out, xor_35_out);
  and and_69 (and_69_out, Q5, xor_36_out);
  or or_33 (or_33_out, and_69_out, and_60_out);
  xor xor_37 (xor_37_out, not_8_out, or_33_out);
  xor xor_38 (xor_38_out, or_44_out, xor_37_out);
  and and_70 (and_70_out, or_33_out, not_22_out);
  or or_34 (or_34_out, and_82_out, and_70_out);
  and and_71 (and_71_out, xor_42_out, or_45_out);
  or or_35 (or_35_out, and_63_out, and_71_out);
  not not_25 (not_25_out, Q3);
  and and_72 (and_72_out, or_34_out, not_25_out);
  and and_73 (and_73_out, or_40_out, not_5_out);
  and and_74 (and_74_out, xor_44_out, or_51_out);
  or or_36 (Q2, and_73_out, and_74_out);
  xor xor_39 (xor_39_out, not_15_out, 1'b0);
  xor xor_40 (xor_40_out, or_41_out, xor_39_out);
  and and_75 (and_75_out, Q7, xor_40_out);
  or or_37 (or_37_out, and_75_out, and_66_out);
  xor xor_41 (xor_41_out, not_11_out, or_37_out);
  and and_76 (and_76_out, xor_41_out, or_47_out);
  or or_38 (or_38_out, and_67_out, and_76_out);
  and and_77 (and_77_out, or_37_out, not_24_out);
  and and_78 (and_78_out, or_42_out, not_12_out);
  and and_79 (and_79_out, xor_47_out, or_48_out);
  or or_39 (or_39_out, and_78_out, and_79_out);
  not not_26 (not_26_out, Q5);
  and and_80 (and_80_out, or_42_out, not_26_out);
  and and_81 (and_81_out, or_43_out, not_7_out);
  not not_27 (not_27_out, Q4);
  and and_82 (and_82_out, Q4, xor_38_out);
  xor xor_42 (xor_42_out, not_4_out, or_34_out);
  xor xor_43 (xor_43_out, or_45_out, xor_42_out);
  and and_83 (and_83_out, Q3, xor_43_out);
  or or_40 (or_40_out, and_83_out, and_72_out);
  xor xor_44 (xor_44_out, not_5_out, or_40_out);
  // XOr xor_45 has open pins: In_1=or_51_out, In_2=xor_44_out, out=open
  and and_84 (and_84_out, in_9, not_14_out);
  and and_85 (and_85_out, xor_50_out, 1'b1);
  or or_41 (or_41_out, and_84_out, and_85_out);
  not not_28 (not_28_out, Q7);
  and and_86 (and_86_out, or_46_out, not_15_out);
  xor xor_46 (xor_46_out, or_47_out, xor_41_out);
  and and_87 (and_87_out, Q6, xor_46_out);
  or or_42 (or_42_out, and_87_out, and_77_out);
  xor xor_47 (xor_47_out, not_12_out, or_42_out);
  xor xor_48 (xor_48_out, or_48_out, xor_47_out);
  and and_88 (and_88_out, Q5, xor_48_out);
  or or_43 (or_43_out, and_88_out, and_80_out);
  xor xor_49 (xor_49_out, not_7_out, or_43_out);
  and and_89 (and_89_out, xor_49_out, or_55_out);
  or or_44 (or_44_out, and_81_out, and_89_out);
  and and_90 (and_90_out, or_43_out, not_27_out);
  and and_91 (and_91_out, or_49_out, not_8_out);
  and and_92 (and_92_out, xor_53_out, or_56_out);
  or or_45 (or_45_out, and_91_out, and_92_out);
  not not_29 (not_29_out, Q3);
  and and_93 (and_93_out, or_49_out, not_29_out);
  and and_94 (and_94_out, or_50_out, not_4_out);
  not not_30 (not_30_out, Q2);
  xor xor_50 (xor_50_out, not_14_out, in_9);
  xor xor_51 (xor_51_out, 1'b1, xor_50_out);
  and and_95 (and_95_out, in_9, not_28_out);
  or or_46 (or_46_out, and_107_out, and_95_out);
  and and_96 (and_96_out, xor_56_out, or_58_out);
  or or_47 (or_47_out, and_86_out, and_96_out);
  not not_31 (not_31_out, Q6);
  and and_97 (and_97_out, or_46_out, not_31_out);
  and and_98 (and_98_out, or_53_out, not_11_out);
  and and_99 (and_99_out, xor_58_out, or_64_out);
  or or_48 (or_48_out, and_98_out, and_99_out);
  not not_32 (not_32_out, Q5);
  and and_100 (and_100_out, or_54_out, not_12_out);
  xor xor_52 (xor_52_out, or_55_out, xor_49_out);
  and and_101 (and_101_out, Q4, xor_52_out);
  or or_49 (or_49_out, and_101_out, and_90_out);
  xor xor_53 (xor_53_out, not_8_out, or_49_out);
  xor xor_54 (xor_54_out, or_56_out, xor_53_out);
  and and_102 (and_102_out, Q3, xor_54_out);
  or or_50 (or_50_out, and_102_out, and_93_out);
  xor xor_55 (xor_55_out, not_4_out, or_50_out);
  and and_103 (and_103_out, xor_55_out, or_61_out);
  or or_51 (or_51_out, and_94_out, and_103_out);
  and and_104 (and_104_out, or_50_out, not_30_out);
  and and_105 (and_105_out, or_57_out, not_5_out);
  and and_106 (and_106_out, xor_61_out, or_62_out);
  or or_52 (Q1, and_105_out, and_106_out);
  and and_107 (and_107_out, Q7, xor_51_out);
  xor xor_56 (xor_56_out, not_15_out, or_46_out);
  xor xor_57 (xor_57_out, or_58_out, xor_56_out);
  and and_108 (and_108_out, Q6, xor_57_out);
  or or_53 (or_53_out, and_108_out, and_97_out);
  xor xor_58 (xor_58_out, not_11_out, or_53_out);
  xor xor_59 (xor_59_out, or_64_out, xor_58_out);
  and and_109 (and_109_out, or_53_out, not_32_out);
  or or_54 (or_54_out, and_120_out, and_109_out);
  and and_110 (and_110_out, xor_63_out, or_65_out);
  or or_55 (or_55_out, and_100_out, and_110_out);
  not not_33 (not_33_out, Q4);
  and and_111 (and_111_out, or_54_out, not_33_out);
  and and_112 (and_112_out, or_59_out, not_7_out);
  and and_113 (and_113_out, xor_65_out, or_71_out);
  or or_56 (or_56_out, and_112_out, and_113_out);
  not not_34 (not_34_out, Q3);
  and and_114 (and_114_out, or_60_out, not_8_out);
  xor xor_60 (xor_60_out, or_61_out, xor_55_out);
  and and_115 (and_115_out, Q2, xor_60_out);
  or or_57 (or_57_out, and_115_out, and_104_out);
  xor xor_61 (xor_61_out, not_5_out, or_57_out);
  // XOr xor_62 has open pins: In_1=or_62_out, In_2=xor_61_out, out=open
  and and_116 (and_116_out, in_10, not_14_out);
  and and_117 (and_117_out, xor_67_out, 1'b1);
  or or_58 (or_58_out, and_116_out, and_117_out);
  not not_35 (not_35_out, Q6);
  and and_118 (and_118_out, in_10, not_35_out);
  and and_119 (and_119_out, or_63_out, not_15_out);
  not not_36 (not_36_out, Q5);
  and and_120 (and_120_out, Q5, xor_59_out);
  xor xor_63 (xor_63_out, not_12_out, or_54_out);
  xor xor_64 (xor_64_out, or_65_out, xor_63_out);
  and and_121 (and_121_out, Q4, xor_64_out);
  or or_59 (or_59_out, and_121_out, and_111_out);
  xor xor_65 (xor_65_out, not_7_out, or_59_out);
  xor xor_66 (xor_66_out, or_71_out, xor_65_out);
  and and_122 (and_122_out, or_59_out, not_34_out);
  or or_60 (or_60_out, and_135_out, and_122_out);
  and and_123 (and_123_out, xor_70_out, or_72_out);
  or or_61 (or_61_out, and_114_out, and_123_out);
  not not_37 (not_37_out, Q2);
  and and_124 (and_124_out, or_60_out, not_37_out);
  and and_125 (and_125_out, or_66_out, not_4_out);
  and and_126 (and_126_out, xor_72_out, or_78_out);
  or or_62 (or_62_out, and_125_out, and_126_out);
  not not_38 (not_38_out, Q1);
  and and_127 (and_127_out, or_67_out, not_5_out);
  xor xor_67 (xor_67_out, not_14_out, in_10);
  xor xor_68 (xor_68_out, 1'b1, xor_67_out);
  and and_128 (and_128_out, Q6, xor_68_out);
  or or_63 (or_63_out, and_128_out, and_118_out);
  xor xor_69 (xor_69_out, not_15_out, or_63_out);
  and and_129 (and_129_out, xor_69_out, or_74_out);
  or or_64 (or_64_out, and_119_out, and_129_out);
  and and_130 (and_130_out, or_63_out, not_36_out);
  and and_131 (and_131_out, or_69_out, not_11_out);
  and and_132 (and_132_out, xor_75_out, or_75_out);
  or or_65 (or_65_out, and_131_out, and_132_out);
  not not_39 (not_39_out, Q4);
  and and_133 (and_133_out, or_69_out, not_39_out);
  and and_134 (and_134_out, or_70_out, not_12_out);
  not not_40 (not_40_out, Q3);
  and and_135 (and_135_out, Q3, xor_66_out);
  xor xor_70 (xor_70_out, not_8_out, or_60_out);
  xor xor_71 (xor_71_out, or_72_out, xor_70_out);
  and and_136 (and_136_out, Q2, xor_71_out);
  or or_66 (or_66_out, and_136_out, and_124_out);
  xor xor_72 (xor_72_out, not_4_out, or_66_out);
  xor xor_73 (xor_73_out, or_78_out, xor_72_out);
  and and_137 (and_137_out, or_66_out, not_38_out);
  or or_67 (or_67_out, and_149_out, and_137_out);
  and and_138 (and_138_out, xor_78_out, or_79_out);
  or or_68 (Q0, and_127_out, and_138_out);
  not not_41 (not_41_out, Q0);
  and and_139 (and_139_out, or_67_out, not_41_out);
  and and_140 (and_140_out, in_11, not_14_out);
  xor xor_74 (xor_74_out, or_74_out, xor_69_out);
  and and_141 (and_141_out, Q5, xor_74_out);
  or or_69 (or_69_out, and_141_out, and_130_out);
  xor xor_75 (xor_75_out, not_11_out, or_69_out);
  xor xor_76 (xor_76_out, or_75_out, xor_75_out);
  and and_142 (and_142_out, Q4, xor_76_out);
  or or_70 (or_70_out, and_142_out, and_133_out);
  xor xor_77 (xor_77_out, not_12_out, or_70_out);
  and and_143 (and_143_out, xor_77_out, or_82_out);
  or or_71 (or_71_out, and_134_out, and_143_out);
  and and_144 (and_144_out, or_70_out, not_40_out);
  and and_145 (and_145_out, or_76_out, not_7_out);
  and and_146 (and_146_out, xor_81_out, or_83_out);
  or or_72 (or_72_out, and_145_out, and_146_out);
  not not_42 (not_42_out, Q2);
  and and_147 (and_147_out, or_76_out, not_42_out);
  and and_148 (and_148_out, or_77_out, not_8_out);
  not not_43 (not_43_out, Q1);
  and and_149 (and_149_out, Q1, xor_73_out);
  xor xor_78 (xor_78_out, not_5_out, or_67_out);
  xor xor_79 (xor_79_out, or_79_out, xor_78_out);
  and and_150 (and_150_out, Q0, xor_79_out);
  or or_73 (R7, and_150_out, and_139_out);
  and and_151 (and_151_out, xor_84_out, 1'b1);
  or or_74 (or_74_out, and_140_out, and_151_out);
  not not_44 (not_44_out, Q5);
  and and_152 (and_152_out, in_11, not_44_out);
  and and_153 (and_153_out, or_80_out, not_15_out);
  and and_154 (and_154_out, xor_86_out, or_90_out);
  or or_75 (or_75_out, and_153_out, and_154_out);
  not not_45 (not_45_out, Q4);
  and and_155 (and_155_out, or_81_out, not_11_out);
  xor xor_80 (xor_80_out, or_82_out, xor_77_out);
  and and_156 (and_156_out, Q3, xor_80_out);
  or or_76 (or_76_out, and_156_out, and_144_out);
  xor xor_81 (xor_81_out, not_7_out, or_76_out);
  xor xor_82 (xor_82_out, or_83_out, xor_81_out);
  and and_157 (and_157_out, Q2, xor_82_out);
  or or_77 (or_77_out, and_157_out, and_147_out);
  xor xor_83 (xor_83_out, not_8_out, or_77_out);
  and and_158 (and_158_out, xor_83_out, or_88_out);
  or or_78 (or_78_out, and_148_out, and_158_out);
  and and_159 (and_159_out, or_77_out, not_43_out);
  and and_160 (and_160_out, or_84_out, not_4_out);
  and and_161 (and_161_out, xor_89_out, or_89_out);
  or or_79 (or_79_out, and_160_out, and_161_out);
  not not_46 (not_46_out, Q0);
  and and_162 (and_162_out, or_84_out, not_46_out);
  xor xor_84 (xor_84_out, not_14_out, in_11);
  xor xor_85 (xor_85_out, 1'b1, xor_84_out);
  and and_163 (and_163_out, Q5, xor_85_out);
  or or_80 (or_80_out, and_163_out, and_152_out);
  xor xor_86 (xor_86_out, not_15_out, or_80_out);
  xor xor_87 (xor_87_out, or_90_out, xor_86_out);
  and and_164 (and_164_out, or_80_out, not_45_out);
  or or_81 (or_81_out, and_173_out, and_164_out);
  and and_165 (and_165_out, xor_91_out, or_91_out);
  or or_82 (or_82_out, and_155_out, and_165_out);
  not not_47 (not_47_out, Q3);
  and and_166 (and_166_out, or_81_out, not_47_out);
  and and_167 (and_167_out, or_86_out, not_12_out);
  and and_168 (and_168_out, xor_93_out, or_96_out);
  or or_83 (or_83_out, and_167_out, and_168_out);
  not not_48 (not_48_out, Q2);
  and and_169 (and_169_out, or_87_out, not_7_out);
  xor xor_88 (xor_88_out, or_88_out, xor_83_out);
  and and_170 (and_170_out, Q1, xor_88_out);
  or or_84 (or_84_out, and_170_out, and_159_out);
  xor xor_89 (xor_89_out, not_4_out, or_84_out);
  xor xor_90 (xor_90_out, or_89_out, xor_89_out);
  and and_171 (and_171_out, Q0, xor_90_out);
  or or_85 (R6, and_171_out, and_162_out);
  and and_172 (and_172_out, in_12, not_14_out);
  not not_49 (not_49_out, Q4);
  and and_173 (and_173_out, Q4, xor_87_out);
  xor xor_91 (xor_91_out, not_11_out, or_81_out);
  xor xor_92 (xor_92_out, or_91_out, xor_91_out);
  and and_174 (and_174_out, Q3, xor_92_out);
  or or_86 (or_86_out, and_174_out, and_166_out);
  xor xor_93 (xor_93_out, not_12_out, or_86_out);
  xor xor_94 (xor_94_out, or_96_out, xor_93_out);
  and and_175 (and_175_out, or_86_out, not_48_out);
  or or_87 (or_87_out, and_186_out, and_175_out);
  and and_176 (and_176_out, xor_96_out, or_97_out);
  or or_88 (or_88_out, and_169_out, and_176_out);
  not not_50 (not_50_out, Q1);
  and and_177 (and_177_out, or_87_out, not_50_out);
  and and_178 (and_178_out, or_92_out, not_8_out);
  and and_179 (and_179_out, xor_98_out, or_101_out);
  or or_89 (or_89_out, and_178_out, and_179_out);
  not not_51 (not_51_out, Q0);
  xor xor_95 (xor_95_out, not_14_out, in_12);
  and and_180 (and_180_out, xor_95_out, 1'b1);
  or or_90 (or_90_out, and_172_out, and_180_out);
  and and_181 (and_181_out, in_12, not_49_out);
  and and_182 (and_182_out, or_94_out, not_15_out);
  and and_183 (and_183_out, xor_101_out, or_98_out);
  or or_91 (or_91_out, and_182_out, and_183_out);
  not not_52 (not_52_out, Q3);
  and and_184 (and_184_out, or_94_out, not_52_out);
  and and_185 (and_185_out, or_95_out, not_11_out);
  not not_53 (not_53_out, Q2);
  and and_186 (and_186_out, Q2, xor_94_out);
  xor xor_96 (xor_96_out, not_7_out, or_87_out);
  xor xor_97 (xor_97_out, or_97_out, xor_96_out);
  and and_187 (and_187_out, Q1, xor_97_out);
  or or_92 (or_92_out, and_187_out, and_177_out);
  xor xor_98 (xor_98_out, not_8_out, or_92_out);
  xor xor_99 (xor_99_out, or_101_out, xor_98_out);
  and and_188 (and_188_out, or_92_out, not_51_out);
  or or_93 (R5, and_197_out, and_188_out);
  xor xor_100 (xor_100_out, 1'b1, xor_95_out);
  and and_189 (and_189_out, Q4, xor_100_out);
  or or_94 (or_94_out, and_189_out, and_181_out);
  xor xor_101 (xor_101_out, not_15_out, or_94_out);
  xor xor_102 (xor_102_out, or_98_out, xor_101_out);
  and and_190 (and_190_out, Q3, xor_102_out);
  or or_95 (or_95_out, and_190_out, and_184_out);
  xor xor_103 (xor_103_out, not_11_out, or_95_out);
  and and_191 (and_191_out, xor_103_out, or_103_out);
  or or_96 (or_96_out, and_185_out, and_191_out);
  and and_192 (and_192_out, or_95_out, not_53_out);
  and and_193 (and_193_out, or_99_out, not_12_out);
  and and_194 (and_194_out, xor_105_out, or_104_out);
  or or_97 (or_97_out, and_193_out, and_194_out);
  not not_54 (not_54_out, Q1);
  and and_195 (and_195_out, or_99_out, not_54_out);
  and and_196 (and_196_out, or_100_out, not_7_out);
  not not_55 (not_55_out, Q0);
  and and_197 (and_197_out, Q0, xor_99_out);
  and and_198 (and_198_out, in_13, not_14_out);
  and and_199 (and_199_out, xor_108_out, 1'b1);
  or or_98 (or_98_out, and_198_out, and_199_out);
  not not_56 (not_56_out, Q3);
  and and_200 (and_200_out, or_102_out, not_15_out);
  xor xor_104 (xor_104_out, or_103_out, xor_103_out);
  and and_201 (and_201_out, Q2, xor_104_out);
  or or_99 (or_99_out, and_201_out, and_192_out);
  xor xor_105 (xor_105_out, not_12_out, or_99_out);
  xor xor_106 (xor_106_out, or_104_out, xor_105_out);
  and and_202 (and_202_out, Q1, xor_106_out);
  or or_100 (or_100_out, and_202_out, and_195_out);
  xor xor_107 (xor_107_out, not_7_out, or_100_out);
  and and_203 (and_203_out, xor_107_out, or_108_out);
  or or_101 (or_101_out, and_196_out, and_203_out);
  and and_204 (and_204_out, or_100_out, not_55_out);
  xor xor_108 (xor_108_out, not_14_out, in_13);
  xor xor_109 (xor_109_out, 1'b1, xor_108_out);
  and and_205 (and_205_out, in_13, not_56_out);
  or or_102 (or_102_out, and_212_out, and_205_out);
  and and_206 (and_206_out, xor_111_out, or_109_out);
  or or_103 (or_103_out, and_200_out, and_206_out);
  not not_57 (not_57_out, Q2);
  and and_207 (and_207_out, or_102_out, not_57_out);
  and and_208 (and_208_out, or_106_out, not_11_out);
  and and_209 (and_209_out, xor_113_out, or_112_out);
  or or_104 (or_104_out, and_208_out, and_209_out);
  not not_58 (not_58_out, Q1);
  and and_210 (and_210_out, or_107_out, not_12_out);
  xor xor_110 (xor_110_out, or_108_out, xor_107_out);
  and and_211 (and_211_out, Q0, xor_110_out);
  or or_105 (R4, and_211_out, and_204_out);
  and and_212 (and_212_out, Q3, xor_109_out);
  xor xor_111 (xor_111_out, not_15_out, or_102_out);
  xor xor_112 (xor_112_out, or_109_out, xor_111_out);
  and and_213 (and_213_out, Q2, xor_112_out);
  or or_106 (or_106_out, and_213_out, and_207_out);
  xor xor_113 (xor_113_out, not_11_out, or_106_out);
  xor xor_114 (xor_114_out, or_112_out, xor_113_out);
  and and_214 (and_214_out, or_106_out, not_58_out);
  or or_107 (or_107_out, and_221_out, and_214_out);
  and and_215 (and_215_out, xor_115_out, or_113_out);
  or or_108 (or_108_out, and_210_out, and_215_out);
  not not_59 (not_59_out, Q0);
  and and_216 (and_216_out, or_107_out, not_59_out);
  and and_217 (and_217_out, in_14, not_14_out);
  and and_218 (and_218_out, xor_117_out, 1'b1);
  or or_109 (or_109_out, and_217_out, and_218_out);
  not not_60 (not_60_out, Q2);
  and and_219 (and_219_out, in_14, not_60_out);
  and and_220 (and_220_out, or_111_out, not_15_out);
  not not_61 (not_61_out, Q1);
  and and_221 (and_221_out, Q1, xor_114_out);
  xor xor_115 (xor_115_out, not_12_out, or_107_out);
  xor xor_116 (xor_116_out, or_113_out, xor_115_out);
  and and_222 (and_222_out, Q0, xor_116_out);
  or or_110 (R3, and_222_out, and_216_out);
  xor xor_117 (xor_117_out, not_14_out, in_14);
  xor xor_118 (xor_118_out, 1'b1, xor_117_out);
  and and_223 (and_223_out, Q2, xor_118_out);
  or or_111 (or_111_out, and_223_out, and_219_out);
  xor xor_119 (xor_119_out, not_15_out, or_111_out);
  and and_224 (and_224_out, xor_119_out, or_116_out);
  or or_112 (or_112_out, and_220_out, and_224_out);
  and and_225 (and_225_out, or_111_out, not_61_out);
  and and_226 (and_226_out, or_114_out, not_11_out);
  and and_227 (and_227_out, xor_121_out, or_117_out);
  or or_113 (or_113_out, and_226_out, and_227_out);
  not not_62 (not_62_out, Q0);
  and and_228 (and_228_out, or_114_out, not_62_out);
  and and_229 (and_229_out, in_15, not_14_out);
  xor xor_120 (xor_120_out, or_116_out, xor_119_out);
  and and_230 (and_230_out, Q1, xor_120_out);
  or or_114 (or_114_out, and_230_out, and_225_out);
  xor xor_121 (xor_121_out, not_11_out, or_114_out);
  xor xor_122 (xor_122_out, or_117_out, xor_121_out);
  and and_231 (and_231_out, Q0, xor_122_out);
  or or_115 (R2, and_231_out, and_228_out);
  and and_232 (and_232_out, xor_123_out, 1'b1);
  or or_116 (or_116_out, and_229_out, and_232_out);
  not not_63 (not_63_out, Q1);
  and and_233 (and_233_out, in_15, not_63_out);
  and and_234 (and_234_out, or_118_out, not_15_out);
  and and_235 (and_235_out, xor_125_out, or_120_out);
  or or_117 (or_117_out, and_234_out, and_235_out);
  not not_64 (not_64_out, Q0);
  xor xor_123 (xor_123_out, not_14_out, in_15);
  xor xor_124 (xor_124_out, 1'b1, xor_123_out);
  and and_236 (and_236_out, Q1, xor_124_out);
  or or_118 (or_118_out, and_236_out, and_233_out);
  xor xor_125 (xor_125_out, not_15_out, or_118_out);
  xor xor_126 (xor_126_out, or_120_out, xor_125_out);
  and and_237 (and_237_out, or_118_out, not_64_out);
  or or_119 (R1, and_239_out, and_237_out);
  and and_238 (and_238_out, in_16, not_14_out);
  not not_65 (not_65_out, Q0);
  and and_239 (and_239_out, Q0, xor_126_out);
  xor xor_127 (xor_127_out, not_14_out, in_16);
  and and_240 (and_240_out, xor_127_out, 1'b1);
  or or_120 (or_120_out, and_238_out, and_240_out);
  and and_241 (and_241_out, in_16, not_65_out);
  xor xor_128 (xor_128_out, 1'b1, xor_127_out);
  and and_242 (and_242_out, Q0, xor_128_out);
  or or_121 (R0, and_242_out, and_241_out);
endmodule
