// Digital circuit Flip-Flop D Master-Slave.dig as structural Verilog
module Flip_Flop_D_Master_Slave (
  input  D,
  input  Clk,
  input  in_4,
  output Q
);

  wire nand_1_out, nand_2_out, nand_3_out, nand_4_out, nand_5_out, nand_6_out, nand_8_out, not_1_out,
       not_2_out, not_3_out;

  nand nand_1 (nand_1_out, Clk, D);
  not not_1 (not_1_out, D);
  nand nand_2 (nand_2_out, Clk, not_1_out);
  nand nand_3 (nand_3_out, nand_1_out, nand_4_out);
  nand nand_4 (nand_4_out, nand_2_out, nand_3_out);
  nand nand_5 (nand_5_out, not_2_out, nand_3_out);
  not not_2 (not_2_out, Clk);
  not not_3 (not_3_out, nand_3_out);
  nand nand_6 (nand_6_out, not_2_out, not_3_out);
  nand nand_7 (Q, nand_5_out, nand_8_out);
  nand nand_8 (nand_8_out, nand_6_out, in_4, Q);
  LED led_1 (.in(Q));
endmodule
