// Digital circuit MUX 1x2 bits.dig as structural Verilog
module MUX_1x2_bits (
  input  A,
  input  I0,
  input  I1,
  output S0
);

  wire and_1_out, and_2_out, not_1_out;

  and and_1 (and_1_out, I0, A);
  and and_2 (and_2_out, I1, not_1_out);
  not not_1 (not_1_out, A);
  or or_1 (S0, and_1_out, and_2_out);
endmodule
