// Digital circuit MUX 1x3 bits.dig as structural Verilog
module MUX_1x3_bits (
);

  wire and_1_out, and_2_out, and_3_out, and_4_out, and_5_out, and_6_out, not_1_out, or_1_out, or_2_out,
       or_3_out, undriven, undriven_2, undriven_3, undriven_4, undriven_5, undriven_6, undriven_7;

  and and_1 (and_1_out, undriven, not_1_out);
  and and_2 (and_2_out, undriven_2, not_1_out);
  and and_3 (and_3_out, undriven_3, not_1_out);
  and and_4 (and_4_out, undriven_4, undriven_7);
  not not_1 (not_1_out, undriven_7);
  and and_5 (and_5_out, undriven_5, undriven_7);
  and and_6 (and_6_out, undriven_6, undriven_7);
  or or_1 (or_1_out, and_1_out, and_4_out);
  or or_2 (or_2_out, and_2_out, and_5_out);
  or or_3 (or_3_out, and_3_out, and_6_out);
endmodule
