// Digital circuit MUX 3bits.dig as structural Verilog
module MUX_3bits (
  input  in_1,
  input  in_2,
  input  in_3,
  input  in_4,
  input  in_5,
  input  in_6,
  input  in_7,
  input  in_8,
  input  in_9,
  input  in_10,
  input  in_11
);

  wire and_1_out, and_2_out, and_3_out, and_4_out, and_5_out, and_6_out, and_7_out, and_8_out, and_9_out,
       and_10_out, and_11_out, and_12_out, and_13_out, and_14_out, and_15_out, and_16_out, and_17_out,
       and_18_out, and_19_out, and_20_out, and_21_out, and_22_out, and_23_out, and_24_out, and_25_out,
       and_26_out, and_27_out, and_28_out, and_29_out, and_30_out, and_31_out, and_32_out, and_33_out,
       and_34_out, and_35_out, and_36_out, and_37_out, and_38_out, and_39_out, and_40_out, and_41_out,
       and_42_out, and_43_out, and_44_out, and_45_out, and_46_out, and_47_out, and_48_out, and_49_out,
       and_50_out, and_51_out, and_52_out, and_53_out, and_54_out, and_55_out, and_56_out, and_57_out,
       and_58_out, and_59_out, and_60_out, and_61_out, and_62_out, and_63_out, and_64_out, not_1_out,
       not_2_out, not_3_out;

  not not_1 (not_1_out, in_1);
  not not_2 (not_2_out, in_2);
  not not_3 (not_3_out, in_3);
  and and_1 (and_1_out, not_3_out, not_2_out, not_1_out, in_4);
  and and_2 (and_2_out, not_3_out, not_2_out, not_1_out, in_5);
  and and_3 (and_3_out, not_3_out, not_2_out, not_1_out, in_11);
  and and_4 (and_4_out, not_3_out, not_2_out, not_1_out, in_6);
  and and_5 (and_5_out, not_3_out, not_2_out, not_1_out, in_7);
  and and_6 (and_6_out, not_3_out, not_2_out, not_1_out, in_8);
  and and_7 (and_7_out, not_3_out, not_2_out, not_1_out, in_9);
  and and_8 (and_8_out, not_3_out, not_2_out, not_1_out, in_10);
  and and_9 (and_9_out, in_3, not_2_out, not_1_out, in_4);
  and and_10 (and_10_out, in_3, not_2_out, not_1_out, in_5);
  and and_11 (and_11_out, in_3, not_2_out, not_1_out, in_11);
  and and_12 (and_12_out, in_3, not_2_out, not_1_out, in_6);
  and and_13 (and_13_out, in_3, not_2_out, not_1_out, in_7);
  and and_14 (and_14_out, in_3, not_2_out, not_1_out, in_8);
  and and_15 (and_15_out, in_3, not_2_out, not_1_out, in_9);
  and and_16 (and_16_out, in_3, not_2_out, not_1_out, in_10);
  and and_17 (and_17_out, not_3_out, in_2, not_1_out, in_4);
  and and_18 (and_18_out, not_3_out, in_2, not_1_out, in_5);
  and and_19 (and_19_out, not_3_out, in_2, not_1_out, in_11);
  and and_20 (and_20_out, not_3_out, in_2, not_1_out, in_6);
  and and_21 (and_21_out, not_3_out, in_2, not_1_out, in_7);
  and and_22 (and_22_out, not_3_out, in_2, not_1_out, in_8);
  and and_23 (and_23_out, not_3_out, in_2, not_1_out, in_9);
  and and_24 (and_24_out, not_3_out, in_2, not_1_out, in_10);
  and and_25 (and_25_out, in_3, in_2, not_1_out, in_4);
  and and_26 (and_26_out, in_3, in_2, not_1_out, in_5);
  and and_27 (and_27_out, in_3, in_2, not_1_out, in_11);
  and and_28 (and_28_out, in_3, in_2, not_1_out, in_6);
  and and_29 (and_29_out, in_3, in_2, not_1_out, in_7);
  and and_30 (and_30_out, in_3, in_2, not_1_out, in_8);
  and and_31 (and_31_out, in_3, in_2, not_1_out, in_9);
  and and_32 (and_32_out, in_3, in_2, not_1_out, in_10);
  and and_33 (and_33_out, not_3_out, not_2_out, in_1, in_4);
  and and_34 (and_34_out, not_3_out, not_2_out, in_1, in_5);
  and and_35 (and_35_out, not_3_out, not_2_out, in_1, in_11);
  and and_36 (and_36_out, not_3_out, not_2_out, in_1, in_6);
  and and_37 (and_37_out, not_3_out, not_2_out, in_1, in_7);
  and and_38 (and_38_out, not_3_out, not_2_out, in_1, in_8);
  and and_39 (and_39_out, not_3_out, not_2_out, in_1, in_9);
  and and_40 (and_40_out, not_3_out, not_2_out, in_1, in_10);
  and and_41 (and_41_out, in_3, not_2_out, in_1, in_4);
  and and_42 (and_42_out, in_3, not_2_out, in_1, in_5);
  and and_43 (and_43_out, in_3, not_2_out, in_1, in_11);
  and and_44 (and_44_out, in_3, not_2_out, in_1, in_6);
  and and_45 (and_45_out, in_3, not_2_out, in_1, in_7);
  and and_46 (and_46_out, in_3, not_2_out, in_1, in_8);
  and and_47 (and_47_out, in_3, not_2_out, in_1, in_9);
  and and_48 (and_48_out, in_3, not_2_out, in_1, in_10);
  and and_49 (and_49_out, not_3_out, in_2, in_1, in_4);
  and and_50 (and_50_out, not_3_out, in_2, in_1, in_5);
  and and_51 (and_51_out, not_3_out, in_2, in_1, in_11);
  and and_52 (and_52_out, not_3_out, in_2, in_1, in_6);
  and and_53 (and_53_out, not_3_out, in_2, in_1, in_7);
  and and_54 (and_54_out, not_3_out, in_2, in_1, in_8);
  and and_55 (and_55_out, not_3_out, in_2, in_1, in_9);
  and and_56 (and_56_out, not_3_out, in_2, in_1, in_10);
  and and_57 (and_57_out, in_3, in_2, in_1, in_4);
  and and_58 (and_58_out, in_3, in_2, in_1, in_5);
  and and_59 (and_59_out, in_3, in_2, in_1, in_11);
  and and_60 (and_60_out, in_3, in_2, in_1, in_6);
  and and_61 (and_61_out, in_3, in_2, in_1, in_7);
  and and_62 (and_62_out, in_3, in_2, in_1, in_8);
  and and_63 (and_63_out, in_3, in_2, in_1, in_9);
  and and_64 (and_64_out, in_3, in_2, in_1, in_10);
endmodule
