// Digital circuit MUX 8x8 bits.dig as structural Verilog
module MUX_8x8_bits (
);

  wire and_1_out, and_2_out, and_3_out, and_4_out, and_5_out, and_6_out, and_7_out, and_8_out, and_9_out,
       and_10_out, and_11_out, and_12_out, and_13_out, and_14_out, and_15_out, and_16_out, and_17_out,
       and_18_out, and_19_out, and_20_out, and_21_out, and_22_out, and_23_out, and_24_out, and_25_out,
       and_26_out, and_27_out, and_28_out, and_29_out, and_30_out, and_31_out, and_32_out, and_33_out,
       and_34_out, and_35_out, and_36_out, and_37_out, and_38_out, and_39_out, and_40_out, and_41_out,
       and_42_out, and_43_out, and_44_out, and_45_out, and_46_out, and_47_out, and_48_out, and_49_out,
       and_50_out, and_51_out, and_52_out, and_53_out, and_54_out, and_55_out, and_56_out, and_57_out,
       and_58_out, and_59_out, and_60_out, and_61_out, and_62_out, and_63_out, and_64_out, and_65_out,
       and_66_out, and_67_out, and_68_out, and_69_out, and_70_out, and_71_out, and_72_out, and_73_out,
       and_74_out, and_75_out, and_76_out, and_77_out, and_78_out, and_79_out, and_80_out, and_81_out,
       and_82_out, and_83_out, and_84_out, and_85_out, and_86_out, and_87_out, and_88_out, and_89_out,
       and_90_out, and_91_out, and_92_out, and_93_out, and_94_out, and_95_out, and_96_out, and_97_out,
       and_98_out, and_99_out, and_100_out, and_101_out, and_102_out, and_103_out, and_104_out, and_105_out,
       and_106_out, and_107_out, and_108_out, and_109_out, and_110_out, and_111_out, and_112_out,
       and_113_out, and_114_out, and_115_out, and_116_out, and_117_out, and_118_out, and_119_out,
       and_120_out, and_121_out, and_122_out, and_123_out, and_124_out, and_125_out, and_126_out,
       and_127_out, and_128_out, or_1_out, or_2_out, or_4_out, or_5_out, or_6_out, or_7_out, or_9_out,
       or_10_out, or_11_out, or_12_out, or_14_out, or_15_out, or_16_out, or_17_out, or_19_out, or_20_out,
       or_21_out, or_22_out, or_24_out, or_25_out, or_26_out, or_27_out, or_29_out, or_30_out, or_31_out,
       or_32_out, or_34_out, or_35_out, or_36_out, or_37_out, or_39_out, or_40_out, undriven, undriven_2,
       undriven_3, undriven_4, undriven_5, undriven_6, undriven_7, undriven_8, undriven_9, undriven_10,
       undriven_11, undriven_12, undriven_13, undriven_14, undriven_15, undriven_16, undriven_17,
       undriven_18, undriven_19, undriven_20, undriven_21, undriven_22, undriven_23, undriven_24,
       undriven_25, undriven_26, undriven_27, undriven_28, undriven_29, undriven_30, undriven_31,
       undriven_32, undriven_33, undriven_34, undriven_35, undriven_36, undriven_37, undriven_38,
       undriven_39, undriven_40, undriven_41, undriven_42, undriven_43, undriven_44, undriven_45,
       undriven_46, undriven_47, undriven_48, undriven_49, undriven_50, undriven_51, undriven_52,
       undriven_53, undriven_54, undriven_55, undriven_56, undriven_57, undriven_58, undriven_59,
       undriven_60, undriven_61, undriven_62, undriven_63, undriven_64, undriven_65, undriven_66,
       undriven_67, undriven_68, undriven_69, undriven_70, undriven_71, undriven_72, undriven_73,
       undriven_74, undriven_75, undriven_76, undriven_77, undriven_78, undriven_79, undriven_80,
       undriven_81, undriven_82, undriven_83, undriven_84, undriven_85, undriven_86, undriven_87,
       undriven_88, undriven_89, undriven_90, undriven_91, undriven_92, undriven_93, undriven_94,
       undriven_95, undriven_96, undriven_97, undriven_98, undriven_99, undriven_100, undriven_101,
       undriven_102, undriven_103, undriven_104, undriven_105, undriven_106, undriven_107, undriven_108,
       undriven_109, undriven_110, undriven_111, undriven_112, undriven_113, undriven_114, undriven_115,
       undriven_116, undriven_117, undriven_118, undriven_119, undriven_120, undriven_121, undriven_122,
       undriven_123, undriven_124, undriven_125, undriven_126, undriven_127, undriven_128, undriven_129,
       undriven_130, undriven_131, undriven_132, undriven_133, undriven_134, undriven_135, undriven_136;

  and and_1 (and_1_out, undriven_130, undriven_132, undriven_134, undriven_136, undriven_128);
  and and_2 (and_2_out, undriven_130, undriven_132, undriven_134, undriven_135, undriven_127);
  or or_1 (or_1_out, and_4_out, and_3_out, and_2_out, and_1_out);
  and and_3 (and_3_out, undriven_130, undriven_132, undriven_133, undriven_136, undriven_126);
  and and_4 (and_4_out, undriven_130, undriven_132, undriven_133, undriven_135, undriven_125);
  and and_5 (and_5_out, undriven_130, undriven_131, undriven_134, undriven_136, undriven_124);
  and and_6 (and_6_out, undriven_130, undriven_131, undriven_134, undriven_135, undriven_123);
  or or_2 (or_2_out, and_8_out, and_7_out, and_6_out, and_5_out);
  and and_7 (and_7_out, undriven_130, undriven_131, undriven_133, undriven_136, undriven_122);
  and and_8 (and_8_out, undriven_130, undriven_131, undriven_133, undriven_135, undriven_121);
  and and_9 (and_9_out, undriven_129, undriven_132, undriven_134, undriven_136, undriven_120);
  // Or or_3 has open pins: In_1=or_5_out, In_2=or_4_out, In_3=or_2_out, In_4=or_1_out, out=open
  and and_10 (and_10_out, undriven_129, undriven_132, undriven_134, undriven_135, undriven_119);
  or or_4 (or_4_out, and_12_out, and_11_out, and_10_out, and_9_out);
  and and_11 (and_11_out, undriven_129, undriven_132, undriven_133, undriven_136, undriven_118);
  and and_12 (and_12_out, undriven_129, undriven_132, undriven_133, undriven_135, undriven_117);
  and and_13 (and_13_out, undriven_129, undriven_131, undriven_134, undriven_136, undriven_116);
  and and_14 (and_14_out, undriven_129, undriven_131, undriven_134, undriven_135, undriven_115);
  or or_5 (or_5_out, and_16_out, and_15_out, and_14_out, and_13_out);
  and and_15 (and_15_out, undriven_129, undriven_131, undriven_133, undriven_136, undriven_114);
  and and_16 (and_16_out, undriven_129, undriven_131, undriven_133, undriven_135, undriven_113);
  and and_17 (and_17_out, undriven_130, undriven_132, undriven_134, undriven_136, undriven_112);
  and and_18 (and_18_out, undriven_130, undriven_132, undriven_134, undriven_135, undriven_111);
  or or_6 (or_6_out, and_20_out, and_19_out, and_18_out, and_17_out);
  and and_19 (and_19_out, undriven_130, undriven_132, undriven_133, undriven_136, undriven_110);
  and and_20 (and_20_out, undriven_130, undriven_132, undriven_133, undriven_135, undriven_109);
  and and_21 (and_21_out, undriven_130, undriven_131, undriven_134, undriven_136, undriven_108);
  and and_22 (and_22_out, undriven_130, undriven_131, undriven_134, undriven_135, undriven_107);
  or or_7 (or_7_out, and_24_out, and_23_out, and_22_out, and_21_out);
  and and_23 (and_23_out, undriven_130, undriven_131, undriven_133, undriven_136, undriven_106);
  and and_24 (and_24_out, undriven_130, undriven_131, undriven_133, undriven_135, undriven_105);
  and and_25 (and_25_out, undriven_129, undriven_132, undriven_134, undriven_136, undriven_104);
  // Or or_8 has open pins: In_1=or_10_out, In_2=or_9_out, In_3=or_7_out, In_4=or_6_out, out=open
  and and_26 (and_26_out, undriven_129, undriven_132, undriven_134, undriven_135, undriven_103);
  or or_9 (or_9_out, and_28_out, and_27_out, and_26_out, and_25_out);
  and and_27 (and_27_out, undriven_129, undriven_132, undriven_133, undriven_136, undriven_102);
  and and_28 (and_28_out, undriven_129, undriven_132, undriven_133, undriven_135, undriven_101);
  and and_29 (and_29_out, undriven_129, undriven_131, undriven_134, undriven_136, undriven_100);
  and and_30 (and_30_out, undriven_129, undriven_131, undriven_134, undriven_135, undriven_99);
  or or_10 (or_10_out, and_32_out, and_31_out, and_30_out, and_29_out);
  and and_31 (and_31_out, undriven_129, undriven_131, undriven_133, undriven_136, undriven_98);
  and and_32 (and_32_out, undriven_129, undriven_131, undriven_133, undriven_135, undriven_97);
  and and_33 (and_33_out, undriven_130, undriven_132, undriven_134, undriven_136, undriven_96);
  and and_34 (and_34_out, undriven_130, undriven_132, undriven_134, undriven_135, undriven_95);
  or or_11 (or_11_out, and_36_out, and_35_out, and_34_out, and_33_out);
  and and_35 (and_35_out, undriven_130, undriven_132, undriven_133, undriven_136, undriven_94);
  and and_36 (and_36_out, undriven_130, undriven_132, undriven_133, undriven_135, undriven_93);
  and and_37 (and_37_out, undriven_130, undriven_131, undriven_134, undriven_136, undriven_92);
  and and_38 (and_38_out, undriven_130, undriven_131, undriven_134, undriven_135, undriven_91);
  or or_12 (or_12_out, and_40_out, and_39_out, and_38_out, and_37_out);
  and and_39 (and_39_out, undriven_130, undriven_131, undriven_133, undriven_136, undriven_90);
  and and_40 (and_40_out, undriven_130, undriven_131, undriven_133, undriven_135, undriven_89);
  and and_41 (and_41_out, undriven_129, undriven_132, undriven_134, undriven_136, undriven_88);
  // Or or_13 has open pins: In_1=or_15_out, In_2=or_14_out, In_3=or_12_out, In_4=or_11_out, out=open
  and and_42 (and_42_out, undriven_129, undriven_132, undriven_134, undriven_135, undriven_87);
  or or_14 (or_14_out, and_44_out, and_43_out, and_42_out, and_41_out);
  and and_43 (and_43_out, undriven_129, undriven_132, undriven_133, undriven_136, undriven_86);
  and and_44 (and_44_out, undriven_129, undriven_132, undriven_133, undriven_135, undriven_85);
  and and_45 (and_45_out, undriven_129, undriven_131, undriven_134, undriven_136, undriven_84);
  and and_46 (and_46_out, undriven_129, undriven_131, undriven_134, undriven_135, undriven_83);
  or or_15 (or_15_out, and_48_out, and_47_out, and_46_out, and_45_out);
  and and_47 (and_47_out, undriven_129, undriven_131, undriven_133, undriven_136, undriven_82);
  and and_48 (and_48_out, undriven_129, undriven_131, undriven_133, undriven_135, undriven_81);
  and and_49 (and_49_out, undriven_130, undriven_132, undriven_134, undriven_136, undriven_80);
  and and_50 (and_50_out, undriven_130, undriven_132, undriven_134, undriven_135, undriven_79);
  or or_16 (or_16_out, and_52_out, and_51_out, and_50_out, and_49_out);
  and and_51 (and_51_out, undriven_130, undriven_132, undriven_133, undriven_136, undriven_78);
  and and_52 (and_52_out, undriven_130, undriven_132, undriven_133, undriven_135, undriven_77);
  and and_53 (and_53_out, undriven_130, undriven_131, undriven_134, undriven_136, undriven_76);
  and and_54 (and_54_out, undriven_130, undriven_131, undriven_134, undriven_135, undriven_75);
  or or_17 (or_17_out, and_56_out, and_55_out, and_54_out, and_53_out);
  and and_55 (and_55_out, undriven_130, undriven_131, undriven_133, undriven_136, undriven_74);
  and and_56 (and_56_out, undriven_130, undriven_131, undriven_133, undriven_135, undriven_73);
  and and_57 (and_57_out, undriven_129, undriven_132, undriven_134, undriven_136, undriven_72);
  // Or or_18 has open pins: In_1=or_20_out, In_2=or_19_out, In_3=or_17_out, In_4=or_16_out, out=open
  and and_58 (and_58_out, undriven_129, undriven_132, undriven_134, undriven_135, undriven_71);
  or or_19 (or_19_out, and_60_out, and_59_out, and_58_out, and_57_out);
  and and_59 (and_59_out, undriven_129, undriven_132, undriven_133, undriven_136, undriven_70);
  and and_60 (and_60_out, undriven_129, undriven_132, undriven_133, undriven_135, undriven_69);
  and and_61 (and_61_out, undriven_129, undriven_131, undriven_134, undriven_136, undriven_68);
  and and_62 (and_62_out, undriven_129, undriven_131, undriven_134, undriven_135, undriven_67);
  or or_20 (or_20_out, and_64_out, and_63_out, and_62_out, and_61_out);
  and and_63 (and_63_out, undriven_129, undriven_131, undriven_133, undriven_136, undriven_66);
  and and_64 (and_64_out, undriven_129, undriven_131, undriven_133, undriven_135, undriven_65);
  and and_65 (and_65_out, undriven_130, undriven_132, undriven_134, undriven_136, undriven_64);
  and and_66 (and_66_out, undriven_130, undriven_132, undriven_134, undriven_135, undriven_63);
  or or_21 (or_21_out, and_68_out, and_67_out, and_66_out, and_65_out);
  and and_67 (and_67_out, undriven_130, undriven_132, undriven_133, undriven_136, undriven_62);
  and and_68 (and_68_out, undriven_130, undriven_132, undriven_133, undriven_135, undriven_61);
  and and_69 (and_69_out, undriven_130, undriven_131, undriven_134, undriven_136, undriven_60);
  and and_70 (and_70_out, undriven_130, undriven_131, undriven_134, undriven_135, undriven_59);
  or or_22 (or_22_out, and_72_out, and_71_out, and_70_out, and_69_out);
  and and_71 (and_71_out, undriven_130, undriven_131, undriven_133, undriven_136, undriven_58);
  and and_72 (and_72_out, undriven_130, undriven_131, undriven_133, undriven_135, undriven_57);
  and and_73 (and_73_out, undriven_129, undriven_132, undriven_134, undriven_136, undriven_56);
  // Or or_23 has open pins: In_1=or_25_out, In_2=or_24_out, In_3=or_22_out, In_4=or_21_out, out=open
  and and_74 (and_74_out, undriven_129, undriven_132, undriven_134, undriven_135, undriven_55);
  or or_24 (or_24_out, and_76_out, and_75_out, and_74_out, and_73_out);
  and and_75 (and_75_out, undriven_129, undriven_132, undriven_133, undriven_136, undriven_54);
  and and_76 (and_76_out, undriven_129, undriven_132, undriven_133, undriven_135, undriven_53);
  and and_77 (and_77_out, undriven_129, undriven_131, undriven_134, undriven_136, undriven_52);
  and and_78 (and_78_out, undriven_129, undriven_131, undriven_134, undriven_135, undriven_51);
  or or_25 (or_25_out, and_80_out, and_79_out, and_78_out, and_77_out);
  and and_79 (and_79_out, undriven_129, undriven_131, undriven_133, undriven_136, undriven_50);
  and and_80 (and_80_out, undriven_129, undriven_131, undriven_133, undriven_135, undriven_49);
  and and_81 (and_81_out, undriven_130, undriven_132, undriven_134, undriven_136, undriven_48);
  and and_82 (and_82_out, undriven_130, undriven_132, undriven_134, undriven_135, undriven_47);
  or or_26 (or_26_out, and_84_out, and_83_out, and_82_out, and_81_out);
  and and_83 (and_83_out, undriven_130, undriven_132, undriven_133, undriven_136, undriven_46);
  and and_84 (and_84_out, undriven_130, undriven_132, undriven_133, undriven_135, undriven_45);
  and and_85 (and_85_out, undriven_130, undriven_131, undriven_134, undriven_136, undriven_44);
  and and_86 (and_86_out, undriven_130, undriven_131, undriven_134, undriven_135, undriven_43);
  or or_27 (or_27_out, and_88_out, and_87_out, and_86_out, and_85_out);
  and and_87 (and_87_out, undriven_130, undriven_131, undriven_133, undriven_136, undriven_42);
  and and_88 (and_88_out, undriven_130, undriven_131, undriven_133, undriven_135, undriven_41);
  and and_89 (and_89_out, undriven_129, undriven_132, undriven_134, undriven_136, undriven_40);
  // Or or_28 has open pins: In_1=or_30_out, In_2=or_29_out, In_3=or_27_out, In_4=or_26_out, out=open
  and and_90 (and_90_out, undriven_129, undriven_132, undriven_134, undriven_135, undriven_39);
  or or_29 (or_29_out, and_92_out, and_91_out, and_90_out, and_89_out);
  and and_91 (and_91_out, undriven_129, undriven_132, undriven_133, undriven_136, undriven_38);
  and and_92 (and_92_out, undriven_129, undriven_132, undriven_133, undriven_135, undriven_37);
  and and_93 (and_93_out, undriven_129, undriven_131, undriven_134, undriven_136, undriven_36);
  and and_94 (and_94_out, undriven_129, undriven_131, undriven_134, undriven_135, undriven_35);
  or or_30 (or_30_out, and_96_out, and_95_out, and_94_out, and_93_out);
  and and_95 (and_95_out, undriven_129, undriven_131, undriven_133, undriven_136, undriven_34);
  and and_96 (and_96_out, undriven_129, undriven_131, undriven_133, undriven_135, undriven_33);
  and and_97 (and_97_out, undriven_130, undriven_132, undriven_134, undriven_136, undriven_32);
  and and_98 (and_98_out, undriven_130, undriven_132, undriven_134, undriven_135, undriven_31);
  or or_31 (or_31_out, and_100_out, and_99_out, and_98_out, and_97_out);
  and and_99 (and_99_out, undriven_130, undriven_132, undriven_133, undriven_136, undriven_30);
  and and_100 (and_100_out, undriven_130, undriven_132, undriven_133, undriven_135, undriven_29);
  and and_101 (and_101_out, undriven_130, undriven_131, undriven_134, undriven_136, undriven_28);
  and and_102 (and_102_out, undriven_130, undriven_131, undriven_134, undriven_135, undriven_27);
  or or_32 (or_32_out, and_104_out, and_103_out, and_102_out, and_101_out);
  and and_103 (and_103_out, undriven_130, undriven_131, undriven_133, undriven_136, undriven);
  and and_104 (and_104_out, undriven_130, undriven_131, undriven_133, undriven_135, undriven_2);
  and and_105 (and_105_out, undriven_129, undriven_132, undriven_134, undriven_136, undriven_3);
  // Or or_33 has open pins: In_1=or_35_out, In_2=or_34_out, In_3=or_32_out, In_4=or_31_out, out=open
  and and_106 (and_106_out, undriven_129, undriven_132, undriven_134, undriven_135, undriven_4);
  or or_34 (or_34_out, and_108_out, and_107_out, and_106_out, and_105_out);
  and and_107 (and_107_out, undriven_129, undriven_132, undriven_133, undriven_136, undriven_5);
  and and_108 (and_108_out, undriven_129, undriven_132, undriven_133, undriven_135, undriven_6);
  and and_109 (and_109_out, undriven_129, undriven_131, undriven_134, undriven_136, undriven_7);
  and and_110 (and_110_out, undriven_129, undriven_131, undriven_134, undriven_135, undriven_8);
  or or_35 (or_35_out, and_112_out, and_111_out, and_110_out, and_109_out);
  and and_111 (and_111_out, undriven_129, undriven_131, undriven_133, undriven_136, undriven_9);
  and and_112 (and_112_out, undriven_129, undriven_131, undriven_133, undriven_135, undriven_10);
  and and_113 (and_113_out, undriven_130, undriven_132, undriven_134, undriven_136, undriven_11);
  and and_114 (and_114_out, undriven_130, undriven_132, undriven_134, undriven_135, undriven_12);
  or or_36 (or_36_out, and_116_out, and_115_out, and_114_out, and_113_out);
  and and_115 (and_115_out, undriven_130, undriven_132, undriven_133, undriven_136, undriven_13);
  and and_116 (and_116_out, undriven_130, undriven_132, undriven_133, undriven_135, undriven_14);
  and and_117 (and_117_out, undriven_130, undriven_131, undriven_134, undriven_136, undriven_15);
  and and_118 (and_118_out, undriven_130, undriven_131, undriven_134, undriven_135, undriven_16);
  or or_37 (or_37_out, and_120_out, and_119_out, and_118_out, and_117_out);
  and and_119 (and_119_out, undriven_130, undriven_131, undriven_133, undriven_136, undriven_17);
  and and_120 (and_120_out, undriven_130, undriven_131, undriven_133, undriven_135, undriven_18);
  and and_121 (and_121_out, undriven_129, undriven_132, undriven_134, undriven_136, undriven_19);
  // Or or_38 has open pins: In_1=or_40_out, In_2=or_39_out, In_3=or_37_out, In_4=or_36_out, out=open
  and and_122 (and_122_out, undriven_129, undriven_132, undriven_134, undriven_135, undriven_20);
  or or_39 (or_39_out, and_124_out, and_123_out, and_122_out, and_121_out);
  and and_123 (and_123_out, undriven_129, undriven_132, undriven_133, undriven_136, undriven_21);
  and and_124 (and_124_out, undriven_129, undriven_132, undriven_133, undriven_135, undriven_22);
  and and_125 (and_125_out, undriven_129, undriven_131, undriven_134, undriven_136, undriven_23);
  and and_126 (and_126_out, undriven_129, undriven_131, undriven_134, undriven_135, undriven_24);
  or or_40 (or_40_out, and_128_out, and_127_out, and_126_out, and_125_out);
  and and_127 (and_127_out, undriven_129, undriven_131, undriven_133, undriven_136, undriven_25);
  and and_128 (and_128_out, undriven_129, undriven_131, undriven_133, undriven_135, undriven_26);
endmodule
