// Digital circuit Memory Loader.dig as structural Verilog
module Memory_Loader (
  input  C,
  input  CE,
  output [7:0] A,
  output W,
  output CLK,
  output _0,
  output _1,
  output [7:0] Do
);

  wire counter_2_out;
  wire [7:0] counter_1_out;

  and and_1 (CLK, C, CE);
  Counter counter_1 (.en(1'b1), .C(CLK), .clr(1'b0), .out(counter_1_out[0]));  // open: ovf
  Counter counter_2 (.en(1'b1), .C(counter_1_out[0]), .clr(1'b0), .out(counter_2_out));  // open: ovf
  Counter counter_3 (.en(1'b1), .C(counter_2_out), .clr(1'b0), .out(counter_1_out[1]));  // open: ovf
  Counter counter_4 (.en(1'b1), .C(counter_1_out[1]), .clr(1'b0), .out(counter_1_out[2]));  // open: ovf
  Counter counter_5 (.en(1'b1), .C(counter_1_out[2]), .clr(1'b0), .out(counter_1_out[3]));  // open: ovf
  Counter counter_6 (.en(1'b1), .C(counter_1_out[3]), .clr(1'b0), .out(counter_1_out[4]));  // open: ovf
  Counter counter_7 (.en(1'b1), .C(counter_1_out[4]), .clr(1'b0), .out(counter_1_out[5]));  // open: ovf
  Counter counter_8 (.en(1'b1), .C(counter_1_out[5]), .clr(1'b0), .out(counter_1_out[6]));  // open: ovf
  assign A = ~counter_1_out;  // Not not_1, 8 bits wide
  Counter counter_9 (.en(1'b1), .C(counter_1_out[6]), .clr(1'b0), .out(counter_1_out[7]));  // open: ovf
  LED led_1 (.in(Do[7]));
  LED led_2 (.in(Do[6]));
  LED led_3 (.in(Do[5]));
  EEPROMDualPort #(.AddrBits(8), .Bits(8)) eepromdualport_1 (
    .A(A), .Din({8{1'b1}}), .str(1'b0), .C(1'b0), .ld(1'b1), .D(Do));
  LED led_4 (.in(Do[4]));
  LED led_5 (.in(Do[3]));
  LED led_6 (.in(Do[2]));
  LED led_7 (.in(Do[1]));
  LED led_8 (.in(Do[0]));

  assign _0 = 1'b0;
  assign _1 = 1'b0;
  assign W = CE;

  // Notes on the sheet:
  //   contents of eepromdualport_1 (hex, n*v repeats v):
  //   a98670,f69b5,0,98bd91,a7dd0c,a98ac7,9009,a7dd0c,9009,9009,9009
  //   ,a98ac7,9009,9009,a7dd0c,a7dd0c,a7dd0c,9009,a98ac7,9009,f69b5
  //   ,a7dd0c,9009,0,a98670,f69b5,0,98bd91,9009,0,98bd91,9009,9009,f69b5
  //   ,a7dd0c,40249,f69b5,0,98bd91,40249,a7dd0c,40249,9009,f69b5,a7dd0c,a7dd0c
  //   ,40249,a98ac7,a98ac7,a98ac7,0,9009,0,98bd91,40249,9009,a98670
  //   ,f69b5,0,98bd91,40249,a98ac7,40249,9009,40249,a98ac7,a98ac7,f69b5
  //   ,a98670,f69b5,0,98bd91,0,a7dd0c,a98ac7,0,a98670,f69b5,0,98bd91
  //   ,a98ac7,0,9009,f69b5,a98ac7,9009,f69b5,a98ac7,9009,a98ac7,0,a7dd0c
  //   ,9009,f69b5,a7dd0c,a98ac7,f69b5,a98ac7,0,98bd91,a98ac7,a98ac7
  //   ,0,a98ac7,0,a98ac7,9009,a98ac7,9009,a7dd0c,a98ac7,9009,a98670
  //   ,f69b5,0,98bd91,a7dd0c,a98ac7,9009,a7dd0c,9009,9009,9009,a98ac7
  //   ,9009,9009,a7dd0c,a7dd0c,a7dd0c,9009,a98ac7,9009,f69b5,a7dd0c
  //   ,9009,0,a98670,f69b5,0,98bd91,9009,0,98bd91,9009,9009,f69b5,a7dd0c
  //   ,40249,f69b5,0,98bd91,40249,a7dd0c,40249,9009,f69b5,a7dd0c,a7dd0c
  //   ,40249,a98ac7,a98ac7,a98ac7,0,9009,0,98bd91,40249,9009,a98670
  //   ,f69b5,0,98bd91,40249,a98ac7,40249,9009,40249,a98ac7,a98ac7,f69b5
  //   ,a98670,f69b5,0,98bd91,0,a7dd0c,a98ac7,0,a98670,f69b5,0,98bd91
  //   ,a98ac7,0,9009,f69b5,a98ac7,9009,f69b5,a98ac7,9009,a98ac7,0,a7dd0c
  //   ,9009,f69b5,a7dd0c,a98ac7,f69b5,a98ac7,0,98bd91,a98ac7,a98ac7
  //   ,0,a98ac7,0,a98ac7,9009,a98ac7,9009,a7dd0c,a98ac7,9009,a98670
  //   ,f69b5,0,98bd91,a7dd0c,a98ac7,9009,a7dd0c,9009,9009,9009,a98ac7
  //   ,9009,9009,a7dd0c,a7dd0c,a7dd0c,9009,a98ac7,9009,f69b5,a7dd0c
  //   ,9009,0,a98670,f69b5,0,98bd91,9009,0,98bd91,9009
endmodule
