// Digital circuit Oscilator D Master-Slave.dig as structural Verilog
module Oscilator_D_Master_Slave (
  input  in_1
);

  wire nand_1_out, nand_2_out, nand_3_out, nand_4_out, nand_5_out, nand_6_out, nand_7_out, nand_8_out,
       not_1_out, not_2_out, not_3_out;

  not not_1 (not_1_out, nand_8_out);
  nand nand_1 (nand_1_out, in_1, nand_8_out);
  nand nand_2 (nand_2_out, in_1, not_1_out);
  nand nand_3 (nand_3_out, nand_1_out, nand_4_out);
  nand nand_4 (nand_4_out, nand_2_out, nand_3_out);
  not not_2 (not_2_out, in_1);
  not not_3 (not_3_out, nand_3_out);
  nand nand_5 (nand_5_out, not_2_out, nand_3_out);
  nand nand_6 (nand_6_out, not_2_out, not_3_out);
  nand nand_7 (nand_7_out, nand_5_out, nand_8_out);
  nand nand_8 (nand_8_out, nand_6_out, nand_7_out);
  LED led_1 (.in(nand_7_out));
endmodule
