// Digital circuit Process Register.dig as structural Verilog
module Process_Register (
  input  D0,
  input  D1,
  input  D2,
  input  D3,
  input  D4,
  input  D5,
  input  D6,
  input  D7,
  input  C,
  input  CE,
  input  SE,
  input  R
);

  wire and_1_out, and_2_out, driver_1_out, driver_2_out, driver_3_out, driver_4_out, driver_5_out,
       driver_6_out, driver_7_out, driver_8_out, nand_1_out, nand_2_out, nand_3_out, nand_4_out, nand_5_out,
       nand_6_out, nand_7_out, nand_8_out, nand_9_out, nand_10_out, nand_11_out, nand_12_out, nand_13_out,
       nand_14_out, nand_15_out, nand_16_out, nand_17_out, nand_18_out, nand_19_out, nand_20_out,
       nand_21_out, nand_22_out, nand_23_out, nand_24_out, nand_25_out, nand_26_out, nand_27_out,
       nand_28_out, nand_29_out, nand_30_out, nand_31_out, nand_32_out, not_1_out, not_2_out, not_3_out,
       not_4_out, not_5_out, not_6_out, not_7_out, not_8_out, not_9_out, not_10_out, not_11_out, reset_1_out,
       xor_1_out, xor_2_out, xor_3_out, xor_4_out, xor_5_out, xor_6_out, xor_7_out, xor_8_out, xor_9_out;

  Reset #(.invertOutput("false")) reset_1 (.out(reset_1_out));
  xor xor_1 (xor_1_out, reset_1_out, R);
  and and_1 (and_1_out, C, CE);
  not not_1 (not_1_out, and_1_out);
  not not_2 (not_2_out, not_3_out);
  not not_3 (not_3_out, not_1_out);
  not not_4 (not_4_out, D0);
  nand nand_1 (nand_1_out, not_4_out, and_2_out);
  and and_2 (and_2_out, ~not_2_out, ~and_1_out);  // And
  nand nand_2 (nand_2_out, and_2_out, D0);
  xor xor_2 (xor_2_out, xor_1_out, nand_1_out);
  nand nand_3 (nand_3_out, nand_2_out, nand_4_out);
  nand nand_4 (nand_4_out, xor_2_out, nand_3_out);
  not not_5 (not_5_out, D1);
  assign driver_1_out = SE ? nand_3_out : 1'bz;  // Driver driver_1
  nand nand_5 (nand_5_out, not_5_out, and_2_out);
  nand nand_6 (nand_6_out, and_2_out, D1);
  xor xor_3 (xor_3_out, xor_1_out, nand_5_out);
  nand nand_7 (nand_7_out, nand_6_out, nand_8_out);
  nand nand_8 (nand_8_out, xor_3_out, nand_7_out);
  not not_6 (not_6_out, D2);
  assign driver_2_out = SE ? nand_7_out : 1'bz;  // Driver driver_2
  nand nand_9 (nand_9_out, not_6_out, and_2_out);
  nand nand_10 (nand_10_out, and_2_out, D2);
  xor xor_4 (xor_4_out, xor_1_out, nand_9_out);
  nand nand_11 (nand_11_out, nand_10_out, nand_12_out);
  nand nand_12 (nand_12_out, xor_4_out, nand_11_out);
  assign driver_3_out = SE ? nand_11_out : 1'bz;  // Driver driver_3
  not not_7 (not_7_out, D3);
  nand nand_13 (nand_13_out, not_7_out, and_2_out);
  nand nand_14 (nand_14_out, and_2_out, D3);
  xor xor_5 (xor_5_out, xor_1_out, nand_13_out);
  nand nand_15 (nand_15_out, nand_14_out, nand_16_out);
  nand nand_16 (nand_16_out, xor_5_out, nand_15_out);
  assign driver_4_out = SE ? nand_15_out : 1'bz;  // Driver driver_4
  not not_8 (not_8_out, D4);
  nand nand_17 (nand_17_out, not_8_out, and_2_out);
  nand nand_18 (nand_18_out, and_2_out, D4);
  xor xor_6 (xor_6_out, xor_1_out, nand_17_out);
  nand nand_19 (nand_19_out, nand_18_out, nand_20_out);
  nand nand_20 (nand_20_out, xor_6_out, nand_19_out);
  not not_9 (not_9_out, D5);
  assign driver_5_out = SE ? nand_19_out : 1'bz;  // Driver driver_5
  nand nand_21 (nand_21_out, not_9_out, and_2_out);
  nand nand_22 (nand_22_out, and_2_out, D5);
  xor xor_7 (xor_7_out, xor_1_out, nand_21_out);
  nand nand_23 (nand_23_out, nand_22_out, nand_24_out);
  nand nand_24 (nand_24_out, xor_7_out, nand_23_out);
  not not_10 (not_10_out, D6);
  assign driver_6_out = SE ? nand_23_out : 1'bz;  // Driver driver_6
  nand nand_25 (nand_25_out, not_10_out, and_2_out);
  nand nand_26 (nand_26_out, and_2_out, D6);
  xor xor_8 (xor_8_out, xor_1_out, nand_25_out);
  nand nand_27 (nand_27_out, nand_26_out, nand_28_out);
  nand nand_28 (nand_28_out, xor_8_out, nand_27_out);
  assign driver_7_out = SE ? nand_27_out : 1'bz;  // Driver driver_7
  not not_11 (not_11_out, D7);
  nand nand_29 (nand_29_out, not_11_out, and_2_out);
  nand nand_30 (nand_30_out, and_2_out, D7);
  xor xor_9 (xor_9_out, xor_1_out, nand_29_out);
  nand nand_31 (nand_31_out, nand_30_out, nand_32_out);
  nand nand_32 (nand_32_out, xor_9_out, nand_31_out);
  assign driver_8_out = SE ? nand_31_out : 1'bz;  // Driver driver_8
endmodule
