// Digital circuit Processor Simplified.dig as structural Verilog
module Processor_Simplified (
  input  in_1
);

  wire ALUOp, ALUScr, and_1_out, Branch, controle_ula_simplified_1_p3, Jump, MemRead, MemToReg, MemWrite,
       not_1_out, or_1_out, RegDst, RegWrite, Zero;
  wire [2:0] multiplexer_2_out, OpCode, rs, rt;
  wire [2:2] rd;
  wire [7:0] add_1_s, Address_imm, alu__arithmetic_logic_unit__simplified_1_p5, multiplexer_1_out,
       multiplexer_3_out, multiplexer_4_out, ramdualport_1_d, register_1_q, registerfile_1_da,
       registerfile_1_db;

  Register #(.Bits(8)) register_1 (.D(multiplexer_1_out), .C(in_1), .en(1'b1), .Q(register_1_q));
  Add #(.Bits(8)) add_1 (.a(8'h1), .b(register_1_q), .c_i(1'b0), .s(add_1_s));  // open: c_o
  // Probe on register_1_q
  ROM #(.AddrBits(8), .Bits(18)) rom_1 (.A(register_1_q), .sel(1'b1), .D({OpCode, rs, rt, rd[2], Address_imm}));
  // Probe on Address_imm
  // Probe on Address_imm[2:0]
  // Probe on OpCode
  Multiplexer #(.Bits(8)) multiplexer_1 (.sel(or_1_out), .in_0(add_1_s), .in_1(Address_imm), .out(multiplexer_1_out));
  // Control_Unit_Simplified control_unit_simplified_1: pin names not known; wires that end beside it: OpCode, RegDst, RegWrite, ALUScr, MemWrite, MemRead, MemToReg, Branch, Jump, ALUOp
  or or_1 (or_1_out, Jump, and_1_out);
  and and_1 (and_1_out, Branch, Zero);
  Multiplexer #(.Bits(3)) multiplexer_2 (
    .sel(RegDst), .in_0(rt), .in_1({rd[2], Address_imm[7:6]}), .out(multiplexer_2_out));
  RegisterFile #(.AddrBits(3), .Bits(8)) registerfile_1 (
    .Din(multiplexer_3_out), .we(RegWrite), .Rw(multiplexer_2_out), .C(in_1), .Ra(rs), .Rb(rt),
    .Da(registerfile_1_da), .Db(registerfile_1_db));
  Multiplexer #(.Bits(8)) multiplexer_3 (
    .sel(MemToReg), .in_0(ramdualport_1_d), .in_1(alu__arithmetic_logic_unit__simplified_1_p5),
    .out(multiplexer_3_out));
  Multiplexer #(.Bits(8)) multiplexer_4 (
    .sel(ALUScr), .in_0(registerfile_1_db), .in_1(Address_imm), .out(multiplexer_4_out));
  // Controle_ULA_Simplified controle_ula_simplified_1: pin names not known; wires that end beside it: Address_imm[2:0], ALUOp, controle_ula_simplified_1_p3
  // ALU__Arithmetic_logic_unit__Simplified alu__arithmetic_logic_unit__simplified_1: pin names not known; wires that end beside it: registerfile_1_da, multiplexer_4_out, controle_ula_simplified_1_p3, Address_imm[5:3], alu__arithmetic_logic_unit__simplified_1_p5, Zero
  not not_1 (not_1_out, in_1);
  RAMDualPort #(.AddrBits(8), .Bits(8)) ramdualport_1 (
    .A(alu__arithmetic_logic_unit__simplified_1_p5), .Din(registerfile_1_db), .str(MemWrite), .C(not_1_out),
    .ld(MemRead), .D(ramdualport_1_d));

  // Other names for the same wires on the sheet: func[2:0] = Address_imm[2:0]; shamt[2:0] = Address_imm[5:3];
  //   rd[1:0] = Address_imm[7:6]; CLK = in_1

  // Notes on the sheet:
  //   contents of rom_1 (hex, n*v repeats v):
  //   1,3ffff,2,6
endmodule
