// Digital circuit Registrador 8 bits Parallel.dig as structural Verilog
module Registrador_8_bits_Parallel (
  input  in_1,
  input  in_2,
  input  in_3,
  input  in_4,
  input  in_5,
  input  in_6,
  input  in_7,
  input  in_8,
  input  in_9,
  input  in_10,
  input  in_11,
  input  in_12
);

  wire nand_1_out, nand_2_out, nand_3_out, nand_4_out, nand_5_out, nand_6_out, nand_7_out, nand_8_out,
       nand_9_out, nand_10_out, nand_11_out, nand_12_out, nand_13_out, nand_14_out, nand_15_out, nand_16_out,
       nand_17_out, nand_18_out, nand_19_out, nand_20_out, nand_21_out, nand_22_out, nand_23_out,
       nand_24_out, nand_25_out, nand_26_out, nand_27_out, nand_28_out, nand_29_out, nand_30_out,
       nand_31_out, nand_32_out, nand_33_out, nand_34_out, nand_35_out, nand_36_out, nand_37_out,
       nand_38_out, nand_39_out, nand_40_out, nand_41_out, nand_42_out, nand_43_out, nand_44_out,
       nand_45_out, nand_46_out, nand_47_out, nand_48_out, nand_49_out, nand_50_out, nand_51_out,
       nand_52_out, nand_53_out, nand_54_out, nand_55_out, nand_56_out, nand_57_out, nand_58_out,
       nand_59_out, nand_60_out, nand_61_out, nand_62_out, nand_63_out, nand_64_out, not_1_out, not_2_out,
       not_3_out, not_4_out, not_5_out, not_6_out, not_7_out, not_8_out, not_9_out, not_10_out, not_11_out,
       not_12_out, not_13_out, not_14_out, not_15_out, not_16_out, not_17_out, not_18_out, not_19_out,
       not_20_out, not_21_out, not_22_out, not_23_out, not_24_out;

  not not_1 (not_1_out, in_4);
  nand nand_1 (nand_1_out, in_2, in_1, in_4, in_3);
  nand nand_2 (nand_2_out, in_3, in_1, not_1_out, in_2);
  nand nand_3 (nand_3_out, nand_1_out, nand_4_out);
  nand nand_4 (nand_4_out, nand_2_out, nand_3_out);
  not not_2 (not_2_out, in_3);
  not not_3 (not_3_out, nand_3_out);
  nand nand_5 (nand_5_out, not_2_out, nand_3_out);
  nand nand_6 (nand_6_out, not_2_out, not_3_out);
  nand nand_7 (nand_7_out, nand_5_out, nand_8_out);
  nand nand_8 (nand_8_out, nand_6_out, nand_7_out);
  not not_4 (not_4_out, in_5);
  nand nand_9 (nand_9_out, in_2, in_1, in_5, in_3);
  nand nand_10 (nand_10_out, in_3, in_1, not_4_out, in_2);
  nand nand_11 (nand_11_out, nand_9_out, nand_12_out);
  nand nand_12 (nand_12_out, nand_10_out, nand_11_out);
  not not_5 (not_5_out, in_3);
  not not_6 (not_6_out, nand_11_out);
  nand nand_13 (nand_13_out, not_5_out, nand_11_out);
  nand nand_14 (nand_14_out, not_5_out, not_6_out);
  nand nand_15 (nand_15_out, nand_13_out, nand_16_out);
  nand nand_16 (nand_16_out, nand_14_out, nand_15_out);
  not not_7 (not_7_out, in_6);
  nand nand_17 (nand_17_out, in_2, in_1, in_6, in_3);
  nand nand_18 (nand_18_out, in_3, in_1, not_7_out, in_2);
  nand nand_19 (nand_19_out, nand_17_out, nand_20_out);
  nand nand_20 (nand_20_out, nand_18_out, nand_19_out);
  not not_8 (not_8_out, in_3);
  not not_9 (not_9_out, nand_19_out);
  nand nand_21 (nand_21_out, not_8_out, nand_19_out);
  nand nand_22 (nand_22_out, not_8_out, not_9_out);
  nand nand_23 (nand_23_out, nand_21_out, nand_24_out);
  nand nand_24 (nand_24_out, nand_22_out, nand_23_out);
  not not_10 (not_10_out, in_7);
  nand nand_25 (nand_25_out, in_2, in_1, in_7, in_3);
  nand nand_26 (nand_26_out, in_3, in_1, not_10_out, in_2);
  nand nand_27 (nand_27_out, nand_25_out, nand_28_out);
  nand nand_28 (nand_28_out, nand_26_out, nand_27_out);
  not not_11 (not_11_out, in_3);
  not not_12 (not_12_out, nand_27_out);
  nand nand_29 (nand_29_out, not_11_out, nand_27_out);
  nand nand_30 (nand_30_out, not_11_out, not_12_out);
  nand nand_31 (nand_31_out, nand_29_out, nand_32_out);
  nand nand_32 (nand_32_out, nand_30_out, nand_31_out);
  not not_13 (not_13_out, in_8);
  nand nand_33 (nand_33_out, in_2, in_1, in_8, in_3);
  nand nand_34 (nand_34_out, in_3, in_1, not_13_out, in_2);
  nand nand_35 (nand_35_out, nand_33_out, nand_36_out);
  nand nand_36 (nand_36_out, nand_34_out, nand_35_out);
  not not_14 (not_14_out, in_3);
  not not_15 (not_15_out, nand_35_out);
  nand nand_37 (nand_37_out, not_14_out, nand_35_out);
  nand nand_38 (nand_38_out, not_14_out, not_15_out);
  nand nand_39 (nand_39_out, nand_37_out, nand_40_out);
  nand nand_40 (nand_40_out, nand_38_out, nand_39_out);
  not not_16 (not_16_out, in_9);
  nand nand_41 (nand_41_out, in_2, in_1, in_9, in_3);
  nand nand_42 (nand_42_out, in_3, in_1, not_16_out, in_2);
  nand nand_43 (nand_43_out, nand_41_out, nand_44_out);
  nand nand_44 (nand_44_out, nand_42_out, nand_43_out);
  not not_17 (not_17_out, in_3);
  not not_18 (not_18_out, nand_43_out);
  nand nand_45 (nand_45_out, not_17_out, nand_43_out);
  nand nand_46 (nand_46_out, not_17_out, not_18_out);
  nand nand_47 (nand_47_out, nand_45_out, nand_48_out);
  nand nand_48 (nand_48_out, nand_46_out, nand_47_out);
  not not_19 (not_19_out, in_10);
  nand nand_49 (nand_49_out, in_2, in_1, in_10, in_3);
  nand nand_50 (nand_50_out, in_3, in_1, not_19_out, in_2);
  nand nand_51 (nand_51_out, nand_49_out, nand_52_out);
  nand nand_52 (nand_52_out, nand_50_out, nand_51_out);
  not not_20 (not_20_out, in_3);
  not not_21 (not_21_out, nand_51_out);
  nand nand_53 (nand_53_out, not_20_out, nand_51_out);
  nand nand_54 (nand_54_out, not_20_out, not_21_out);
  nand nand_55 (nand_55_out, nand_53_out, nand_56_out);
  nand nand_56 (nand_56_out, nand_54_out, nand_55_out);
  not not_22 (not_22_out, in_11);
  nand nand_57 (nand_57_out, in_2, in_1, in_11, in_3);
  nand nand_58 (nand_58_out, in_3, in_1, not_22_out, in_2);
  nand nand_59 (nand_59_out, nand_57_out, nand_60_out);
  nand nand_60 (nand_60_out, nand_58_out, nand_59_out);
  not not_23 (not_23_out, in_3);
  not not_24 (not_24_out, nand_59_out);
  nand nand_61 (nand_61_out, not_23_out, nand_59_out);
  nand nand_62 (nand_62_out, not_23_out, not_24_out);
  nand nand_63 (nand_63_out, nand_61_out, nand_64_out);
  nand nand_64 (nand_64_out, nand_62_out, nand_63_out);
endmodule
