// Digital circuit Tester ALU.dig as structural Verilog
module Tester_ALU (
  input  [7:0] in_1,
  input  [7:0] in_2,
  input  in_3,
  input  in_4,
  input  in_5,
  input  in_6,
  input  in_7,
  input  in_8
);

  wire alu__arithmetic_logic_unit_1_cout;
  wire [7:0] alu__arithmetic_logic_unit_1_s7;

  ALU__Arithmetic_logic_unit alu__arithmetic_logic_unit_1 (
    .A0(in_1[0]), .A1(in_1[1]), .A2(in_1[2]), .A3(in_1[3]), .A4(in_1[4]), .A5(in_1[5]), .A6(in_1[6]),
    .A7(in_1[7]), .B0(in_2[0]), .B1(in_2[1]), .B2(in_2[2]), .B3(in_2[3]), .B4(in_2[4]), .B5(in_2[5]),
    .B6(in_2[6]), .B7(in_2[7]), .OP0(in_3), .OP1(in_4), .OP2(in_5), .OP3(in_6), .B(in_7), .Cin(in_8),
    .S0(alu__arithmetic_logic_unit_1_s7[0]), .S1(alu__arithmetic_logic_unit_1_s7[1]),
    .S2(alu__arithmetic_logic_unit_1_s7[2]), .S3(alu__arithmetic_logic_unit_1_s7[3]),
    .S4(alu__arithmetic_logic_unit_1_s7[4]), .S5(alu__arithmetic_logic_unit_1_s7[5]),
    .S6(alu__arithmetic_logic_unit_1_s7[6]), .S7(alu__arithmetic_logic_unit_1_s7[7]),
    .Cout(alu__arithmetic_logic_unit_1_cout));
  // Probe on alu__arithmetic_logic_unit_1_s7
  LED led_1 (.in(alu__arithmetic_logic_unit_1_cout));
endmodule
