// Digital circuit test register file.dig as structural Verilog
module test_register_file (
  input  [7:0] Din,
  input  We,
  input  [2:0] RW,
  input  C,
  input  [2:0] Ra,
  input  [2:0] Rb
);

  wire [7:0] registerfile_1_da, registerfile_1_db, undriven, undriven_2;

  RegisterFile #(.AddrBits(3), .Bits(8)) registerfile_1 (
    .Din(Din), .we(We), .Rw(RW), .C(C), .Ra(Ra), .Rb(Rb), .Da(registerfile_1_da), .Db(registerfile_1_db));
  RegisterFile registerfile_2 (.D0(Din[0]));
  // Probe on undriven
  // Probe on registerfile_1_da
  // Probe on undriven_2
  // Probe on registerfile_1_db
endmodule
