// Digital circuit teste.dig as structural Verilog
module teste (
  input  C,
  input  CE
);

  wire and_1_out, counter_2_out, \memória_8_bits_256_bytes_1_p5 , \memória_8_bits_256_bytes_1_p6 ,
       \memória_8_bits_256_bytes_1_p7 , \memória_8_bits_256_bytes_1_p8 , \memória_8_bits_256_bytes_1_p9 ,
       \memória_8_bits_256_bytes_1_p10 , \memória_8_bits_256_bytes_1_p11 , \memória_8_bits_256_bytes_1_p12 ;
  wire [7:0] counter_6_out, eepromdualport_1_d, not_1_out;

  and and_1 (and_1_out, C, CE);
  Counter counter_1 (.en(1'b1), .C(and_1_out), .clr(1'b0), .out(counter_6_out[0]));  // open: ovf
  Counter counter_2 (.en(1'b1), .C(counter_6_out[0]), .clr(1'b0), .out(counter_2_out));  // open: ovf
  Counter counter_3 (.en(1'b1), .C(counter_2_out), .clr(1'b0), .out(counter_6_out[1]));  // open: ovf
  Counter counter_4 (.en(1'b1), .C(counter_6_out[1]), .clr(1'b0), .out(counter_6_out[2]));  // open: ovf
  Counter counter_5 (.en(1'b1), .C(counter_6_out[2]), .clr(1'b0), .out(counter_6_out[3]));  // open: ovf
  Counter counter_6 (.en(1'b1), .C(counter_6_out[3]), .clr(1'b0), .out(counter_6_out[4]));  // open: ovf
  Counter counter_7 (.en(1'b1), .C(counter_6_out[4]), .clr(1'b0), .out(counter_6_out[5]));  // open: ovf
  Counter counter_8 (.en(1'b1), .C(counter_6_out[5]), .clr(1'b0), .out(counter_6_out[6]));  // open: ovf
  assign not_1_out = ~counter_6_out;  // Not not_1, 8 bits wide
  Counter counter_9 (.en(1'b1), .C(counter_6_out[6]), .clr(1'b0), .out(counter_6_out[7]));  // open: ovf
  LED led_1 (.in(eepromdualport_1_d[7]));
  LED led_2 (.in(eepromdualport_1_d[6]));
  LED led_3 (.in(eepromdualport_1_d[5]));
  LED led_4 (.in(eepromdualport_1_d[4]));
  LED led_5 (.in(eepromdualport_1_d[3]));
  EEPROMDualPort #(.AddrBits(8), .Bits(8)) eepromdualport_1 (
    .A(not_1_out), .Din({8{1'b1}}), .str(1'b0), .C(1'b0), .ld(1'b1), .D(eepromdualport_1_d));
  LED led_6 (.in(eepromdualport_1_d[2]));
  LED led_7 (.in(eepromdualport_1_d[1]));
  LED led_8 (.in(eepromdualport_1_d[0]));
  // Memória_8_bits_256_Bytes memória_8_bits_256_bytes_1: pin names not known; wires that end beside it: CE, and_1_out, 1'b0, 1'b0, \memória_8_bits_256_bytes_1_p5 , \memória_8_bits_256_bytes_1_p6 , \memória_8_bits_256_bytes_1_p7 , \memória_8_bits_256_bytes_1_p8 , \memória_8_bits_256_bytes_1_p9 , \memória_8_bits_256_bytes_1_p10 , \memória_8_bits_256_bytes_1_p11 , \memória_8_bits_256_bytes_1_p12 
  LED led_9 (.in(\memória_8_bits_256_bytes_1_p11 ));
  LED led_10 (.in(\memória_8_bits_256_bytes_1_p12 ));
  LED led_11 (.in(\memória_8_bits_256_bytes_1_p7 ));
  LED led_12 (.in(\memória_8_bits_256_bytes_1_p8 ));
  LED led_13 (.in(\memória_8_bits_256_bytes_1_p9 ));
  LED led_14 (.in(\memória_8_bits_256_bytes_1_p10 ));
  LED led_15 (.in(\memória_8_bits_256_bytes_1_p5 ));
  LED led_16 (.in(\memória_8_bits_256_bytes_1_p6 ));

  // Notes on the sheet:
  //   C: Hz: 50
  //   contents of eepromdualport_1 (hex, n*v repeats v):
  //   a98670,f69b5,0,98bd91,a7dd0c,a98ac7,9009,a7dd0c,9009,9009,9009
  //   ,a98ac7,9009,9009,a7dd0c,a7dd0c,a7dd0c,9009,a98ac7,9009,f69b5
  //   ,a7dd0c,9009,0,a98670,f69b5,0,98bd91,9009,0,98bd91,9009,9009,f69b5
  //   ,a7dd0c,40249,f69b5,0,98bd91,40249,a7dd0c,40249,9009,f69b5,a7dd0c,a7dd0c
  //   ,40249,a98ac7,a98ac7,a98ac7,0,9009,0,98bd91,40249,9009,a98670
  //   ,f69b5,0,98bd91,40249,a98ac7,40249,9009,40249,a98ac7,a98ac7,f69b5
  //   ,a98670,f69b5,0,98bd91,0,a7dd0c,a98ac7,0,a98670,f69b5,0,98bd91
  //   ,a98ac7,0,9009,f69b5,a98ac7,9009,f69b5,a98ac7,9009,a98ac7,0,a7dd0c
  //   ,9009,f69b5,a7dd0c,a98ac7,f69b5,a98ac7,0,98bd91,a98ac7,a98ac7
  //   ,0,a98ac7,0,a98ac7,9009,a98ac7,9009,a7dd0c,a98ac7,9009,a98670
  //   ,f69b5,0,98bd91,a7dd0c,a98ac7,9009,a7dd0c,9009,9009,9009,a98ac7
  //   ,9009,9009,a7dd0c,a7dd0c,a7dd0c,9009,a98ac7,9009,f69b5,a7dd0c
  //   ,9009,0,a98670,f69b5,0,98bd91,9009,0,98bd91,9009,9009,f69b5,a7dd0c
  //   ,40249,f69b5,0,98bd91,40249,a7dd0c,40249,9009,f69b5,a7dd0c,a7dd0c
  //   ,40249,a98ac7,a98ac7,a98ac7,0,9009,0,98bd91,40249,9009,a98670
  //   ,f69b5,0,98bd91,40249,a98ac7,40249,9009,40249,a98ac7,a98ac7,f69b5
  //   ,a98670,f69b5,0,98bd91,0,a7dd0c,a98ac7,0,a98670,f69b5,0,98bd91
  //   ,a98ac7,0,9009,f69b5,a98ac7,9009,f69b5,a98ac7,9009,a98ac7,0,a7dd0c
  //   ,9009,f69b5,a7dd0c,a98ac7,f69b5,a98ac7,0,98bd91,a98ac7,a98ac7
  //   ,0,a98ac7,0,a98ac7,9009,a98ac7,9009,a7dd0c,a98ac7,9009,a98670
  //   ,f69b5,0,98bd91,a7dd0c,a98ac7,9009,a7dd0c,9009,9009,9009,a98ac7
  //   ,9009,9009,a7dd0c,a7dd0c,a7dd0c,9009,a98ac7,9009,f69b5,a7dd0c
  //   ,9009,0,a98670,f69b5,0,98bd91,9009,0,98bd91,9009
endmodule
