// Digital circuit teste2.dig as structural Verilog
module teste2 (
  input  in_1,
  input  in_2,
  input  clk,
  input  in_4,
  input  [2:0] in_5
);

  wire demultiplexer_1_out_4, demultiplexer_1_out_5, demultiplexer_1_out_6, demultiplexer_1_out_7, not_1_out,
       register_8_bits_parallel_1_p2, register_8_bits_parallel_2_p2, register_8_bits_parallel_3_p2,
       register_8_bits_parallel_4_p2;
  wire [2:0] driver_1_out;
  wire [7:0] \memória_8_bits_256_bytes_1_p1 , undriven;
  wire [19:0] memory_loader_1_s;

  Memory_Loader memory_loader_1 (.C(clk), .CE(in_1), .SE(in_2), .S(memory_loader_1_s));
  // Memória_8_bits_256_Bytes memória_8_bits_256_bytes_1: pin names not known; wires that end beside it: \memória_8_bits_256_bytes_1_p1 [0], \memória_8_bits_256_bytes_1_p1 [1], \memória_8_bits_256_bytes_1_p1 [2], \memória_8_bits_256_bytes_1_p1 [3], \memória_8_bits_256_bytes_1_p1 [4], \memória_8_bits_256_bytes_1_p1 [5], \memória_8_bits_256_bytes_1_p1 [6], \memória_8_bits_256_bytes_1_p1 [7]
  LED led_1 (.in(\memória_8_bits_256_bytes_1_p1 [7]));
  LED led_2 (.in(\memória_8_bits_256_bytes_1_p1 [6]));
  LED led_3 (.in(\memória_8_bits_256_bytes_1_p1 [5]));
  LED led_4 (.in(\memória_8_bits_256_bytes_1_p1 [4]));
  LED led_5 (.in(\memória_8_bits_256_bytes_1_p1 [3]));
  LED led_6 (.in(\memória_8_bits_256_bytes_1_p1 [2]));
  LED led_7 (.in(\memória_8_bits_256_bytes_1_p1 [1]));
  LED led_8 (.in(\memória_8_bits_256_bytes_1_p1 [0]));
  // Register_8_bits_Parallel register_8_bits_parallel_1: pin names not known; wires that end beside it: memory_loader_1_s[9], register_8_bits_parallel_1_p2, register_8_bits_parallel_1_p2, 1'b0
  // Register_8_bits_Parallel register_8_bits_parallel_2: pin names not known; wires that end beside it: memory_loader_1_s[9], register_8_bits_parallel_2_p2, register_8_bits_parallel_2_p2, 1'b0
  // Register_8_bits_Parallel register_8_bits_parallel_3: pin names not known; wires that end beside it: memory_loader_1_s[9], register_8_bits_parallel_3_p2, register_8_bits_parallel_3_p2, 1'b0
  assign driver_1_out = in_4 ? memory_loader_1_s[2:0] : 3'bz;  // Driver driver_1
  not not_1 (not_1_out, in_4);
  assign driver_1_out = not_1_out ? in_5 : 3'bz;  // Driver driver_2
  // Register_8_bits_Parallel register_8_bits_parallel_4: pin names not known; wires that end beside it: memory_loader_1_s[9], register_8_bits_parallel_4_p2, register_8_bits_parallel_4_p2, 1'b0
  Demultiplexer #(.Selector_Bits(3)) demultiplexer_1 (
    .sel(driver_1_out), .in(1'b1), .out_0(register_8_bits_parallel_1_p2),
    .out_1(register_8_bits_parallel_2_p2), .out_2(register_8_bits_parallel_3_p2),
    .out_3(register_8_bits_parallel_4_p2), .out_4(demultiplexer_1_out_4), .out_5(demultiplexer_1_out_5),
    .out_6(demultiplexer_1_out_6), .out_7(demultiplexer_1_out_7));
  // Register_8_bits_Parallel register_8_bits_parallel_5: pin names not known; wires that end beside it: memory_loader_1_s[9], demultiplexer_1_out_4, demultiplexer_1_out_4, 1'b0
  // Register_8_bits_Parallel register_8_bits_parallel_6: pin names not known; wires that end beside it: memory_loader_1_s[9], demultiplexer_1_out_5, demultiplexer_1_out_5, 1'b0
  LED led_9 (.in(undriven[7]));
  LED led_10 (.in(undriven[6]));
  LED led_11 (.in(undriven[2]));
  LED led_12 (.in(undriven[3]));
  LED led_13 (.in(undriven[4]));
  LED led_14 (.in(undriven[5]));
  LED led_15 (.in(undriven[1]));
  LED led_16 (.in(undriven[0]));
  // Register_8_bits_Parallel register_8_bits_parallel_7: pin names not known; wires that end beside it: memory_loader_1_s[9], demultiplexer_1_out_6, demultiplexer_1_out_6, 1'b0
  // Register_8_bits_Parallel register_8_bits_parallel_8: pin names not known; wires that end beside it: memory_loader_1_s[9], demultiplexer_1_out_7, demultiplexer_1_out_7, 1'b0

  // Notes on the sheet:
  //   clk: Hz: 50
endmodule
