// Digital circuit ALU (Arithmetic logic unit).dig as structural Verilog
module ALU__Arithmetic_logic_unit (
  input  in_1,
  input  in_2,
  input  in_3,
  input  in_4,
  input  in_5,
  input  in_6,
  input  in_7,
  input  in_8,
  input  in_9,
  input  in_10,
  input  in_11,
  input  in_12,
  input  in_13,
  input  in_14,
  input  in_15,
  input  in_16,
  input  in_17,
  input  in_18,
  input  in_19,
  input  in_20,
  input  in_21
);

  wire and_1_out, and_2_out, and_3_out, and_4_out, and_5_out, and_6_out, and_7_out, and_8_out, and_9_out,
       and_10_out, and_11_out, and_12_out, and_13_out, and_14_out, and_15_out, and_16_out, and_17_out,
       and_18_out, and_19_out, and_20_out, and_21_out, and_22_out, and_23_out, and_24_out, and_25_out,
       and_26_out, and_27_out, and_28_out, and_29_out, and_30_out, and_31_out, and_32_out, and_33_out,
       and_34_out, and_35_out, and_36_out, and_37_out, and_38_out, and_39_out, and_40_out, and_41_out,
       and_42_out, and_43_out, and_44_out, and_45_out, and_46_out, and_47_out, and_48_out, and_49_out,
       and_50_out, and_51_out, and_52_out, and_53_out, and_54_out, and_55_out, and_56_out, and_57_out,
       and_58_out, and_59_out, and_60_out, and_61_out, and_62_out, and_63_out, and_64_out, and_65_out,
       and_66_out, and_67_out, and_68_out, and_69_out, and_70_out, and_71_out, and_72_out, and_73_out,
       and_74_out, and_75_out, and_76_out, and_77_out, and_78_out, and_79_out, and_80_out, and_81_out,
       and_82_out, and_83_out, and_84_out, and_85_out, and_86_out, and_87_out, and_88_out, and_89_out,
       and_90_out, and_91_out, and_92_out, and_93_out, and_94_out, and_95_out, and_96_out, and_97_out,
       and_98_out, and_99_out, and_100_out, and_101_out, and_102_out, and_103_out, and_104_out, and_105_out,
       and_106_out, and_107_out, and_108_out, and_109_out, and_110_out, and_111_out, and_112_out,
       and_113_out, and_114_out, and_115_out, and_116_out, and_117_out, and_118_out, and_119_out,
       and_120_out, and_121_out, and_122_out, and_123_out, and_124_out, and_125_out, and_126_out,
       and_127_out, and_128_out, and_129_out, and_130_out, and_131_out, and_132_out, and_133_out,
       and_134_out, and_135_out, and_136_out, and_137_out, and_138_out, and_139_out, and_140_out,
       and_141_out, and_142_out, and_143_out, and_144_out, and_145_out, and_146_out, and_147_out,
       and_148_out, and_149_out, and_150_out, and_151_out, and_152_out, and_153_out, and_154_out,
       and_155_out, and_156_out, and_157_out, and_158_out, and_159_out, and_160_out, and_161_out,
       and_162_out, and_163_out, and_164_out, and_165_out, and_166_out, and_167_out, and_168_out,
       and_169_out, and_170_out, and_171_out, and_172_out, and_173_out, and_174_out, and_175_out,
       and_176_out, and_177_out, and_178_out, and_179_out, and_180_out, and_181_out, and_182_out,
       and_183_out, and_184_out, and_185_out, and_186_out, and_187_out, and_188_out, and_189_out,
       and_190_out, and_191_out, and_192_out, and_193_out, and_194_out, and_195_out, and_196_out,
       and_197_out, and_198_out, and_199_out, and_200_out, and_201_out, and_202_out, and_203_out,
       and_204_out, and_205_out, and_206_out, and_207_out, and_208_out, and_209_out, and_210_out,
       and_211_out, and_212_out, and_213_out, and_214_out, and_215_out, and_216_out, and_217_out,
       and_218_out, and_219_out, and_220_out, and_221_out, and_222_out, and_223_out, and_224_out,
       and_225_out, and_226_out, and_227_out, and_228_out, and_229_out, and_230_out, and_231_out,
       and_232_out, and_233_out, and_234_out, and_235_out, and_236_out, and_237_out, and_238_out,
       and_239_out, and_240_out, and_241_out, and_242_out, and_243_out, and_244_out, and_245_out,
       and_246_out, and_247_out, and_248_out, and_249_out, and_250_out, and_251_out, and_252_out,
       and_253_out, and_254_out, and_255_out, and_256_out, and_257_out, and_258_out, and_259_out,
       and_260_out, and_261_out, and_262_out, and_263_out, and_264_out, and_265_out, and_266_out,
       and_267_out, and_268_out, and_269_out, and_270_out, and_271_out, and_272_out, and_273_out,
       and_274_out, and_275_out, and_276_out, and_277_out, and_278_out, and_279_out, and_280_out,
       and_281_out, and_282_out, and_283_out, and_284_out, and_285_out, and_286_out, and_287_out,
       and_288_out, and_289_out, and_290_out, and_291_out, and_292_out, and_293_out, and_294_out,
       and_295_out, and_296_out, and_297_out, and_298_out, and_299_out, and_300_out, and_301_out,
       and_302_out, and_303_out, and_304_out, and_305_out, and_306_out, and_307_out, and_308_out,
       and_309_out, and_310_out, and_311_out, and_312_out, nand_1_out, nand_2_out, nand_3_out, nand_4_out,
       nand_5_out, nand_6_out, nand_7_out, nand_8_out, nor_1_out, nor_2_out, nor_3_out, nor_4_out, nor_5_out,
       nor_6_out, nor_7_out, nor_8_out, not_1_out, not_2_out, not_3_out, not_4_out, or_1_out, or_2_out,
       or_3_out, or_4_out, or_5_out, or_6_out, or_7_out, or_8_out, or_9_out, or_10_out, or_11_out, or_12_out,
       or_13_out, or_14_out, or_15_out, or_16_out, or_17_out, or_18_out, or_19_out, or_20_out, or_21_out,
       or_22_out, or_23_out, or_24_out, or_25_out, or_26_out, or_27_out, or_28_out, or_29_out, or_30_out,
       or_31_out, or_32_out, or_33_out, or_34_out, or_35_out, or_36_out, or_37_out, or_38_out, or_39_out,
       or_40_out, or_41_out, or_42_out, or_43_out, or_44_out, or_45_out, or_46_out, or_47_out, or_48_out,
       or_49_out, or_50_out, or_51_out, or_52_out, or_53_out, or_54_out, or_55_out, or_56_out, or_57_out,
       or_58_out, or_59_out, or_60_out, or_61_out, or_62_out, or_63_out, or_64_out, or_65_out, or_66_out,
       or_67_out, or_68_out, or_69_out, or_70_out, or_71_out, or_72_out, or_73_out, or_74_out, or_75_out,
       or_76_out, or_77_out, or_78_out, or_79_out, or_80_out, or_81_out, or_82_out, or_83_out, or_84_out,
       or_85_out, or_86_out, or_87_out, or_88_out, or_89_out, or_90_out, or_91_out, or_92_out, or_93_out,
       or_94_out, or_95_out, or_96_out, or_97_out, or_98_out, or_99_out, or_100_out, or_101_out, or_102_out,
       or_103_out, xnor_1_out, xnor_2_out, xnor_3_out, xnor_4_out, xnor_5_out, xnor_6_out, xnor_7_out,
       xnor_8_out, xor_1_out, xor_2_out, xor_3_out, xor_4_out, xor_5_out, xor_6_out, xor_7_out, xor_8_out,
       xor_9_out, xor_10_out, xor_11_out, xor_12_out, xor_13_out, xor_14_out, xor_15_out, xor_16_out,
       xor_17_out, xor_18_out, xor_19_out, xor_20_out, xor_21_out, xor_22_out, xor_23_out, xor_24_out,
       xor_25_out, xor_26_out, xor_27_out, xor_28_out, xor_29_out, xor_30_out, xor_31_out, xor_32_out,
       xor_33_out, xor_34_out, xor_35_out, xor_36_out, xor_37_out, xor_38_out, xor_39_out, xor_40_out,
       xor_41_out, xor_42_out, xor_43_out, xor_44_out, xor_45_out, xor_46_out, xor_47_out, xor_48_out,
       xor_49_out, xor_50_out, xor_51_out, xor_52_out, xor_53_out, xor_54_out, xor_55_out, xor_56_out,
       xor_57_out, xor_58_out, xor_59_out, xor_60_out, xor_61_out, xor_62_out, xor_63_out, xor_64_out,
       xor_65_out, xor_66_out, xor_67_out, xor_68_out, xor_69_out, xor_70_out, xor_71_out, xor_72_out,
       xor_73_out, xor_74_out, xor_75_out, xor_76_out, xor_77_out, xor_78_out, xor_79_out, xor_80_out,
       xor_81_out, xor_82_out, xor_83_out, xor_84_out, xor_85_out, xor_86_out, xor_87_out, xor_88_out,
       xor_89_out, xor_90_out, xor_91_out, xor_92_out, xor_93_out, xor_94_out, xor_95_out, xor_96_out,
       xor_97_out, xor_98_out, xor_99_out, xor_100_out, xor_101_out, xor_102_out, xor_103_out, xor_104_out,
       xor_105_out, xor_106_out, xor_107_out, xor_108_out, xor_109_out, xor_110_out, xor_111_out,
       xor_112_out, xor_113_out, xor_114_out, xor_115_out, xor_116_out, xor_117_out, xor_118_out,
       xor_119_out, xor_120_out, xor_121_out, xor_122_out, xor_123_out, xor_124_out, xor_125_out,
       xor_126_out, xor_127_out, xor_128_out;

  not not_1 (not_1_out, in_21);
  not not_2 (not_2_out, in_20);
  not not_3 (not_3_out, in_19);
  not not_4 (not_4_out, in_18);
  and and_1 (and_1_out, not_1_out, not_2_out, not_3_out, not_4_out, xor_8_out);
  and and_2 (and_2_out, not_1_out, not_2_out, not_3_out, in_18, or_39_out);
  or or_1 (or_1_out, and_4_out, and_3_out, and_2_out, and_1_out);
  and and_3 (and_3_out, not_1_out, not_2_out, in_19, not_4_out, and_107_out);
  and and_4 (and_4_out, not_1_out, not_2_out, in_19, in_18, xor_16_out);
  and and_5 (and_5_out, not_1_out, in_20, not_3_out, not_4_out, xor_24_out);
  and and_6 (and_6_out, not_1_out, in_20, not_3_out, in_18, xnor_8_out);
  or or_2 (or_2_out, and_8_out, and_7_out, and_6_out, and_5_out);
  and and_7 (and_7_out, not_1_out, in_20, in_19, not_4_out, nor_8_out);
  and and_8 (and_8_out, not_1_out, in_20, in_19, in_18, nand_8_out);
  and and_9 (and_9_out, in_21, not_2_out, not_3_out, not_4_out, xor_114_out);
  or or_3 (or_3_out, or_5_out, or_4_out, or_2_out, or_1_out);
  and and_10 (and_10_out, in_21, not_2_out, not_3_out, in_18, 1'b0);
  or or_4 (or_4_out, and_12_out, and_11_out, and_10_out, and_9_out);
  and and_11 (and_11_out, in_21, not_2_out, in_19, not_4_out, 1'b0);
  and and_12 (and_12_out, in_21, not_2_out, in_19, in_18, 1'b0);
  and and_13 (and_13_out, in_21, in_20, not_3_out, not_4_out, 1'b0);
  and and_14 (and_14_out, in_21, in_20, not_3_out, in_18, 1'b0);
  or or_5 (or_5_out, and_16_out, and_15_out, and_14_out, and_13_out);
  and and_15 (and_15_out, in_21, in_20, in_19, not_4_out, 1'b0);
  and and_16 (and_16_out, in_21, in_20, in_19, in_18, 1'b0);
  and and_17 (and_17_out, not_1_out, not_2_out, not_3_out, not_4_out, xor_7_out);
  and and_18 (and_18_out, not_1_out, not_2_out, not_3_out, in_18, or_38_out);
  or or_6 (or_6_out, and_20_out, and_19_out, and_18_out, and_17_out);
  and and_19 (and_19_out, not_1_out, not_2_out, in_19, not_4_out, and_106_out);
  and and_20 (and_20_out, not_1_out, not_2_out, in_19, in_18, xor_15_out);
  and and_21 (and_21_out, not_1_out, in_20, not_3_out, not_4_out, xor_23_out);
  and and_22 (and_22_out, not_1_out, in_20, not_3_out, in_18, xnor_7_out);
  or or_7 (or_7_out, and_24_out, and_23_out, and_22_out, and_21_out);
  and and_23 (and_23_out, not_1_out, in_20, in_19, not_4_out, nor_7_out);
  and and_24 (and_24_out, not_1_out, in_20, in_19, in_18, nand_7_out);
  and and_25 (and_25_out, in_21, not_2_out, not_3_out, not_4_out, xor_99_out);
  or or_8 (or_8_out, or_10_out, or_9_out, or_7_out, or_6_out);
  and and_26 (and_26_out, in_21, not_2_out, not_3_out, in_18, 1'b0);
  or or_9 (or_9_out, and_28_out, and_27_out, and_26_out, and_25_out);
  and and_27 (and_27_out, in_21, not_2_out, in_19, not_4_out, 1'b0);
  and and_28 (and_28_out, in_21, not_2_out, in_19, in_18, 1'b0);
  and and_29 (and_29_out, in_21, in_20, not_3_out, not_4_out, 1'b0);
  and and_30 (and_30_out, in_21, in_20, not_3_out, in_18, 1'b0);
  or or_10 (or_10_out, and_32_out, and_31_out, and_30_out, and_29_out);
  and and_31 (and_31_out, in_21, in_20, in_19, not_4_out, 1'b0);
  and and_32 (and_32_out, in_21, in_20, in_19, in_18, 1'b0);
  and and_33 (and_33_out, not_1_out, not_2_out, not_3_out, not_4_out, xor_6_out);
  and and_34 (and_34_out, not_1_out, not_2_out, not_3_out, in_18, or_37_out);
  or or_11 (or_11_out, and_36_out, and_35_out, and_34_out, and_33_out);
  and and_35 (and_35_out, not_1_out, not_2_out, in_19, not_4_out, and_105_out);
  and and_36 (and_36_out, not_1_out, not_2_out, in_19, in_18, xor_14_out);
  and and_37 (and_37_out, not_1_out, in_20, not_3_out, not_4_out, xor_22_out);
  and and_38 (and_38_out, not_1_out, in_20, not_3_out, in_18, xnor_6_out);
  or or_12 (or_12_out, and_40_out, and_39_out, and_38_out, and_37_out);
  and and_39 (and_39_out, not_1_out, in_20, in_19, not_4_out, nor_6_out);
  and and_40 (and_40_out, not_1_out, in_20, in_19, in_18, nand_6_out);
  and and_41 (and_41_out, in_21, not_2_out, not_3_out, not_4_out, xor_84_out);
  or or_13 (or_13_out, or_15_out, or_14_out, or_12_out, or_11_out);
  and and_42 (and_42_out, in_21, not_2_out, not_3_out, in_18, 1'b0);
  or or_14 (or_14_out, and_44_out, and_43_out, and_42_out, and_41_out);
  and and_43 (and_43_out, in_21, not_2_out, in_19, not_4_out, 1'b0);
  and and_44 (and_44_out, in_21, not_2_out, in_19, in_18, 1'b0);
  and and_45 (and_45_out, in_21, in_20, not_3_out, not_4_out, 1'b0);
  and and_46 (and_46_out, in_21, in_20, not_3_out, in_18, 1'b0);
  or or_15 (or_15_out, and_48_out, and_47_out, and_46_out, and_45_out);
  and and_47 (and_47_out, in_21, in_20, in_19, not_4_out, 1'b0);
  and and_48 (and_48_out, in_21, in_20, in_19, in_18, 1'b0);
  and and_49 (and_49_out, not_1_out, not_2_out, not_3_out, not_4_out, xor_5_out);
  and and_50 (and_50_out, not_1_out, not_2_out, not_3_out, in_18, or_36_out);
  or or_16 (or_16_out, and_52_out, and_51_out, and_50_out, and_49_out);
  and and_51 (and_51_out, not_1_out, not_2_out, in_19, not_4_out, and_104_out);
  and and_52 (and_52_out, not_1_out, not_2_out, in_19, in_18, xor_13_out);
  and and_53 (and_53_out, not_1_out, in_20, not_3_out, not_4_out, xor_21_out);
  and and_54 (and_54_out, not_1_out, in_20, not_3_out, in_18, xnor_5_out);
  or or_17 (or_17_out, and_56_out, and_55_out, and_54_out, and_53_out);
  and and_55 (and_55_out, not_1_out, in_20, in_19, not_4_out, nor_5_out);
  and and_56 (and_56_out, not_1_out, in_20, in_19, in_18, nand_5_out);
  and and_57 (and_57_out, in_21, not_2_out, not_3_out, not_4_out, xor_69_out);
  or or_18 (or_18_out, or_20_out, or_19_out, or_17_out, or_16_out);
  and and_58 (and_58_out, in_21, not_2_out, not_3_out, in_18, 1'b0);
  or or_19 (or_19_out, and_60_out, and_59_out, and_58_out, and_57_out);
  and and_59 (and_59_out, in_21, not_2_out, in_19, not_4_out, 1'b0);
  and and_60 (and_60_out, in_21, not_2_out, in_19, in_18, 1'b0);
  and and_61 (and_61_out, in_21, in_20, not_3_out, not_4_out, 1'b0);
  and and_62 (and_62_out, in_21, in_20, not_3_out, in_18, 1'b0);
  or or_20 (or_20_out, and_64_out, and_63_out, and_62_out, and_61_out);
  and and_63 (and_63_out, in_21, in_20, in_19, not_4_out, 1'b0);
  and and_64 (and_64_out, in_21, in_20, in_19, in_18, 1'b0);
  and and_65 (and_65_out, not_1_out, not_2_out, not_3_out, not_4_out, xor_4_out);
  and and_66 (and_66_out, not_1_out, not_2_out, not_3_out, in_18, or_35_out);
  or or_21 (or_21_out, and_68_out, and_67_out, and_66_out, and_65_out);
  and and_67 (and_67_out, not_1_out, not_2_out, in_19, not_4_out, and_103_out);
  and and_68 (and_68_out, not_1_out, not_2_out, in_19, in_18, xor_12_out);
  and and_69 (and_69_out, not_1_out, in_20, not_3_out, not_4_out, xor_20_out);
  and and_70 (and_70_out, not_1_out, in_20, not_3_out, in_18, xnor_4_out);
  or or_22 (or_22_out, and_72_out, and_71_out, and_70_out, and_69_out);
  and and_71 (and_71_out, not_1_out, in_20, in_19, not_4_out, nor_4_out);
  and and_72 (and_72_out, not_1_out, in_20, in_19, in_18, nand_4_out);
  and and_73 (and_73_out, in_21, not_2_out, not_3_out, not_4_out, xor_54_out);
  or or_23 (or_23_out, or_25_out, or_24_out, or_22_out, or_21_out);
  and and_74 (and_74_out, in_21, not_2_out, not_3_out, in_18, 1'b0);
  or or_24 (or_24_out, and_76_out, and_75_out, and_74_out, and_73_out);
  and and_75 (and_75_out, in_21, not_2_out, in_19, not_4_out, 1'b0);
  and and_76 (and_76_out, in_21, not_2_out, in_19, in_18, 1'b0);
  and and_77 (and_77_out, in_21, in_20, not_3_out, not_4_out, 1'b0);
  and and_78 (and_78_out, in_21, in_20, not_3_out, in_18, 1'b0);
  or or_25 (or_25_out, and_80_out, and_79_out, and_78_out, and_77_out);
  and and_79 (and_79_out, in_21, in_20, in_19, not_4_out, 1'b0);
  and and_80 (and_80_out, in_21, in_20, in_19, in_18, 1'b0);
  and and_81 (and_81_out, not_1_out, not_2_out, not_3_out, not_4_out, xor_3_out);
  and and_82 (and_82_out, not_1_out, not_2_out, not_3_out, in_18, or_34_out);
  or or_26 (or_26_out, and_84_out, and_83_out, and_82_out, and_81_out);
  and and_83 (and_83_out, not_1_out, not_2_out, in_19, not_4_out, and_102_out);
  and and_84 (and_84_out, not_1_out, not_2_out, in_19, in_18, xor_11_out);
  and and_85 (and_85_out, not_1_out, in_20, not_3_out, not_4_out, xor_19_out);
  and and_86 (and_86_out, not_1_out, in_20, not_3_out, in_18, xnor_3_out);
  or or_27 (or_27_out, and_88_out, and_87_out, and_86_out, and_85_out);
  and and_87 (and_87_out, not_1_out, in_20, in_19, not_4_out, nor_3_out);
  and and_88 (and_88_out, not_1_out, in_20, in_19, in_18, nand_3_out);
  and and_89 (and_89_out, in_21, not_2_out, not_3_out, not_4_out, xor_39_out);
  or or_28 (or_28_out, or_30_out, or_29_out, or_27_out, or_26_out);
  and and_90 (and_90_out, in_21, not_2_out, not_3_out, in_18, 1'b0);
  or or_29 (or_29_out, and_92_out, and_91_out, and_90_out, and_89_out);
  LED led_1 (.in(or_3_out));
  and and_91 (and_91_out, in_21, not_2_out, in_19, not_4_out, 1'b0);
  LED led_2 (.in(or_23_out));
  LED led_3 (.in(or_18_out));
  LED led_4 (.in(or_13_out));
  LED led_5 (.in(or_8_out));
  and and_92 (and_92_out, in_21, not_2_out, in_19, in_18, 1'b0);
  LED led_6 (.in(or_74_out));
  LED led_7 (.in(or_55_out));
  LED led_8 (.in(or_28_out));
  and and_93 (and_93_out, in_21, in_20, not_3_out, not_4_out, 1'b0);
  and and_94 (and_94_out, in_21, in_20, not_3_out, in_18, 1'b0);
  or or_30 (or_30_out, and_96_out, and_95_out, and_94_out, and_93_out);
  and and_95 (and_95_out, in_21, in_20, in_19, not_4_out, 1'b0);
  and and_96 (and_96_out, in_21, in_20, in_19, in_18, 1'b0);
  and and_97 (and_97_out, not_1_out, not_2_out, not_3_out, not_4_out, xor_2_out);
  and and_98 (and_98_out, not_1_out, not_2_out, not_3_out, in_18, or_33_out);
  or or_31 (or_31_out, and_108_out, and_99_out, and_98_out, and_97_out);
  nand nand_1 (nand_1_out, in_1, in_9);
  nand nand_2 (nand_2_out, in_2, in_10);
  nand nand_3 (nand_3_out, in_3, in_11);
  nand nand_4 (nand_4_out, in_4, in_12);
  nand nand_5 (nand_5_out, in_5, in_13);
  nand nand_6 (nand_6_out, in_6, in_14);
  nand nand_7 (nand_7_out, in_7, in_15);
  nand nand_8 (nand_8_out, in_8, in_16);
  nor nor_1 (nor_1_out, in_1, in_9);
  nor nor_2 (nor_2_out, in_2, in_10);
  nor nor_3 (nor_3_out, in_3, in_11);
  nor nor_4 (nor_4_out, in_4, in_12);
  nor nor_5 (nor_5_out, in_5, in_13);
  nor nor_6 (nor_6_out, in_6, in_14);
  nor nor_7 (nor_7_out, in_7, in_15);
  nor nor_8 (nor_8_out, in_8, in_16);
  xnor xnor_1 (xnor_1_out, in_1, in_9);
  xnor xnor_2 (xnor_2_out, in_2, in_10);
  xnor xnor_3 (xnor_3_out, in_3, in_11);
  xnor xnor_4 (xnor_4_out, in_4, in_12);
  xnor xnor_5 (xnor_5_out, in_5, in_13);
  xnor xnor_6 (xnor_6_out, in_6, in_14);
  xnor xnor_7 (xnor_7_out, in_7, in_15);
  xnor xnor_8 (xnor_8_out, in_8, in_16);
  xor xor_1 (xor_1_out, in_9, in_17);
  xor xor_2 (xor_2_out, in_10, in_17);
  xor xor_3 (xor_3_out, in_11, in_17);
  xor xor_4 (xor_4_out, in_12, in_17);
  xor xor_5 (xor_5_out, in_13, in_17);
  xor xor_6 (xor_6_out, in_14, in_17);
  xor xor_7 (xor_7_out, in_15, in_17);
  xor xor_8 (xor_8_out, in_16, in_17);
  and and_99 (and_99_out, not_1_out, not_2_out, in_19, not_4_out, and_101_out);
  xor xor_9 (xor_9_out, in_1, xor_1_out);
  and and_100 (and_100_out, in_1, xor_1_out);
  or or_32 (or_32_out, in_1, xor_1_out);
  xor xor_10 (xor_10_out, in_2, xor_2_out);
  and and_101 (and_101_out, in_2, xor_2_out);
  or or_33 (or_33_out, in_2, xor_2_out);
  xor xor_11 (xor_11_out, in_3, xor_3_out);
  and and_102 (and_102_out, in_3, xor_3_out);
  or or_34 (or_34_out, in_3, xor_3_out);
  xor xor_12 (xor_12_out, in_4, xor_4_out);
  and and_103 (and_103_out, in_4, xor_4_out);
  or or_35 (or_35_out, in_4, xor_4_out);
  xor xor_13 (xor_13_out, in_5, xor_5_out);
  and and_104 (and_104_out, in_5, xor_5_out);
  or or_36 (or_36_out, in_5, xor_5_out);
  xor xor_14 (xor_14_out, in_6, xor_6_out);
  and and_105 (and_105_out, in_6, xor_6_out);
  or or_37 (or_37_out, in_6, xor_6_out);
  xor xor_15 (xor_15_out, in_7, xor_7_out);
  and and_106 (and_106_out, in_7, xor_7_out);
  or or_38 (or_38_out, in_7, xor_7_out);
  xor xor_16 (xor_16_out, in_8, xor_8_out);
  and and_107 (and_107_out, in_8, xor_8_out);
  or or_39 (or_39_out, in_8, xor_8_out);
  and and_108 (and_108_out, not_1_out, not_2_out, in_19, in_18, xor_10_out);
  and and_109 (and_109_out, in_1, in_9);
  and and_110 (and_110_out, in_1, in_10);
  and and_111 (and_111_out, in_9, in_2);
  and and_112 (and_112_out, in_1, in_11);
  and and_113 (and_113_out, in_10, in_2);
  and and_114 (and_114_out, in_1, in_12);
  and and_115 (and_115_out, in_11, in_2);
  and and_116 (and_116_out, in_1, in_13);
  and and_117 (and_117_out, in_12, in_2);
  and and_118 (and_118_out, in_1, in_14);
  and and_119 (and_119_out, in_13, in_2);
  and and_120 (and_120_out, in_1, in_15);
  and and_121 (and_121_out, in_14, in_2);
  and and_122 (and_122_out, in_1, in_16);
  and and_123 (and_123_out, in_15, in_2);
  and and_124 (and_124_out, in_16, in_2);
  and and_125 (and_125_out, not_1_out, in_20, not_3_out, not_4_out, xor_18_out);
  xor xor_17 (xor_17_out, 1'b0, xor_9_out);
  and and_126 (and_126_out, xor_9_out, 1'b0);
  xor xor_18 (xor_18_out, or_40_out, xor_10_out);
  and and_127 (and_127_out, xor_10_out, or_40_out);
  xor xor_19 (xor_19_out, or_41_out, xor_11_out);
  and and_128 (and_128_out, xor_11_out, or_41_out);
  xor xor_20 (xor_20_out, or_42_out, xor_12_out);
  and and_129 (and_129_out, xor_12_out, or_42_out);
  xor xor_21 (xor_21_out, or_43_out, xor_13_out);
  and and_130 (and_130_out, xor_13_out, or_43_out);
  xor xor_22 (xor_22_out, or_44_out, xor_14_out);
  and and_131 (and_131_out, xor_14_out, or_44_out);
  xor xor_23 (xor_23_out, or_45_out, xor_15_out);
  and and_132 (and_132_out, xor_15_out, or_45_out);
  xor xor_24 (xor_24_out, or_46_out, xor_16_out);
  and and_133 (and_133_out, xor_16_out, or_46_out);
  and and_134 (and_134_out, not_1_out, in_20, not_3_out, in_18, xnor_2_out);
  xor xor_25 (xor_25_out, and_111_out, and_110_out);
  and and_135 (and_135_out, and_111_out, and_110_out);
  xor xor_26 (xor_26_out, and_113_out, and_112_out);
  and and_136 (and_136_out, and_113_out, and_112_out);
  xor xor_27 (xor_27_out, and_115_out, and_114_out);
  and and_137 (and_137_out, and_115_out, and_114_out);
  xor xor_28 (xor_28_out, and_117_out, and_116_out);
  and and_138 (and_138_out, and_117_out, and_116_out);
  xor xor_29 (xor_29_out, and_119_out, and_118_out);
  and and_139 (and_139_out, and_119_out, and_118_out);
  xor xor_30 (xor_30_out, and_121_out, and_120_out);
  and and_140 (and_140_out, and_121_out, and_120_out);
  xor xor_31 (xor_31_out, and_123_out, and_122_out);
  and and_141 (and_141_out, and_123_out, and_122_out);
  xor xor_32 (xor_32_out, and_124_out, or_54_out);
  and and_142 (and_142_out, and_124_out, or_54_out);
  or or_40 (or_40_out, and_126_out, and_100_out);
  or or_41 (or_41_out, and_127_out, and_101_out);
  or or_42 (or_42_out, and_128_out, and_102_out);
  or or_43 (or_43_out, and_129_out, and_103_out);
  or or_44 (or_44_out, and_130_out, and_104_out);
  or or_45 (or_45_out, and_131_out, and_105_out);
  or or_46 (or_46_out, and_132_out, and_106_out);
  or or_47 (or_47_out, and_133_out, and_107_out);
  or or_48 (or_48_out, and_150_out, and_149_out, and_134_out, and_125_out);
  xor xor_33 (xor_33_out, and_135_out, xor_26_out);
  and and_143 (and_143_out, xor_26_out, and_135_out);
  xor xor_34 (xor_34_out, or_49_out, xor_27_out);
  and and_144 (and_144_out, xor_27_out, or_49_out);
  xor xor_35 (xor_35_out, or_50_out, xor_28_out);
  and and_145 (and_145_out, xor_28_out, or_50_out);
  xor xor_36 (xor_36_out, or_51_out, xor_29_out);
  and and_146 (and_146_out, xor_29_out, or_51_out);
  xor xor_37 (xor_37_out, or_52_out, xor_30_out);
  and and_147 (and_147_out, xor_30_out, or_52_out);
  xor xor_38 (xor_38_out, or_53_out, xor_31_out);
  and and_148 (and_148_out, xor_31_out, or_53_out);
  and and_149 (and_149_out, not_1_out, in_20, in_19, not_4_out, nor_2_out);
  or or_49 (or_49_out, and_143_out, and_136_out);
  or or_50 (or_50_out, and_144_out, and_137_out);
  or or_51 (or_51_out, and_145_out, and_138_out);
  or or_52 (or_52_out, and_146_out, and_139_out);
  or or_53 (or_53_out, and_147_out, and_140_out);
  or or_54 (or_54_out, and_148_out, and_141_out);
  and and_150 (and_150_out, not_1_out, in_20, in_19, in_18, nand_2_out);
  LED led_9 (.in(or_47_out));
  and and_151 (and_151_out, in_21, not_2_out, not_3_out, not_4_out, xor_25_out);
  or or_55 (or_55_out, or_64_out, or_56_out, or_48_out, or_31_out);
  and and_152 (and_152_out, in_21, not_2_out, not_3_out, in_18, 1'b0);
  and and_153 (and_153_out, in_3, in_9);
  and and_154 (and_154_out, in_3, in_10);
  and and_155 (and_155_out, in_3, in_11);
  and and_156 (and_156_out, in_3, in_12);
  and and_157 (and_157_out, in_3, in_13);
  and and_158 (and_158_out, in_3, in_14);
  and and_159 (and_159_out, in_3, in_15);
  and and_160 (and_160_out, in_3, in_16);
  or or_56 (or_56_out, and_170_out, and_161_out, and_152_out, and_151_out);
  and and_161 (and_161_out, in_21, not_2_out, in_19, not_4_out, 1'b0);
  xor xor_39 (xor_39_out, xor_33_out, and_153_out);
  and and_162 (and_162_out, xor_33_out, and_153_out);
  xor xor_40 (xor_40_out, xor_34_out, and_154_out);
  and and_163 (and_163_out, xor_34_out, and_154_out);
  xor xor_41 (xor_41_out, xor_35_out, and_155_out);
  and and_164 (and_164_out, xor_35_out, and_155_out);
  xor xor_42 (xor_42_out, xor_36_out, and_156_out);
  and and_165 (and_165_out, xor_36_out, and_156_out);
  xor xor_43 (xor_43_out, xor_37_out, and_157_out);
  and and_166 (and_166_out, xor_37_out, and_157_out);
  xor xor_44 (xor_44_out, xor_38_out, and_158_out);
  and and_167 (and_167_out, xor_38_out, and_158_out);
  xor xor_45 (xor_45_out, xor_32_out, and_159_out);
  and and_168 (and_168_out, xor_32_out, and_159_out);
  xor xor_46 (xor_46_out, and_142_out, and_160_out);
  and and_169 (and_169_out, and_142_out, and_160_out);
  and and_170 (and_170_out, in_21, not_2_out, in_19, in_18, 1'b0);
  xor xor_47 (xor_47_out, and_162_out, xor_40_out);
  and and_171 (and_171_out, xor_40_out, and_162_out);
  xor xor_48 (xor_48_out, or_57_out, xor_41_out);
  and and_172 (and_172_out, xor_41_out, or_57_out);
  xor xor_49 (xor_49_out, or_58_out, xor_42_out);
  and and_173 (and_173_out, xor_42_out, or_58_out);
  xor xor_50 (xor_50_out, or_59_out, xor_43_out);
  and and_174 (and_174_out, xor_43_out, or_59_out);
  xor xor_51 (xor_51_out, or_60_out, xor_44_out);
  and and_175 (and_175_out, xor_44_out, or_60_out);
  xor xor_52 (xor_52_out, or_61_out, xor_45_out);
  and and_176 (and_176_out, xor_45_out, or_61_out);
  xor xor_53 (xor_53_out, or_62_out, xor_46_out);
  and and_177 (and_177_out, xor_46_out, or_62_out);
  and and_178 (and_178_out, in_21, in_20, not_3_out, not_4_out, 1'b0);
  and and_179 (and_179_out, in_21, in_20, not_3_out, in_18, 1'b0);
  or or_57 (or_57_out, and_171_out, and_163_out);
  or or_58 (or_58_out, and_172_out, and_164_out);
  or or_59 (or_59_out, and_173_out, and_165_out);
  or or_60 (or_60_out, and_174_out, and_166_out);
  or or_61 (or_61_out, and_175_out, and_167_out);
  or or_62 (or_62_out, and_176_out, and_168_out);
  or or_63 (or_63_out, and_177_out, and_169_out);
  or or_64 (or_64_out, and_181_out, and_180_out, and_179_out, and_178_out);
  and and_180 (and_180_out, in_21, in_20, in_19, not_4_out, 1'b0);
  and and_181 (and_181_out, in_21, in_20, in_19, in_18, 1'b0);
  and and_182 (and_182_out, in_4, in_9);
  and and_183 (and_183_out, in_4, in_10);
  and and_184 (and_184_out, in_4, in_11);
  and and_185 (and_185_out, in_4, in_12);
  and and_186 (and_186_out, in_4, in_13);
  and and_187 (and_187_out, in_4, in_14);
  and and_188 (and_188_out, in_4, in_15);
  and and_189 (and_189_out, in_4, in_16);
  and and_190 (and_190_out, not_1_out, not_2_out, not_3_out, not_4_out, xor_1_out);
  xor xor_54 (xor_54_out, xor_47_out, and_182_out);
  and and_191 (and_191_out, xor_47_out, and_182_out);
  xor xor_55 (xor_55_out, xor_48_out, and_183_out);
  and and_192 (and_192_out, xor_48_out, and_183_out);
  xor xor_56 (xor_56_out, xor_49_out, and_184_out);
  and and_193 (and_193_out, xor_49_out, and_184_out);
  xor xor_57 (xor_57_out, xor_50_out, and_185_out);
  and and_194 (and_194_out, xor_50_out, and_185_out);
  xor xor_58 (xor_58_out, xor_51_out, and_186_out);
  and and_195 (and_195_out, xor_51_out, and_186_out);
  xor xor_59 (xor_59_out, xor_52_out, and_187_out);
  and and_196 (and_196_out, xor_52_out, and_187_out);
  xor xor_60 (xor_60_out, xor_53_out, and_188_out);
  and and_197 (and_197_out, xor_53_out, and_188_out);
  xor xor_61 (xor_61_out, or_63_out, and_189_out);
  and and_198 (and_198_out, or_63_out, and_189_out);
  and and_199 (and_199_out, not_1_out, not_2_out, not_3_out, in_18, or_32_out);
  or or_65 (or_65_out, and_208_out, and_207_out, and_199_out, and_190_out);
  xor xor_62 (xor_62_out, and_191_out, xor_55_out);
  and and_200 (and_200_out, xor_55_out, and_191_out);
  xor xor_63 (xor_63_out, or_66_out, xor_56_out);
  and and_201 (and_201_out, xor_56_out, or_66_out);
  xor xor_64 (xor_64_out, or_67_out, xor_57_out);
  and and_202 (and_202_out, xor_57_out, or_67_out);
  xor xor_65 (xor_65_out, or_68_out, xor_58_out);
  and and_203 (and_203_out, xor_58_out, or_68_out);
  xor xor_66 (xor_66_out, or_69_out, xor_59_out);
  and and_204 (and_204_out, xor_59_out, or_69_out);
  xor xor_67 (xor_67_out, or_70_out, xor_60_out);
  and and_205 (and_205_out, xor_60_out, or_70_out);
  xor xor_68 (xor_68_out, or_71_out, xor_61_out);
  and and_206 (and_206_out, xor_61_out, or_71_out);
  and and_207 (and_207_out, not_1_out, not_2_out, in_19, not_4_out, and_100_out);
  or or_66 (or_66_out, and_200_out, and_192_out);
  or or_67 (or_67_out, and_201_out, and_193_out);
  or or_68 (or_68_out, and_202_out, and_194_out);
  or or_69 (or_69_out, and_203_out, and_195_out);
  or or_70 (or_70_out, and_204_out, and_196_out);
  or or_71 (or_71_out, and_205_out, and_197_out);
  or or_72 (or_72_out, and_206_out, and_198_out);
  and and_208 (and_208_out, not_1_out, not_2_out, in_19, in_18, xor_9_out);
  and and_209 (and_209_out, not_1_out, in_20, not_3_out, not_4_out, xor_17_out);
  and and_210 (and_210_out, not_1_out, in_20, not_3_out, in_18, xnor_1_out);
  and and_211 (and_211_out, in_5, in_9);
  and and_212 (and_212_out, in_5, in_10);
  and and_213 (and_213_out, in_5, in_11);
  and and_214 (and_214_out, in_5, in_12);
  and and_215 (and_215_out, in_5, in_13);
  and and_216 (and_216_out, in_5, in_14);
  and and_217 (and_217_out, in_5, in_15);
  and and_218 (and_218_out, in_5, in_16);
  or or_73 (or_73_out, and_228_out, and_219_out, and_210_out, and_209_out);
  and and_219 (and_219_out, not_1_out, in_20, in_19, not_4_out, nor_1_out);
  xor xor_69 (xor_69_out, xor_62_out, and_211_out);
  and and_220 (and_220_out, xor_62_out, and_211_out);
  xor xor_70 (xor_70_out, xor_63_out, and_212_out);
  and and_221 (and_221_out, xor_63_out, and_212_out);
  xor xor_71 (xor_71_out, xor_64_out, and_213_out);
  and and_222 (and_222_out, xor_64_out, and_213_out);
  xor xor_72 (xor_72_out, xor_65_out, and_214_out);
  and and_223 (and_223_out, xor_65_out, and_214_out);
  xor xor_73 (xor_73_out, xor_66_out, and_215_out);
  and and_224 (and_224_out, xor_66_out, and_215_out);
  xor xor_74 (xor_74_out, xor_67_out, and_216_out);
  and and_225 (and_225_out, xor_67_out, and_216_out);
  xor xor_75 (xor_75_out, xor_68_out, and_217_out);
  and and_226 (and_226_out, xor_68_out, and_217_out);
  xor xor_76 (xor_76_out, or_72_out, and_218_out);
  and and_227 (and_227_out, or_72_out, and_218_out);
  and and_228 (and_228_out, not_1_out, in_20, in_19, in_18, nand_1_out);
  xor xor_77 (xor_77_out, and_220_out, xor_70_out);
  and and_229 (and_229_out, xor_70_out, and_220_out);
  xor xor_78 (xor_78_out, or_75_out, xor_71_out);
  and and_230 (and_230_out, xor_71_out, or_75_out);
  xor xor_79 (xor_79_out, or_76_out, xor_72_out);
  and and_231 (and_231_out, xor_72_out, or_76_out);
  xor xor_80 (xor_80_out, or_77_out, xor_73_out);
  and and_232 (and_232_out, xor_73_out, or_77_out);
  xor xor_81 (xor_81_out, or_78_out, xor_74_out);
  and and_233 (and_233_out, xor_74_out, or_78_out);
  xor xor_82 (xor_82_out, or_79_out, xor_75_out);
  and and_234 (and_234_out, xor_75_out, or_79_out);
  xor xor_83 (xor_83_out, or_80_out, xor_76_out);
  and and_235 (and_235_out, xor_76_out, or_80_out);
  and and_236 (and_236_out, in_21, not_2_out, not_3_out, not_4_out, and_109_out);
  or or_74 (or_74_out, or_83_out, or_82_out, or_73_out, or_65_out);
  or or_75 (or_75_out, and_229_out, and_221_out);
  or or_76 (or_76_out, and_230_out, and_222_out);
  or or_77 (or_77_out, and_231_out, and_223_out);
  or or_78 (or_78_out, and_232_out, and_224_out);
  or or_79 (or_79_out, and_233_out, and_225_out);
  or or_80 (or_80_out, and_234_out, and_226_out);
  or or_81 (or_81_out, and_235_out, and_227_out);
  and and_237 (and_237_out, in_21, not_2_out, not_3_out, in_18, 1'b0);
  or or_82 (or_82_out, and_239_out, and_238_out, and_237_out, and_236_out);
  and and_238 (and_238_out, in_21, not_2_out, in_19, not_4_out, 1'b0);
  and and_239 (and_239_out, in_21, not_2_out, in_19, in_18, 1'b0);
  and and_240 (and_240_out, in_6, in_9);
  and and_241 (and_241_out, in_6, in_10);
  and and_242 (and_242_out, in_6, in_11);
  and and_243 (and_243_out, in_6, in_12);
  and and_244 (and_244_out, in_6, in_13);
  and and_245 (and_245_out, in_6, in_14);
  and and_246 (and_246_out, in_6, in_15);
  and and_247 (and_247_out, in_6, in_16);
  and and_248 (and_248_out, in_21, in_20, not_3_out, not_4_out, 1'b0);
  xor xor_84 (xor_84_out, xor_77_out, and_240_out);
  and and_249 (and_249_out, xor_77_out, and_240_out);
  xor xor_85 (xor_85_out, xor_78_out, and_241_out);
  and and_250 (and_250_out, xor_78_out, and_241_out);
  xor xor_86 (xor_86_out, xor_79_out, and_242_out);
  and and_251 (and_251_out, xor_79_out, and_242_out);
  xor xor_87 (xor_87_out, xor_80_out, and_243_out);
  and and_252 (and_252_out, xor_80_out, and_243_out);
  xor xor_88 (xor_88_out, xor_81_out, and_244_out);
  and and_253 (and_253_out, xor_81_out, and_244_out);
  xor xor_89 (xor_89_out, xor_82_out, and_245_out);
  and and_254 (and_254_out, xor_82_out, and_245_out);
  xor xor_90 (xor_90_out, xor_83_out, and_246_out);
  and and_255 (and_255_out, xor_83_out, and_246_out);
  xor xor_91 (xor_91_out, or_81_out, and_247_out);
  and and_256 (and_256_out, or_81_out, and_247_out);
  and and_257 (and_257_out, in_21, in_20, not_3_out, in_18, 1'b0);
  or or_83 (or_83_out, and_266_out, and_265_out, and_257_out, and_248_out);
  xor xor_92 (xor_92_out, and_249_out, xor_85_out);
  and and_258 (and_258_out, xor_85_out, and_249_out);
  xor xor_93 (xor_93_out, or_84_out, xor_86_out);
  and and_259 (and_259_out, xor_86_out, or_84_out);
  xor xor_94 (xor_94_out, or_85_out, xor_87_out);
  and and_260 (and_260_out, xor_87_out, or_85_out);
  xor xor_95 (xor_95_out, or_86_out, xor_88_out);
  and and_261 (and_261_out, xor_88_out, or_86_out);
  xor xor_96 (xor_96_out, or_87_out, xor_89_out);
  and and_262 (and_262_out, xor_89_out, or_87_out);
  xor xor_97 (xor_97_out, or_88_out, xor_90_out);
  and and_263 (and_263_out, xor_90_out, or_88_out);
  xor xor_98 (xor_98_out, or_89_out, xor_91_out);
  and and_264 (and_264_out, xor_91_out, or_89_out);
  and and_265 (and_265_out, in_21, in_20, in_19, not_4_out, 1'b0);
  or or_84 (or_84_out, and_258_out, and_250_out);
  or or_85 (or_85_out, and_259_out, and_251_out);
  or or_86 (or_86_out, and_260_out, and_252_out);
  or or_87 (or_87_out, and_261_out, and_253_out);
  or or_88 (or_88_out, and_262_out, and_254_out);
  or or_89 (or_89_out, and_263_out, and_255_out);
  or or_90 (or_90_out, and_264_out, and_256_out);
  and and_266 (and_266_out, in_21, in_20, in_19, in_18, 1'b0);
  and and_267 (and_267_out, in_7, in_9);
  and and_268 (and_268_out, in_7, in_10);
  and and_269 (and_269_out, in_7, in_11);
  and and_270 (and_270_out, in_7, in_12);
  and and_271 (and_271_out, in_7, in_13);
  and and_272 (and_272_out, in_7, in_14);
  and and_273 (and_273_out, in_7, in_15);
  and and_274 (and_274_out, in_7, in_16);
  xor xor_99 (xor_99_out, xor_92_out, and_267_out);
  and and_275 (and_275_out, xor_92_out, and_267_out);
  xor xor_100 (xor_100_out, xor_93_out, and_268_out);
  and and_276 (and_276_out, xor_93_out, and_268_out);
  xor xor_101 (xor_101_out, xor_94_out, and_269_out);
  and and_277 (and_277_out, xor_94_out, and_269_out);
  xor xor_102 (xor_102_out, xor_95_out, and_270_out);
  and and_278 (and_278_out, xor_95_out, and_270_out);
  xor xor_103 (xor_103_out, xor_96_out, and_271_out);
  and and_279 (and_279_out, xor_96_out, and_271_out);
  xor xor_104 (xor_104_out, xor_97_out, and_272_out);
  and and_280 (and_280_out, xor_97_out, and_272_out);
  xor xor_105 (xor_105_out, xor_98_out, and_273_out);
  and and_281 (and_281_out, xor_98_out, and_273_out);
  xor xor_106 (xor_106_out, or_90_out, and_274_out);
  and and_282 (and_282_out, or_90_out, and_274_out);
  xor xor_107 (xor_107_out, and_275_out, xor_100_out);
  and and_283 (and_283_out, xor_100_out, and_275_out);
  xor xor_108 (xor_108_out, or_91_out, xor_101_out);
  and and_284 (and_284_out, xor_101_out, or_91_out);
  xor xor_109 (xor_109_out, or_92_out, xor_102_out);
  and and_285 (and_285_out, xor_102_out, or_92_out);
  xor xor_110 (xor_110_out, or_93_out, xor_103_out);
  and and_286 (and_286_out, xor_103_out, or_93_out);
  xor xor_111 (xor_111_out, or_94_out, xor_104_out);
  and and_287 (and_287_out, xor_104_out, or_94_out);
  xor xor_112 (xor_112_out, or_95_out, xor_105_out);
  and and_288 (and_288_out, xor_105_out, or_95_out);
  xor xor_113 (xor_113_out, or_96_out, xor_106_out);
  and and_289 (and_289_out, xor_106_out, or_96_out);
  or or_91 (or_91_out, and_283_out, and_276_out);
  or or_92 (or_92_out, and_284_out, and_277_out);
  or or_93 (or_93_out, and_285_out, and_278_out);
  or or_94 (or_94_out, and_286_out, and_279_out);
  or or_95 (or_95_out, and_287_out, and_280_out);
  or or_96 (or_96_out, and_288_out, and_281_out);
  or or_97 (or_97_out, and_289_out, and_282_out);
  and and_290 (and_290_out, in_8, in_9);
  and and_291 (and_291_out, in_8, in_10);
  and and_292 (and_292_out, in_8, in_11);
  and and_293 (and_293_out, in_8, in_12);
  and and_294 (and_294_out, in_8, in_13);
  and and_295 (and_295_out, in_8, in_14);
  and and_296 (and_296_out, in_8, in_15);
  and and_297 (and_297_out, in_8, in_16);
  xor xor_114 (xor_114_out, xor_107_out, and_290_out);
  and and_298 (and_298_out, xor_107_out, and_290_out);
  xor xor_115 (xor_115_out, xor_108_out, and_291_out);
  and and_299 (and_299_out, xor_108_out, and_291_out);
  xor xor_116 (xor_116_out, xor_109_out, and_292_out);
  and and_300 (and_300_out, xor_109_out, and_292_out);
  xor xor_117 (xor_117_out, xor_110_out, and_293_out);
  and and_301 (and_301_out, xor_110_out, and_293_out);
  xor xor_118 (xor_118_out, xor_111_out, and_294_out);
  and and_302 (and_302_out, xor_111_out, and_294_out);
  xor xor_119 (xor_119_out, xor_112_out, and_295_out);
  and and_303 (and_303_out, xor_112_out, and_295_out);
  xor xor_120 (xor_120_out, xor_113_out, and_296_out);
  and and_304 (and_304_out, xor_113_out, and_296_out);
  xor xor_121 (xor_121_out, or_97_out, and_297_out);
  and and_305 (and_305_out, or_97_out, and_297_out);
  xor xor_122 (xor_122_out, and_298_out, xor_115_out);
  and and_306 (and_306_out, xor_115_out, and_298_out);
  xor xor_123 (xor_123_out, or_98_out, xor_116_out);
  and and_307 (and_307_out, xor_116_out, or_98_out);
  xor xor_124 (xor_124_out, or_99_out, xor_117_out);
  and and_308 (and_308_out, xor_117_out, or_99_out);
  xor xor_125 (xor_125_out, or_100_out, xor_118_out);
  and and_309 (and_309_out, xor_118_out, or_100_out);
  xor xor_126 (xor_126_out, or_101_out, xor_119_out);
  and and_310 (and_310_out, xor_119_out, or_101_out);
  xor xor_127 (xor_127_out, or_102_out, xor_120_out);
  and and_311 (and_311_out, xor_120_out, or_102_out);
  xor xor_128 (xor_128_out, or_103_out, xor_121_out);
  and and_312 (and_312_out, xor_121_out, or_103_out);
  LED led_10 (.in(xor_122_out));
  or or_98 (or_98_out, and_306_out, and_299_out);
  LED led_11 (.in(xor_123_out));
  or or_99 (or_99_out, and_307_out, and_300_out);
  LED led_12 (.in(xor_124_out));
  or or_100 (or_100_out, and_308_out, and_301_out);
  LED led_13 (.in(xor_125_out));
  or or_101 (or_101_out, and_309_out, and_302_out);
  LED led_14 (.in(xor_126_out));
  or or_102 (or_102_out, and_310_out, and_303_out);
  LED led_15 (.in(xor_127_out));
  or or_103 (or_103_out, and_311_out, and_304_out);
  LED led_16 (.in(xor_128_out));
  // Or or_104 has open pins: In_1=and_312_out, In_2=and_305_out, out=open

  // Notes on the sheet:
  //   B
  //   A
  //   Complemento B
  //   AvB
  //   !B
  //   A\^B
  //   SumDiff
  //   A⊕B
  //   Co
  //   NOT
  //   OR
  //   AND
  //   XOR
  //   SUMDIFF
  //   NAND
  //   NOR
  //   XNOR
  //   MUL
endmodule
