// Digital circuit Memória.dig as structural Verilog
module \Memória  (
  input  in_1,
  input  in_2,
  input  in_3,
  input  in_4,
  input  in_5,
  input  in_6
);

  wire and_1_out, and_2_out, and_3_out, and_4_out, driver_1_out, nand_1_out, nand_2_out, nand_3_out,
       nand_4_out, not_1_out, not_2_out, xor_1_out;

  assign driver_1_out = in_2 ? in_5 : 1'bz;  // Driver driver_1
  and and_1 (and_1_out, in_3, in_2);
  and and_2 (and_2_out, not_1_out, in_4);
  not not_1 (not_1_out, in_2);
  LED led_1 (.in(driver_1_out));
  and and_3 (and_3_out, and_1_out, in_1);
  and and_4 (and_4_out, in_1, and_2_out);
  not not_2 (not_2_out, driver_1_out);
  nand nand_1 (nand_1_out, not_2_out, and_3_out);
  nand nand_2 (nand_2_out, and_3_out, driver_1_out);
  xor xor_1 (xor_1_out, in_6, nand_1_out);
  nand nand_3 (nand_3_out, nand_2_out, nand_4_out);
  nand nand_4 (nand_4_out, xor_1_out, nand_3_out);
  assign driver_1_out = and_4_out ? nand_3_out : 1'bz;  // Driver driver_2

  // Notes on the sheet:
  //   in_3: Clock
  //   Data I/O
  //   A
  //   Clock
  //   W/R
  //   CE
  //   Clear
  //   Célula de Memória
endmodule
